// Logisim project ht-pc0_complete.circ as structural Verilog
module outside (
  input  in_1
);

  wire undriven;

  ht_pc0 ht_pc0_1 (
    .Activity(undriven), .Power(in_1));  // open: Input_Set, Input_Data, LongOutput_Data, LongOutput_Set, MomentaryOutput_Data, MomentaryOutput_Set
  LED led_1 (.in(undriven));
endmodule

module ht_pc0 (
  input  Activity,
  input  Power,
  input  Input_Set,
  input  [7:0] Input_Data,
  output [7:0] LongOutput_Data,
  output LongOutput_Set,
  output [7:0] MomentaryOutput_Data,
  output MomentaryOutput_Set
);

  wire and_1_out, clock_1_out, controlled_buffer_1_out, controlled_buffer_3_out, cpu_1_ramjump, cpu_1_ramset,
       cpu_1_romjump, cpu_1_useram, cpu_1_useramonce, cpu_1_useramquick, not_1_out, not_2_out, not_3_out,
       not_4_out, not_5_out, or_1_out, or_2_out, or_3_out, or_4_out, or_5_out;
  wire [7:0] commander_1_out_4, controlled_buffer_2_out, controlled_buffer_4_out, cpu_1_ramaddout,
       cpu_1_ramout, cpu_1_romadd, ram_1_addressout, ram_1_out_9, ram_1_out_10, rom_1_out_4, rom_1_out_5;

  Clock clock_1 (.out(clock_1_out));
  and and_1 (and_1_out, not_1_out, not_2_out);
  assign controlled_buffer_1_out = and_1_out ? clock_1_out : 1'bz;  // Controlled_Buffer controlled_buffer_1
  Pull_Resistor pull_resistor_1 (.node(controlled_buffer_1_out));
  not not_1 (not_1_out, or_3_out);
  not not_2 (not_2_out, not_4_out);
  not not_3 (not_3_out, not_4_out);
  assign controlled_buffer_2_out = not_3_out ? cpu_1_romadd : 8'bz;  // Controlled_Buffer controlled_buffer_2
  Pull_Resistor pull_resistor_2 (.node(controlled_buffer_2_out));
  or or_1 (or_1_out, not_4_out, cpu_1_romjump);
  cpu cpu_1 (
    .I_s(Input_Set), .I_main(Input_Data), .ramin(ram_1_out_10), .ramout(cpu_1_ramout),
    .\output (MomentaryOutput_Data), .ramset(cpu_1_ramset), .outputout(MomentaryOutput_Set),
    .romadd(cpu_1_romadd), .romjump(cpu_1_romjump), .address(rom_1_out_4), .command(commander_1_out_4),
    .ramaddout(cpu_1_ramaddout), .ramaddin(ram_1_addressout), .ramchipsin(ram_1_out_9),
    .ramjump(cpu_1_ramjump), .activity(Activity), .reset(not_4_out), .\disable (not_4_out),
    .useram(cpu_1_useram), .useramquick(cpu_1_useramquick), .useramonce(cpu_1_useramonce));
  rom rom_1 (
    .out_5(rom_1_out_5), .in_1(controlled_buffer_1_out), .in_2(controlled_buffer_2_out), .in_3(or_1_out),
    .out_4(rom_1_out_4));
  Pull_Resistor pull_resistor_3 (.node(Activity));
  or or_2 (or_2_out, cpu_1_useramquick, cpu_1_useramonce);
  or or_3 (or_3_out, cpu_1_useram, cpu_1_useramonce);
  commander commander_1 (.in_1(or_3_out), .out_4(commander_1_out_4), .in_2(rom_1_out_5), .in_3(ram_1_out_10));
  or or_4 (or_4_out, not_4_out, or_2_out);
  not not_4 (not_4_out, Power);
  assign controlled_buffer_3_out = or_3_out ? clock_1_out : 1'bz;  // Controlled_Buffer controlled_buffer_3
  Pull_Resistor pull_resistor_4 (.node(controlled_buffer_3_out));
  not not_5 (not_5_out, not_4_out);
  assign controlled_buffer_4_out = not_5_out ? cpu_1_ramaddout : 8'bz;  // Controlled_Buffer controlled_buffer_4
  Pull_Resistor pull_resistor_5 (.node(controlled_buffer_4_out));
  ram ram_1 (
    .out_9(ram_1_out_9), .out_10(ram_1_out_10), .in_4(controlled_buffer_4_out), .in_5(cpu_1_ramout),
    .in_6(cpu_1_ramset), .addressout(ram_1_addressout), .setadd(or_5_out), .clear(not_4_out),
    .sync(or_4_out), .increment(controlled_buffer_3_out), .useramforcmmnds(or_3_out));
  or or_5 (or_5_out, not_4_out, cpu_1_ramjump);
  Pull_Resistor pull_resistor_6 (.node(Input_Set));
  Pull_Resistor pull_resistor_7 (.node(Input_Data));
  Pull_Resistor pull_resistor_8 (.node(MomentaryOutput_Data));
  Pull_Resistor pull_resistor_9 (.node(MomentaryOutput_Set));
  Register #(.width(9)) register_1 (
    .D({MomentaryOutput_Set, MomentaryOutput_Data}), .en(MomentaryOutput_Set),
    .Q({LongOutput_Set, LongOutput_Data}), .clk(MomentaryOutput_Set));  // open: clr
endmodule

module cpu (
  input  I_s,
  input  [7:0] I_main,
  input  [7:0] ramin,
  input  [7:0] ramaddin,
  input  [7:0] ramchipsin,
  input  \disable ,
  input  reset,
  input  [7:0] address,
  input  [7:0] command,
  output [7:0] ramout,
  output [7:0] \output ,
  output ramset,
  output outputout,
  output [7:0] romadd,
  output romjump,
  output [7:0] ramaddout,
  output ramjump,
  output useram,
  output activity,
  output useramquick,
  output useramonce
);

  wire alu_1_s, command_unit_1_aluenable, command_unit_1_out_19, command_unit_1_out_21,
       command_unit_1_out_23, command_unit_1_out_25, command_unit_1_out_27, command_unit_1_out_29,
       command_unit_1_out_31, command_unit_1_out_33, command_unit_1_out_35, command_unit_1_out_37,
       controlled_buffer_1_out, or_2_out, or_3_out, or_5_out;
  wire [3:0] command_unit_1_aluins;
  wire [7:0] alu_1_c, alu_1_d, command_unit_1_out_20, command_unit_1_out_22, command_unit_1_out_24,
       command_unit_1_out_28, command_unit_1_out_30, command_unit_1_out_32, command_unit_1_out_34,
       command_unit_1_out_36, or_1_out, or_4_out, pull_resistor_1_node, register_1_q, register_2_q,
       register_3_q, register_4_q, register_5_q, register_6_q, register_7_q, register_8_q, register_9_q,
       register_10_q;

  alu alu_1 (.ins(command_unit_1_aluins), .B(register_2_q), .A(register_1_q), .D(alu_1_d), .C(alu_1_c), .S(alu_1_s));
  assign controlled_buffer_1_out = command_unit_1_aluenable ? alu_1_s : 1'bz;  // Controlled_Buffer controlled_buffer_1
  Register register_1 (
    .D(command_unit_1_out_20), .en(command_unit_1_out_19), .Q(register_1_q), .clk(command_unit_1_out_19));  // open: clr
  Register register_2 (
    .D(command_unit_1_out_22), .en(command_unit_1_out_21), .Q(register_2_q), .clk(command_unit_1_out_21));  // open: clr
  Register register_3 (.D(or_1_out), .en(or_2_out), .Q(register_3_q), .clk(or_2_out));  // open: clr
  assign or_1_out = command_unit_1_out_24 | alu_1_c;  // OR_Gate or_1, 8 bits wide
  or or_2 (or_2_out, controlled_buffer_1_out, command_unit_1_out_23);
  or or_3 (or_3_out, controlled_buffer_1_out, command_unit_1_out_25);
  Pull_Resistor pull_resistor_1 (.node(pull_resistor_1_node));
  Pull_Resistor pull_resistor_2 (.node(controlled_buffer_1_out));
  Pull_Resistor pull_resistor_3 (.node(activity));
  Register register_4 (.D(or_4_out), .en(or_3_out), .Q(register_4_q), .clk(or_3_out));  // open: clr
  assign or_4_out = pull_resistor_1_node | alu_1_d;  // OR_Gate or_4, 8 bits wide
  Pull_Resistor pull_resistor_4 (.node(alu_1_d));
  Register register_5 (
    .D(command_unit_1_out_28), .en(command_unit_1_out_27), .Q(register_5_q), .clk(command_unit_1_out_27));  // open: clr
  Register register_6 (
    .D(command_unit_1_out_30), .en(command_unit_1_out_29), .Q(register_6_q), .clk(command_unit_1_out_29));  // open: clr
  command_unit command_unit_1 (
    .reset(reset), .useram(useram), .activity(activity), .\disable (\disable ), .address(address),
    .ins(command), .aluins(command_unit_1_aluins), .aluenable(command_unit_1_aluenable), .in_1(register_1_q),
    .out_19(command_unit_1_out_19), .out_20(command_unit_1_out_20), .in_2(register_2_q),
    .out_21(command_unit_1_out_21), .out_22(command_unit_1_out_22), .in_3(register_3_q),
    .out_23(command_unit_1_out_23), .out_24(command_unit_1_out_24), .in_4(register_4_q),
    .out_25(command_unit_1_out_25), .out_26(pull_resistor_1_node), .in_5(register_5_q),
    .out_27(command_unit_1_out_27), .out_28(command_unit_1_out_28), .in_6(register_6_q),
    .out_29(command_unit_1_out_29), .out_30(command_unit_1_out_30), .in_7(register_7_q),
    .out_31(command_unit_1_out_31), .out_32(command_unit_1_out_32), .in_8(register_8_q),
    .out_33(command_unit_1_out_33), .out_34(command_unit_1_out_34), .in_9(register_9_q),
    .out_35(command_unit_1_out_35), .out_36(command_unit_1_out_36), .in_10(register_10_q),
    .out_37(command_unit_1_out_37), .out_38(I_main), .out_52(useramonce), .useramquick(useramquick),
    .ramin(ramin), .inputin(register_10_q), .ramout(ramout), .ramset(ramset), .outputout(\output ),
    .outputset(outputout), .ramaddin(ramaddin), .ramchipsin(ramchipsin), .ramaddout(ramaddout),
    .romout(romadd), .ramaddset(ramjump), .romset(romjump));
  Register register_7 (
    .D(command_unit_1_out_32), .en(command_unit_1_out_31), .Q(register_7_q), .clk(command_unit_1_out_31));  // open: clr
  Register register_8 (
    .D(command_unit_1_out_34), .en(command_unit_1_out_33), .Q(register_8_q), .clk(command_unit_1_out_33));  // open: clr
  Register register_9 (
    .D(command_unit_1_out_36), .en(command_unit_1_out_35), .Q(register_9_q), .clk(command_unit_1_out_35));  // open: clr
  Register register_10 (.D(I_main), .en(or_5_out), .Q(register_10_q), .clk(or_5_out));  // open: clr
  or or_5 (or_5_out, command_unit_1_out_37, I_s);

  // Notes on the sheet:
  //   input
endmodule

module alu (
  input  [7:0] B,
  input  [7:0] A,
  input  [3:0] ins,
  output [7:0] D,
  output [7:0] C,
  output S
);

  wire buffer_1_out, buffer_3_out, buffer_4_out, buffer_5_out, buffer_6_out, buffer_7_out, buffer_8_out,
       n4bitdecoder_1_o_0, n4bitdecoder_1_o_15, n4bitdecoder_1_out_3, n4bitdecoder_1_out_4,
       n4bitdecoder_1_out_5, n4bitdecoder_1_out_6, n4bitdecoder_1_out_7, n4bitdecoder_1_out_8,
       n4bitdecoder_1_out_9, n4bitdecoder_1_out_10, n4bitdecoder_1_out_11, n4bitdecoder_1_out_12,
       n4bitdecoder_1_out_13, n4bitdecoder_1_out_14, n4bitdecoder_1_out_15, n4bitdecoder_1_out_16, or_3_out;
  wire [3:0] or_2_out, undriven;
  wire [7:0] adder_1_out, and_1_out, divider_1_out, divider_1_rem, multiplier_1_out, or_1_out, shifter_1_out,
       shifter_2_out, subtractor_1_out, xnor_1_out;

  assign xnor_1_out = ~(A ^ B);  // XNOR_Gate xnor_1, 8 bits wide
  Shifter shifter_1 (.in(A), .\dist (B[2:0]), .out(shifter_1_out));
  Shifter #(.shift("lr")) shifter_2 (.in(A), .\dist (B[2:0]), .out(shifter_2_out));
  Divider divider_1 (.a(A), .b(B), .out(divider_1_out), .rem(divider_1_rem));  // open: upper
  assign D = n4bitdecoder_1_out_5 ? divider_1_rem : 8'bz;  // Controlled_Buffer controlled_buffer_1
  Multiplier multiplier_1 (.a(A), .b(B), .out(multiplier_1_out));  // open: cin, cout
  Subtractor subtractor_1 (.a(A), .b(B), .out(subtractor_1_out));  // open: bin, bout
  Adder adder_1 (.a(A), .b(B), .out(adder_1_out));  // open: cin, cout
  assign C = n4bitdecoder_1_out_10 ? xnor_1_out : 8'bz;  // Controlled_Buffer controlled_buffer_2
  assign C = n4bitdecoder_1_out_9 ? ~A : 8'bz;  // Controlled_Inverter controlled_inverter_1
  assign C = n4bitdecoder_1_out_9 ? ~B : 8'bz;  // Controlled_Inverter controlled_inverter_2
  assign C = n4bitdecoder_1_out_7 ? shifter_1_out : 8'bz;  // Controlled_Buffer controlled_buffer_3
  assign C = n4bitdecoder_1_out_6 ? shifter_2_out : 8'bz;  // Controlled_Buffer controlled_buffer_4
  assign C = n4bitdecoder_1_out_5 ? divider_1_out : 8'bz;  // Controlled_Buffer controlled_buffer_5
  assign C = n4bitdecoder_1_out_4 ? multiplier_1_out : 8'bz;  // Controlled_Buffer controlled_buffer_6
  assign C = n4bitdecoder_1_out_3 ? subtractor_1_out : 8'bz;  // Controlled_Buffer controlled_buffer_7
  assign C = n4bitdecoder_1_o_0 ? adder_1_out : 8'bz;  // Controlled_Buffer controlled_buffer_8
  assign and_1_out = B & A;  // AND_Gate and_1, 8 bits wide
  assign C = n4bitdecoder_1_out_11 ? and_1_out : 8'bz;  // Controlled_Buffer controlled_buffer_9
  assign or_1_out = B | A;  // OR_Gate or_1, 8 bits wide
  assign C = n4bitdecoder_1_out_12 ? or_1_out : 8'bz;  // Controlled_Buffer controlled_buffer_10
  buf buffer_1 (buffer_1_out, buffer_3_out);
  buf buffer_2 (S, buffer_4_out);
  buf buffer_3 (buffer_3_out, buffer_6_out);
  buf buffer_4 (buffer_4_out, buffer_1_out);
  Comparator comparator_1 (.a(A), .b(B), .gt(or_2_out[1]), .eq(or_2_out[2]), .lt(or_2_out[3]));
  assign C = n4bitdecoder_1_out_13 ? {undriven, or_2_out} : 8'bz;  // Controlled_Buffer controlled_buffer_11
  buf buffer_5 (buffer_5_out, or_3_out);
  buf buffer_6 (buffer_6_out, buffer_7_out);
  buf buffer_7 (buffer_7_out, buffer_8_out);
  buf buffer_8 (buffer_8_out, buffer_5_out);
  or or_2 (or_2_out[0], or_2_out[1], or_2_out[3]);
  or or_3 (or_3_out, n4bitdecoder_1_out_10, n4bitdecoder_1_o_15, n4bitdecoder_1_out_16, n4bitdecoder_1_out_15, n4bitdecoder_1_out_14, n4bitdecoder_1_out_13, n4bitdecoder_1_out_12, n4bitdecoder_1_out_11, n4bitdecoder_1_out_9, n4bitdecoder_1_out_8, n4bitdecoder_1_out_7, n4bitdecoder_1_out_6, n4bitdecoder_1_out_5, n4bitdecoder_1_out_4, n4bitdecoder_1_out_3, n4bitdecoder_1_o_0);
  _4bitdecoder u_4bitdecoder_1 (
    .in_1(ins), .O_0(n4bitdecoder_1_o_0), .out_3(n4bitdecoder_1_out_3), .out_4(n4bitdecoder_1_out_4),
    .out_5(n4bitdecoder_1_out_5), .out_6(n4bitdecoder_1_out_6), .out_7(n4bitdecoder_1_out_7),
    .out_8(n4bitdecoder_1_out_8), .out_9(n4bitdecoder_1_out_9), .out_10(n4bitdecoder_1_out_10),
    .out_11(n4bitdecoder_1_out_11), .out_12(n4bitdecoder_1_out_12), .out_13(n4bitdecoder_1_out_13),
    .out_14(n4bitdecoder_1_out_14), .out_15(n4bitdecoder_1_out_15), .out_16(n4bitdecoder_1_out_16),
    .O_15(n4bitdecoder_1_o_15));
endmodule

module _8bitreg (
  input  in_1,
  input  [7:0] in_2,
  output [7:0] out_3
);

  wire and_1_out, and_2_out, and_3_out, and_4_out, and_5_out, and_6_out, and_7_out, and_8_out, and_9_out,
       and_10_out, and_11_out, and_12_out, and_13_out, and_14_out, and_15_out, and_16_out, nor_2_out,
       nor_4_out, nor_7_out, nor_8_out, nor_10_out, nor_12_out, nor_14_out, nor_15_out, not_1_out, not_2_out,
       not_3_out, not_4_out, not_5_out, not_6_out, not_7_out, not_8_out;

  nor nor_1 (out_3[7], and_1_out, nor_2_out);
  and and_1 (and_1_out, not_1_out, in_1);
  not not_1 (not_1_out, in_2[7]);
  nor nor_2 (nor_2_out, out_3[7], and_3_out);
  and and_2 (and_2_out, not_2_out, in_1);
  and and_3 (and_3_out, in_1, in_2[7]);
  not not_2 (not_2_out, in_2[6]);
  nor nor_3 (out_3[6], and_2_out, nor_4_out);
  nor nor_4 (nor_4_out, out_3[6], and_4_out);
  and and_4 (and_4_out, in_1, in_2[6]);
  nor nor_5 (out_3[5], and_5_out, nor_7_out);
  and and_5 (and_5_out, not_3_out, in_1);
  not not_3 (not_3_out, in_2[5]);
  nor nor_6 (out_3[4], and_7_out, nor_8_out);
  nor nor_7 (nor_7_out, out_3[5], and_6_out);
  and and_6 (and_6_out, in_1, in_2[5]);
  and and_7 (and_7_out, not_4_out, in_1);
  not not_4 (not_4_out, in_2[4]);
  nor nor_8 (nor_8_out, out_3[4], and_8_out);
  and and_8 (and_8_out, in_1, in_2[4]);
  not not_5 (not_5_out, in_2[3]);
  nor nor_9 (out_3[3], and_10_out, nor_10_out);
  nor nor_10 (nor_10_out, out_3[3], and_9_out);
  and and_9 (and_9_out, in_1, in_2[3]);
  and and_10 (and_10_out, not_5_out, in_1);
  nor nor_11 (out_3[2], and_11_out, nor_12_out);
  and and_11 (and_11_out, not_6_out, in_1);
  not not_6 (not_6_out, in_2[2]);
  nor nor_12 (nor_12_out, out_3[2], and_13_out);
  nor nor_13 (out_3[1], and_12_out, nor_14_out);
  and and_12 (and_12_out, not_7_out, in_1);
  and and_13 (and_13_out, in_1, in_2[2]);
  not not_7 (not_7_out, in_2[1]);
  nor nor_14 (nor_14_out, out_3[1], and_14_out);
  and and_14 (and_14_out, in_1, in_2[1]);
  nor nor_15 (nor_15_out, out_3[0], and_16_out);
  nor nor_16 (out_3[0], and_15_out, nor_15_out);
  and and_15 (and_15_out, not_8_out, in_1);
  not not_8 (not_8_out, in_2[0]);
  and and_16 (and_16_out, in_1, in_2[0]);
endmodule

module adder (
  input  b,
  input  a,
  input  cin,
  output cout,
  output out
);

  wire and_1_out, and_2_out, xor_1_out;

  and and_1 (and_1_out, b, a);
  xor xor_1 (xor_1_out, b, a);
  or or_1 (cout, and_1_out, and_2_out);
  and and_2 (and_2_out, cin, xor_1_out);
  xor xor_2 (out, cin, xor_1_out);
endmodule

module command_unit (
  input  [7:0] in_1,
  input  [7:0] in_2,
  input  [7:0] in_3,
  input  [7:0] in_4,
  input  [7:0] in_5,
  input  [7:0] in_6,
  input  [7:0] in_7,
  input  [7:0] in_8,
  input  [7:0] in_9,
  input  [7:0] in_10,
  input  [7:0] ramin,
  input  [7:0] inputin,
  input  reset,
  input  \disable ,
  input  [7:0] ramaddin,
  input  [7:0] ramchipsin,
  input  [7:0] address,
  input  [7:0] ins,
  output out_19,
  output [7:0] out_20,
  output out_21,
  output [7:0] out_22,
  output out_23,
  output [7:0] out_24,
  output out_25,
  output [7:0] out_26,
  output out_27,
  output [7:0] out_28,
  output out_29,
  output [7:0] out_30,
  output out_31,
  output [7:0] out_32,
  output out_33,
  output [7:0] out_34,
  output out_35,
  output [7:0] out_36,
  output out_37,
  output [7:0] out_38,
  output [7:0] ramout,
  output ramset,
  output [7:0] outputout,
  output outputset,
  output useram,
  output activity,
  output [7:0] ramaddout,
  output [7:0] romout,
  output ramaddset,
  output romset,
  output [3:0] aluins,
  output aluenable,
  output useramquick,
  output out_52
);

  wire areg0set, breg0set, controlled_buffer_1_out, controlled_buffer_2_out, controlled_buffer_3_out,
       creg0set, getramadd, getramchips, hreg0set, hyper4router_1_out_12, hyper4router_1_out_14,
       hyper10router_1_out_14, hyper10router_1_out_18, hyper10router_1_out_20, hyper10router_1_out_22,
       hyper10router_1_out_24, hyper10router_1_out_26, hyper10router_1_out_28, hyper10router_1_out_30,
       hyper10router_1_out_32, mov10set, mov20set, n3bitdecoder_1_out_4, n3bitdecoder_1_out_5,
       n3bitdecoder_1_out_6, n3bitdecoder_1_out_7, n3bitdecoder_1_out_8, n3bitdecoder_1_out_9,
       n3bitdecoder_1_out_10, n3bitdecoder_1_out_11, n8_256_1_out_3, n8_256_1_out_4, n8_256_1_out_5,
       n8_256_1_out_6, n8_256_1_out_7, n8_256_1_out_8, n8_256_1_out_9, n8_256_1_out_10, n8_256_1_out_11,
       n8_256_1_out_16, n8_256_1_out_17, n8_256_1_out_18, n8_256_1_out_19, n8_256_1_out_20, n8_256_1_out_21,
       n8_256_1_out_22, n8_256_1_out_195, n8_256_1_out_196, n8_256_1_out_197, n8_256_1_out_198,
       n8_256_1_out_199, n8_256_1_out_200, n8_256_1_out_201, n8_256_1_out_202, n8_256_1_out_203,
       n8_256_1_out_204, n8_256_1_out_205, n8_256_1_out_206, n8_256_1_out_207, n8_256_1_out_208,
       n8_256_1_out_209, n8_256_1_out_210, n8_256_1_out_211, n8_256_1_out_212, n8_256_1_out_213,
       n8_256_1_out_214, n8_256_1_out_215, n8_256_1_out_216, n8_256_1_out_217, n8_256_1_out_218,
       n8_256_1_out_219, n8_256_1_out_220, n8_256_1_out_221, n8_256_1_out_222, n8_256_1_out_223,
       n8_256_1_out_224, n8_256_1_out_225, n8_256_1_out_226, n8_256_1_out_227, n8_256_1_out_228,
       n8_256_1_out_229, n8_256_1_out_230, n8_256_1_out_231, n8_256_1_out_232, n8_256_1_out_233,
       n8_256_1_out_234, n8_256_1_out_235, n8_256_1_out_236, n8_256_1_out_237, n8_256_1_out_238,
       n8_256_1_out_239, n8_256_1_out_240, n8_256_1_out_241, n8_256_1_out_242, n8_256_1_out_243,
       n8_256_1_out_244, n8_256_1_out_245, n8_256_1_out_246, n8_256_1_out_247, n8_256_1_out_248,
       n8_256_1_out_249, n8_256_1_out_250, n8_256_1_out_251, n8_256_1_out_252, n8_256_1_out_253,
       n8_256_1_out_254, n8_256_1_out_255, n8_256_1_out_256, n8_256_1_out_257, n8_256_1_out_258, nor_1_out,
       not_2_out, or_1_out, or_2_out, or_3_out, pull_resistor_5_node, pull_resistor_9_node,
       pull_resistor_10_node, pull_resistor_11_node, pull_resistor_12_node;
  wire [3:0] conditionals0;
  wire [7:0] areg0, breg0, creg0, hreg0, hyper4router_1__1, hyper4router_1__2_2, hyper10router_1_a_2,
       hyper10router_1_mover_2_2, hyper10router_1_out_15, hyper10router_1_out_17, hyper10router_1_out_19,
       hyper10router_1_out_21, hyper10router_1_out_23, hyper10router_1_out_25, hyper10router_1_out_27,
       hyper10router_1_out_29, mov10, mov20, multiplexer_1_out, multiplexer_2_out, multiplexer_3_out,
       multiplexer_4_out, multiplexer_6_out, multiplexer_9_out, multiplexer_15_out, multiplexer_17_out,
       multiplexer_19_out;
  wire [8:0] toa0;

  Multiplexer #(.width(8), .disabled(0), .enable("false")) multiplexer_1 (
    .in0(toa0[8:1]), .in1(multiplexer_2_out), .out(multiplexer_1_out), .sel(getramchips));
  not not_1 (activity, or_1_out);
  Multiplexer #(.width(8), .disabled(0), .enable("false")) multiplexer_2 (
    .in0(ramchipsin), .in1(multiplexer_3_out), .out(multiplexer_2_out), .sel(getramadd));
  Multiplexer #(.width(8), .disabled(0), .enable("false")) multiplexer_3 (
    .in0(ramaddin), .in1(areg0), .out(multiplexer_3_out), .sel(areg0set));
  T_Flip_Flop t_ff_1 (.clk(useramquick), .T(useramquick), .Q(useram), .reset(reset));  // open: Qn, preset, en
  or or_1 (or_1_out, n8_256_1_out_3, \disable );
  Pull_Resistor pull_resistor_1 (.node(\disable ));
  assign controlled_buffer_1_out = nor_1_out ? address[0] : 1'bz;  // Controlled_Buffer controlled_buffer_1
  assign controlled_buffer_2_out = nor_1_out ? address[1] : 1'bz;  // Controlled_Buffer controlled_buffer_2
  assign controlled_buffer_3_out = nor_1_out ? address[2] : 1'bz;  // Controlled_Buffer controlled_buffer_3
  nor nor_1 (nor_1_out, address[3], address[4], address[5], address[6], or_2_out);
  or or_2 (or_2_out, address[7], \disable );
  Pull_Resistor pull_resistor_2 (.node(address));
  Multiplexer #(.width(8), .disabled(0), .enable("false")) multiplexer_4 (
    .in0(ins), .in1(multiplexer_1_out), .out(multiplexer_4_out), .sel(toa0[0]));
  or or_3 (or_3_out, getramchips, toa0[0], areg0set, n3bitdecoder_1_out_11, getramadd);
  _3bitdecoder u_3bitdecoder_1 (
    .out_4(n3bitdecoder_1_out_4), .out_5(n3bitdecoder_1_out_5), .out_6(n3bitdecoder_1_out_6),
    .out_7(n3bitdecoder_1_out_7), .out_8(n3bitdecoder_1_out_8), .out_9(n3bitdecoder_1_out_9),
    .out_10(n3bitdecoder_1_out_10), .out_11(n3bitdecoder_1_out_11), .in_1(controlled_buffer_1_out),
    .in_2(controlled_buffer_2_out), .in_3(controlled_buffer_3_out));
  Pull_Resistor pull_resistor_3 (.node(ins));
  or or_4 (out_19, or_3_out, hyper10router_1_out_14);
  Multiplexer #(.width(8), .disabled(0), .enable("false")) multiplexer_5 (
    .in0(hyper10router_1_a_2), .in1(multiplexer_4_out), .out(out_20), .sel(or_3_out));
  not not_2 (not_2_out, \disable );
  Pull_Resistor pull_resistor_4 (.node(multiplexer_4_out));
  _8_256 u_8_256_1 (
    .in_1(ins), .in_2(not_2_out), .out_3(n8_256_1_out_3), .out_4(n8_256_1_out_4), .out_5(n8_256_1_out_5),
    .out_6(n8_256_1_out_6), .out_7(n8_256_1_out_7), .out_8(n8_256_1_out_8), .out_9(n8_256_1_out_9),
    .out_10(n8_256_1_out_10), .out_11(n8_256_1_out_11), .out_12(conditionals0[0]), .out_13(conditionals0[1]),
    .out_14(conditionals0[2]), .out_15(conditionals0[3]), .out_16(n8_256_1_out_16), .out_17(n8_256_1_out_17),
    .out_18(n8_256_1_out_18), .out_19(n8_256_1_out_19), .out_20(n8_256_1_out_20), .out_21(n8_256_1_out_21),
    .out_22(n8_256_1_out_22), .out_23(ramaddset), .out_24(getramchips), .out_25(getramadd),
    .out_26(useramquick), .out_27(breg0set), .out_28(hreg0set), .out_29(areg0set), .out_30(hreg0set),
    .out_31(areg0set), .out_32(breg0set), .out_33(hreg0set), .out_34(areg0set), .out_35(breg0set),
    .out_36(creg0set), .out_37(areg0set), .out_38(mov10set), .out_39(breg0set), .out_40(mov10set),
    .out_41(creg0set), .out_42(mov10set), .out_43(areg0set), .out_44(out_52), .out_195(n8_256_1_out_195),
    .out_196(n8_256_1_out_196), .out_197(n8_256_1_out_197), .out_198(n8_256_1_out_198),
    .out_199(n8_256_1_out_199), .out_200(n8_256_1_out_200), .out_201(n8_256_1_out_201),
    .out_202(n8_256_1_out_202), .out_203(n8_256_1_out_203), .out_204(n8_256_1_out_204),
    .out_205(n8_256_1_out_205), .out_206(n8_256_1_out_206), .out_207(n8_256_1_out_207),
    .out_208(n8_256_1_out_208), .out_209(n8_256_1_out_209), .out_210(n8_256_1_out_210),
    .out_211(n8_256_1_out_211), .out_212(n8_256_1_out_212), .out_213(n8_256_1_out_213),
    .out_214(n8_256_1_out_214), .out_215(n8_256_1_out_215), .out_216(n8_256_1_out_216),
    .out_217(n8_256_1_out_217), .out_218(n8_256_1_out_218), .out_219(n8_256_1_out_219),
    .out_220(n8_256_1_out_220), .out_221(n8_256_1_out_221), .out_222(n8_256_1_out_222),
    .out_223(n8_256_1_out_223), .out_224(n8_256_1_out_224), .out_225(n8_256_1_out_225),
    .out_226(n8_256_1_out_226), .out_227(n8_256_1_out_227), .out_228(n8_256_1_out_228),
    .out_229(n8_256_1_out_229), .out_230(n8_256_1_out_230), .out_231(n8_256_1_out_231),
    .out_232(n8_256_1_out_232), .out_233(n8_256_1_out_233), .out_234(n8_256_1_out_234),
    .out_235(n8_256_1_out_235), .out_236(n8_256_1_out_236), .out_237(n8_256_1_out_237),
    .out_238(n8_256_1_out_238), .out_239(n8_256_1_out_239), .out_240(n8_256_1_out_240),
    .out_241(n8_256_1_out_241), .out_242(n8_256_1_out_242), .out_243(n8_256_1_out_243),
    .out_244(n8_256_1_out_244), .out_245(n8_256_1_out_245), .out_246(n8_256_1_out_246),
    .out_247(n8_256_1_out_247), .out_248(n8_256_1_out_248), .out_249(n8_256_1_out_249),
    .out_250(n8_256_1_out_250), .out_251(n8_256_1_out_251), .out_252(n8_256_1_out_252),
    .out_253(n8_256_1_out_253), .out_254(n8_256_1_out_254), .out_255(n8_256_1_out_255),
    .out_256(n8_256_1_out_256), .out_257(n8_256_1_out_257), .out_258(n8_256_1_out_258));  // open: out_45, out_46, out_47, out_48, out_49, out_50, out_51, out_52, out_53, out_54, out_55, out_56, out_57, out_58, out_59, out_60, out_61, out_62, out_63, out_64, out_65, out_66, out_67, out_68, out_69, out_70, out_71, out_72, out_73, out_74, out_75, out_76, out_77, out_78, out_79, out_80, out_81, out_82, out_83, out_84, out_85, out_86, out_87, out_88, out_89, out_90, out_91, out_92, out_93, out_94, out_95, out_96, out_97, out_98, out_99, out_100, out_101, out_102, out_103, out_104, out_105, out_106, out_107, out_108, out_109, out_110, out_111, out_112, out_113, out_114, out_115, out_116, out_117, out_118, out_119, out_120, out_121, out_122, out_123, out_124, out_125, out_126, out_127, out_128, out_129, out_130, out_131, out_132, out_133, out_134, out_135, out_136, out_137, out_138, out_139, out_140, out_141, out_142, out_143, out_144, out_145, out_146, out_147, out_148, out_149, out_150, out_151, out_152, out_153, out_154, out_155, out_156, out_157, out_158, out_159, out_160, out_161, out_162, out_163, out_164, out_165, out_166, out_167, out_168, out_169, out_170, out_171, out_172, out_173, out_174, out_175, out_176, out_177, out_178, out_179, out_180, out_181, out_182, out_183, out_184, out_185, out_186, out_187, out_188, out_189, out_190, out_191, out_192, out_193, out_194
  or or_5 (out_21, n3bitdecoder_1_out_10, breg0set, pull_resistor_5_node);
  Pull_Resistor pull_resistor_5 (.node(pull_resistor_5_node));
  hyper10router hyper10router_1 (
    .A_2(hyper10router_1_a_2), .out_14(hyper10router_1_out_14), .out_15(hyper10router_1_out_15),
    .out_16(pull_resistor_5_node), .out_17(hyper10router_1_out_17), .out_18(hyper10router_1_out_18),
    .out_19(hyper10router_1_out_19), .out_20(hyper10router_1_out_20), .out_21(hyper10router_1_out_21),
    .out_22(hyper10router_1_out_22), .out_23(hyper10router_1_out_23), .out_24(hyper10router_1_out_24),
    .out_25(hyper10router_1_out_25), .out_26(hyper10router_1_out_26), .out_27(hyper10router_1_out_27),
    .out_28(hyper10router_1_out_28), .out_29(hyper10router_1_out_29), .out_30(hyper10router_1_out_30),
    .Mover_2_2(hyper10router_1_mover_2_2), .out_32(hyper10router_1_out_32), .in_1(in_1), .Mover_2(in_10),
    .in_4(in_9), .in_5(in_8), .in_6(in_7), .in_7(in_6), .in_8(in_5), .in_9(in_4), .in_10(in_3), .in_11(in_1),
    .A(in_1), .X(n8_256_1_out_4));
  Pull_Resistor pull_resistor_6 (.node(hyper10router_1_out_14));
  _64constant u_64constant_1 (
    .in_1(n8_256_1_out_195), .in_2(n8_256_1_out_196), .in_3(n8_256_1_out_197), .in_4(n8_256_1_out_198),
    .in_5(n8_256_1_out_199), .in_6(n8_256_1_out_200), .in_7(n8_256_1_out_201), .in_8(n8_256_1_out_202),
    .in_9(n8_256_1_out_203), .in_10(n8_256_1_out_204), .in_11(n8_256_1_out_205), .in_12(n8_256_1_out_206),
    .in_13(n8_256_1_out_207), .in_14(n8_256_1_out_208), .in_15(n8_256_1_out_209), .in_16(n8_256_1_out_210),
    .in_17(n8_256_1_out_211), .in_18(n8_256_1_out_212), .in_19(n8_256_1_out_213), .in_20(n8_256_1_out_214),
    .in_21(n8_256_1_out_215), .in_22(n8_256_1_out_216), .in_23(n8_256_1_out_217), .in_24(n8_256_1_out_218),
    .in_25(n8_256_1_out_219), .in_26(n8_256_1_out_220), .in_27(n8_256_1_out_221), .in_28(n8_256_1_out_222),
    .in_29(n8_256_1_out_223), .in_30(n8_256_1_out_224), .in_31(n8_256_1_out_225), .in_32(n8_256_1_out_226),
    .in_33(n8_256_1_out_227), .in_34(n8_256_1_out_228), .in_35(n8_256_1_out_229), .in_36(n8_256_1_out_230),
    .in_37(n8_256_1_out_231), .in_38(n8_256_1_out_232), .in_39(n8_256_1_out_233), .in_40(n8_256_1_out_234),
    .in_41(n8_256_1_out_235), .in_42(n8_256_1_out_236), .in_43(n8_256_1_out_237), .in_44(n8_256_1_out_238),
    .in_45(n8_256_1_out_239), .in_46(n8_256_1_out_240), .in_47(n8_256_1_out_241), .in_48(n8_256_1_out_242),
    .in_49(n8_256_1_out_243), .in_50(n8_256_1_out_244), .in_51(n8_256_1_out_245), .in_52(n8_256_1_out_246),
    .in_53(n8_256_1_out_247), .in_54(n8_256_1_out_248), .in_55(n8_256_1_out_249), .in_56(n8_256_1_out_250),
    .in_57(n8_256_1_out_251), .in_58(n8_256_1_out_252), .in_59(n8_256_1_out_253), .in_60(n8_256_1_out_254),
    .in_61(n8_256_1_out_255), .in_62(n8_256_1_out_256), .in_63(n8_256_1_out_257), .in_64(n8_256_1_out_258),
    .out_65(toa0[0]), .out_66(toa0[8:1]));
  Multiplexer #(.width(8), .enable("false")) multiplexer_6 (
    .in0(multiplexer_4_out), .in1(breg0), .out(multiplexer_6_out), .sel(breg0set));
  Multiplexer #(.width(8), .disabled(0), .enable("false")) multiplexer_7 (
    .in0(hyper10router_1_out_15), .in1(multiplexer_6_out), .out(out_22), .sel(n3bitdecoder_1_out_10));
  Pull_Resistor pull_resistor_7 (.node(hyper10router_1_out_15));
  or or_6 (out_23, n3bitdecoder_1_out_9, creg0set, hyper10router_1_out_18);
  Pull_Resistor pull_resistor_8 (.node(hyper10router_1_out_18));
  assign romout = romset ? in_1 : 8'bz;  // Controlled_Buffer controlled_buffer_4
  Multiplexer #(.width(8), .disabled(0), .enable("false")) multiplexer_8 (
    .in0(hyper10router_1_out_17), .in1(multiplexer_9_out), .out(out_24), .sel(n3bitdecoder_1_out_9));
  Multiplexer #(.width(8), .enable("false")) multiplexer_9 (
    .in0(multiplexer_4_out), .in1(creg0), .out(multiplexer_9_out), .sel(creg0set));
  or or_7 (romset, pull_resistor_10_node, pull_resistor_11_node, pull_resistor_9_node, pull_resistor_12_node, n8_256_1_out_10);
  or or_8 (aluenable, n8_256_1_out_6, n8_256_1_out_7, n8_256_1_out_8, n8_256_1_out_9, n8_256_1_out_11, n8_256_1_out_16, n8_256_1_out_17, n8_256_1_out_18, n8_256_1_out_19, n8_256_1_out_20, n8_256_1_out_21, n8_256_1_out_22);
  Pull_Resistor pull_resistor_9 (.node(pull_resistor_9_node));
  Pull_Resistor pull_resistor_10 (.node(pull_resistor_10_node));
  Pull_Resistor pull_resistor_11 (.node(pull_resistor_11_node));
  Pull_Resistor pull_resistor_12 (.node(pull_resistor_12_node));
  assign aluins = n8_256_1_out_6 ? 4'b0000 : 4'bz;  // Controlled_Buffer controlled_buffer_5
  assign aluins = n8_256_1_out_7 ? 4'b0001 : 4'bz;  // Controlled_Buffer controlled_buffer_6
  assign aluins = n8_256_1_out_8 ? 4'b0010 : 4'bz;  // Controlled_Buffer controlled_buffer_7
  assign aluins = n8_256_1_out_9 ? 4'b0011 : 4'bz;  // Controlled_Buffer controlled_buffer_8
  or or_9 (out_25, n3bitdecoder_1_out_8, hyper10router_1_out_20);
  Multiplexer #(.width(8), .disabled(0), .enable("false")) multiplexer_10 (
    .in0(hyper10router_1_out_19), .in1(multiplexer_4_out), .out(out_26), .sel(n3bitdecoder_1_out_8));
  Pull_Resistor pull_resistor_13 (.node(hyper10router_1_out_20));
  assign pull_resistor_10_node = conditionals0[1] ? in_3[0] : 1'bz;  // Controlled_Buffer NEQ
  assign pull_resistor_9_node = conditionals0[3] ? in_3[3] : 1'bz;  // Controlled_Buffer LSS
  assign pull_resistor_11_node = conditionals0[0] ? in_3[1] : 1'bz;  // Controlled_Buffer GTR
  assign pull_resistor_12_node = conditionals0[2] ? in_3[2] : 1'bz;  // Controlled_Buffer EQU
  assign aluins = n8_256_1_out_11 ? 4'b1100 : 4'bz;  // Controlled_Buffer controlled_buffer_9
  assign aluins = n8_256_1_out_16 ? 4'b0100 : 4'bz;  // Controlled_Buffer controlled_buffer_10
  assign aluins = n8_256_1_out_17 ? 4'b0101 : 4'bz;  // Controlled_Buffer controlled_buffer_11
  assign aluins = n8_256_1_out_18 ? 4'b0111 : 4'bz;  // Controlled_Buffer controlled_buffer_12
  Pull_Resistor pull_resistor_14 (.node(aluins));
  assign aluins = n8_256_1_out_19 ? 4'b0110 : 4'bz;  // Controlled_Buffer controlled_buffer_13
  assign aluins = n8_256_1_out_20 ? 4'b1001 : 4'bz;  // Controlled_Buffer controlled_buffer_14
  assign aluins = n8_256_1_out_21 ? 4'b1010 : 4'bz;  // Controlled_Buffer controlled_buffer_15
  assign aluins = n8_256_1_out_22 ? 4'b1011 : 4'bz;  // Controlled_Buffer controlled_buffer_16
  or or_10 (out_27, n3bitdecoder_1_out_7, hyper10router_1_out_22);
  Pull_Resistor pull_resistor_15 (.node(hyper10router_1_out_22));
  Multiplexer #(.width(8), .disabled(0), .enable("false")) multiplexer_11 (
    .in0(hyper10router_1_out_21), .in1(multiplexer_4_out), .out(out_28), .sel(n3bitdecoder_1_out_7));
  assign breg0 = breg0set ? in_1 : 8'bz;  // Controlled_Buffer controlled_buffer_17
  assign hreg0 = hreg0set ? in_1 : 8'bz;  // Controlled_Buffer controlled_buffer_18
  assign areg0 = areg0set ? in_1 : 8'bz;  // Controlled_Buffer controlled_buffer_19
  assign hreg0 = hreg0set ? in_1 : 8'bz;  // Controlled_Buffer controlled_buffer_20
  assign areg0 = areg0set ? in_3 : 8'bz;  // Controlled_Buffer controlled_buffer_21
  assign breg0 = breg0set ? in_3 : 8'bz;  // Controlled_Buffer controlled_buffer_22
  assign hreg0 = hreg0set ? in_3 : 8'bz;  // Controlled_Buffer controlled_buffer_23
  assign areg0 = areg0set ? in_8 : 8'bz;  // Controlled_Buffer controlled_buffer_24
  assign breg0 = breg0set ? in_8 : 8'bz;  // Controlled_Buffer controlled_buffer_25
  assign creg0 = creg0set ? in_8 : 8'bz;  // Controlled_Buffer controlled_buffer_26
  assign areg0 = areg0set ? in_9 : 8'bz;  // Controlled_Buffer controlled_buffer_27
  assign mov10 = mov10set ? in_1 : 8'bz;  // Controlled_Buffer controlled_buffer_28
  assign breg0 = breg0set ? in_9 : 8'bz;  // Controlled_Buffer controlled_buffer_29
  assign mov10 = mov10set ? in_1 : 8'bz;  // Controlled_Buffer controlled_buffer_30
  assign creg0 = creg0set ? in_9 : 8'bz;  // Controlled_Buffer controlled_buffer_31
  assign mov10 = mov10set ? in_3 : 8'bz;  // Controlled_Buffer controlled_buffer_32
  assign areg0 = areg0set ? in_10 : 8'bz;  // Controlled_Buffer controlled_buffer_33
  Multiplexer #(.width(8), .disabled(0), .enable("false")) multiplexer_12 (
    .in0(hyper10router_1_out_23), .in1(multiplexer_4_out), .out(out_30), .sel(n3bitdecoder_1_out_6));
  or or_11 (out_29, n3bitdecoder_1_out_6, hyper10router_1_out_24);
  Pull_Resistor pull_resistor_16 (.node(hyper10router_1_out_24));
  or or_12 (out_31, n3bitdecoder_1_out_5, hyper10router_1_out_26);
  Pull_Resistor pull_resistor_17 (.node(hyper10router_1_out_26));
  Multiplexer #(.width(8), .disabled(0), .enable("false")) multiplexer_13 (
    .in0(hyper10router_1_out_25), .in1(multiplexer_4_out), .out(out_32), .sel(n3bitdecoder_1_out_5));
  or or_13 (out_33, n3bitdecoder_1_out_4, hyper10router_1_out_28);
  Pull_Resistor pull_resistor_18 (.node(hyper10router_1_out_28));
  Multiplexer #(.width(8), .disabled(0), .enable("false")) multiplexer_14 (
    .in0(hyper10router_1_out_27), .in1(multiplexer_15_out), .out(out_34), .sel(n3bitdecoder_1_out_4));
  Multiplexer #(.width(8), .enable("false")) multiplexer_15 (
    .in0(multiplexer_4_out), .in1(hreg0), .out(multiplexer_15_out), .sel(hreg0set));
  Multiplexer #(.width(8), .disabled(0), .enable("false")) multiplexer_16 (
    .in0(hyper10router_1_out_29), .in1(multiplexer_17_out), .out(out_36), .sel(hyper4router_1_out_12));
  or or_14 (out_35, hyper10router_1_out_30, mov10set, hyper4router_1_out_12);
  Pull_Resistor pull_resistor_19 (.node(hyper10router_1_out_30));
  Multiplexer #(.width(8), .enable("false")) multiplexer_17 (
    .in0(hyper4router_1__1), .in1(mov10), .out(multiplexer_17_out), .sel(mov10set));
  or or_15 (out_37, hyper4router_1_out_14, mov20set, hyper10router_1_out_32);
  Pull_Resistor pull_resistor_20 (.node(ramset));
  Pull_Resistor pull_resistor_21 (.node(outputset));
  hyper4router hyper4router_1 (
    .in_1(in_1), .S(n8_256_1_out_5), .R(ramin), .in_4(inputin), .in_5(in_9), ._2(in_10), .R_2(ramout),
    .out_8(ramset), .I(outputout), .out_10(outputset), ._1(hyper4router_1__1),
    .out_12(hyper4router_1_out_12), ._2_2(hyper4router_1__2_2), .out_14(hyper4router_1_out_14));
  Pull_Resistor pull_resistor_22 (.node(hyper4router_1_out_14));
  Pull_Resistor pull_resistor_23 (.node(hyper10router_1_out_32));
  Pull_Resistor pull_resistor_24 (.node(hyper4router_1_out_12));
  Multiplexer #(.width(8), .disabled(0), .enable("false")) multiplexer_18 (
    .in0(hyper10router_1_mover_2_2), .in1(multiplexer_19_out), .out(out_38), .sel(hyper4router_1_out_14));
  Multiplexer #(.width(8), .enable("false")) multiplexer_19 (
    .in0(hyper4router_1__2_2), .in1(mov20), .out(multiplexer_19_out), .sel(mov20set));
  Pull_Resistor pull_resistor_25 (.node(ramin));
  Pull_Resistor pull_resistor_26 (.node(inputin));
  Pull_Resistor pull_resistor_27 (.node(mov20));
  Pull_Resistor pull_resistor_28 (.node(mov20set));

  assign in_2 = in_1;
  assign ramaddout = in_1;

  // Other names for the same wires on the sheet: aluinterface0[4:0] = {aluenable, aluins}; ain0[7:0] = in_1;
  //   bin0[7:0] = in_1; cin0[7:0] = in_3; command[7:0] = ins; hin0[7:0] = in_8; mov1in0[7:0] = in_9;
  //   mov2in0[7:0] = in_10

  // Notes on the sheet:
  //   Register Router
  //   External
  //   Router
endmodule

module commander (
  input  in_1,
  input  [7:0] in_2,
  input  [7:0] in_3,
  output [7:0] out_4
);

  wire not_1_out;
  wire [7:0] pull_resistor_1_node, pull_resistor_2_node;

  Pull_Resistor pull_resistor_1 (.node(pull_resistor_1_node));
  assign pull_resistor_1_node = not_1_out ? in_2 : 8'bz;  // Controlled_Buffer controlled_buffer_1
  not not_1 (not_1_out, in_1);
  assign out_4 = pull_resistor_1_node | pull_resistor_2_node;  // OR_Gate or_1, 8 bits wide
  Pull_Resistor pull_resistor_2 (.node(pull_resistor_2_node));
  assign pull_resistor_2_node = in_1 ? in_3 : 8'bz;  // Controlled_Buffer controlled_buffer_2
endmodule

module rom (
  input  in_1,
  input  [7:0] in_2,
  input  in_3,
  output [7:0] out_4,
  output [7:0] out_5
);

  wire or_1_out;
  wire [7:0] counter_1_q;

  Counter counter_1 (.load(in_3), .D(in_2), .count(in_1), .Q(counter_1_q), .clk(or_1_out));  // open: carry, clr
  or or_1 (or_1_out, in_3, in_1);
  ROM rom_1 (.addr(counter_1_q), .data(out_5));  // open: sel

  assign out_4 = in_2;
endmodule

module ram (
  input  useramforcmmnds,
  input  increment,
  input  sync,
  input  [7:0] in_4,
  input  [7:0] in_5,
  input  in_6,
  input  setadd,
  input  clear,
  output [7:0] out_9,
  output [7:0] out_10,
  output [7:0] addressout
);

  wire or_1_out;
  wire [7:0] counter_1_q, multiplexer_1_out;
  wire [8:0] ramchip_1_out_2, ramchip_2_out_2, ramchip_3_out_2, ramchip_4_out_2, ramchip_5_out_2,
       ramchip_6_out_2, ramchip_7_out_2, ramchip_8_out_2;
  wire [13:0] ramcontrol_1_out_14, ramcontrol_1_out_15, ramcontrol_1_out_16, ramcontrol_1_out_17,
       ramcontrol_1_out_18, ramcontrol_1_out_19, ramcontrol_1_out_20, ramcontrol_1_out_21;

  or or_1 (or_1_out, sync, increment);
  Counter counter_1 (.load(sync), .D(in_4), .count(increment), .Q(counter_1_q), .clk(or_1_out));  // open: carry, clr
  Register register_1 (.D(in_4), .en(setadd), .Q(addressout), .clk(setadd));  // open: clr
  Multiplexer #(.width(8), .enable("false")) multiplexer_1 (
    .in0(addressout), .in1(counter_1_q), .out(multiplexer_1_out), .sel(useramforcmmnds));
  RAM #(.bus("separate")) ram_1 (
    .addr(multiplexer_1_out), .din(in_5), .data(out_10), .str(in_6), .ld(1'b1), .clr(clear));  // open: sel, clk
  ramchip ramchip_1 (.in_1(ramcontrol_1_out_15), .out_2(ramchip_1_out_2));
  ramchip ramchip_2 (.in_1(ramcontrol_1_out_17), .out_2(ramchip_2_out_2));
  ramchip ramchip_3 (.in_1(ramcontrol_1_out_19), .out_2(ramchip_3_out_2));
  ramchip ramchip_4 (.in_1(ramcontrol_1_out_21), .out_2(ramchip_4_out_2));
  ramcontrol ramcontrol_1 (
    .out_15(ramcontrol_1_out_15), .in_5(ramchip_1_out_2), .out_17(ramcontrol_1_out_17),
    .in_7(ramchip_2_out_2), .out_19(ramcontrol_1_out_19), .in_9(ramchip_3_out_2),
    .out_21(ramcontrol_1_out_21), .in_11(ramchip_4_out_2), .out_14(ramcontrol_1_out_14),
    .in_4(ramchip_5_out_2), .out_16(ramcontrol_1_out_16), .in_6(ramchip_6_out_2),
    .out_18(ramcontrol_1_out_18), .in_8(ramchip_7_out_2), .out_20(ramcontrol_1_out_20),
    .in_10(ramchip_8_out_2));  // open: out_12, out_13, in_1, in_2, in_3
  ramchip ramchip_5 (.in_1(ramcontrol_1_out_14), .out_2(ramchip_5_out_2));
  ramchip ramchip_6 (.in_1(ramcontrol_1_out_16), .out_2(ramchip_6_out_2));
  ramchip ramchip_7 (.in_1(ramcontrol_1_out_18), .out_2(ramchip_7_out_2));
  ramchip ramchip_8 (.in_1(ramcontrol_1_out_20), .out_2(ramchip_8_out_2));

  assign out_9 = {8{1'b1}};
endmodule

module ramcontrol (
  input  [7:0] in_1,
  input  [7:0] in_2,
  input  in_3,
  input  [8:0] in_4,
  input  [8:0] in_5,
  input  [8:0] in_6,
  input  [8:0] in_7,
  input  [8:0] in_8,
  input  [8:0] in_9,
  input  [8:0] in_10,
  input  [8:0] in_11,
  output [7:0] out_12,
  output [7:0] out_13,
  output [13:0] out_14,
  output [13:0] out_15,
  output [13:0] out_16,
  output [13:0] out_17,
  output [13:0] out_18,
  output [13:0] out_19,
  output [13:0] out_20,
  output [13:0] out_21
);

  wire n3bitdecoder_1_out_4, n3bitdecoder_1_out_5, n3bitdecoder_1_out_6, n3bitdecoder_1_out_7,
       n3bitdecoder_1_out_8, n3bitdecoder_1_out_9, n3bitdecoder_1_out_10, n3bitdecoder_1_out_11;

  assign out_15 = n3bitdecoder_1_out_4 ? {in_3, in_1[4:0], in_2} : 14'bz;  // Controlled_Buffer controlled_buffer_1
  assign {out_12[7], out_13} = n3bitdecoder_1_out_4 ? in_5 : 9'bz;  // Controlled_Buffer controlled_buffer_2
  assign out_17 = n3bitdecoder_1_out_5 ? {in_3, in_1[4:0], in_2} : 14'bz;  // Controlled_Buffer controlled_buffer_3
  assign {out_12[6], out_13} = n3bitdecoder_1_out_5 ? in_7 : 9'bz;  // Controlled_Buffer controlled_buffer_4
  assign out_19 = n3bitdecoder_1_out_6 ? {in_3, in_1[4:0], in_2} : 14'bz;  // Controlled_Buffer controlled_buffer_5
  assign {out_12[5], out_13} = n3bitdecoder_1_out_6 ? in_9 : 9'bz;  // Controlled_Buffer controlled_buffer_6
  assign out_21 = n3bitdecoder_1_out_7 ? {in_3, in_1[4:0], in_2} : 14'bz;  // Controlled_Buffer controlled_buffer_7
  assign {out_12[4], out_13} = n3bitdecoder_1_out_7 ? in_11 : 9'bz;  // Controlled_Buffer controlled_buffer_8
  _3bitdecoder u_3bitdecoder_1 (
    .out_4(n3bitdecoder_1_out_4), .out_5(n3bitdecoder_1_out_5), .out_6(n3bitdecoder_1_out_6),
    .out_7(n3bitdecoder_1_out_7), .out_8(n3bitdecoder_1_out_8), .out_9(n3bitdecoder_1_out_9),
    .out_10(n3bitdecoder_1_out_10), .out_11(n3bitdecoder_1_out_11), .in_1(in_1[5]), .in_2(in_1[6]),
    .in_3(in_1[7]));
  assign out_14 = n3bitdecoder_1_out_11 ? {in_3, in_1[4:0], in_2} : 14'bz;  // Controlled_Buffer controlled_buffer_9
  assign {out_12[0], out_13} = n3bitdecoder_1_out_11 ? in_4 : 9'bz;  // Controlled_Buffer controlled_buffer_10
  assign out_16 = n3bitdecoder_1_out_10 ? {in_3, in_1[4:0], in_2} : 14'bz;  // Controlled_Buffer controlled_buffer_11
  assign {out_12[1], out_13} = n3bitdecoder_1_out_10 ? in_6 : 9'bz;  // Controlled_Buffer controlled_buffer_12
  assign out_18 = n3bitdecoder_1_out_9 ? {in_3, in_1[4:0], in_2} : 14'bz;  // Controlled_Buffer controlled_buffer_13
  assign {out_12[2], out_13} = n3bitdecoder_1_out_9 ? in_8 : 9'bz;  // Controlled_Buffer controlled_buffer_14
  assign out_20 = n3bitdecoder_1_out_8 ? {in_3, in_1[4:0], in_2} : 14'bz;  // Controlled_Buffer controlled_buffer_15
  assign {out_12[3], out_13} = n3bitdecoder_1_out_8 ? in_10 : 9'bz;  // Controlled_Buffer controlled_buffer_16
endmodule

module ramchip (
  input  [13:0] in_1,
  output [8:0] out_2
);

  wire controlled_buffer_21_out, controlled_buffer_22_out, controlled_buffer_23_out,
       controlled_buffer_24_out, controlled_buffer_25_out, controlled_buffer_26_out,
       controlled_buffer_27_out, controlled_buffer_28_out, controlled_buffer_29_out,
       controlled_buffer_30_out, controlled_buffer_51_out, controlled_buffer_52_out,
       controlled_buffer_53_out, controlled_buffer_54_out, controlled_buffer_55_out,
       controlled_buffer_56_out, controlled_buffer_57_out, controlled_buffer_58_out,
       controlled_buffer_59_out, controlled_buffer_60_out, controlled_buffer_83_out,
       controlled_buffer_84_out, controlled_buffer_85_out, controlled_buffer_86_out,
       controlled_buffer_87_out, controlled_buffer_88_out, controlled_buffer_89_out,
       controlled_buffer_90_out, controlled_buffer_91_out, controlled_buffer_92_out,
       controlled_buffer_93_out, n5bitdecoder_1_out_6, n5bitdecoder_1_out_7, n5bitdecoder_1_out_8,
       n5bitdecoder_1_out_9, n5bitdecoder_1_out_10, n5bitdecoder_1_out_11, n5bitdecoder_1_out_12,
       n5bitdecoder_1_out_14, n5bitdecoder_1_out_15, n5bitdecoder_1_out_16, n5bitdecoder_1_out_17,
       n5bitdecoder_1_out_18, n5bitdecoder_1_out_19, n5bitdecoder_1_out_20, n5bitdecoder_1_out_21,
       n5bitdecoder_1_out_22, n5bitdecoder_1_out_23, n5bitdecoder_1_out_24, n5bitdecoder_1_out_25,
       n5bitdecoder_1_out_26, n5bitdecoder_1_out_27, n5bitdecoder_1_out_28, n5bitdecoder_1_out_29,
       n5bitdecoder_1_out_30, n5bitdecoder_1_out_31, n5bitdecoder_1_out_32, n5bitdecoder_1_out_33,
       n5bitdecoder_1_out_34, n5bitdecoder_1_out_35, n5bitdecoder_1_out_36, n5bitdecoder_1_out_37;
  wire [7:0] controlled_buffer_1_out, controlled_buffer_3_out, controlled_buffer_5_out,
       controlled_buffer_7_out, controlled_buffer_9_out, controlled_buffer_11_out, controlled_buffer_13_out,
       controlled_buffer_15_out, controlled_buffer_17_out, controlled_buffer_19_out,
       controlled_buffer_31_out, controlled_buffer_33_out, controlled_buffer_35_out,
       controlled_buffer_37_out, controlled_buffer_39_out, controlled_buffer_41_out,
       controlled_buffer_43_out, controlled_buffer_45_out, controlled_buffer_47_out,
       controlled_buffer_49_out, controlled_buffer_61_out, controlled_buffer_63_out,
       controlled_buffer_65_out, controlled_buffer_67_out, controlled_buffer_69_out,
       controlled_buffer_71_out, controlled_buffer_73_out, controlled_buffer_75_out,
       controlled_buffer_77_out, controlled_buffer_79_out, controlled_buffer_81_out, register_1_q,
       register_2_q, register_3_q, register_4_q, register_5_q, register_6_q, register_7_q, register_8_q,
       register_9_q, register_10_q, register_11_q, register_12_q, register_13_q, register_14_q,
       register_15_q, register_16_q, register_17_q, register_18_q, register_19_q, register_20_q,
       register_21_q, register_22_q, register_23_q, register_24_q, register_25_q, register_26_q,
       register_27_q, register_28_q, register_29_q, register_30_q, register_31_q;

  assign controlled_buffer_1_out = n5bitdecoder_1_out_6 ? in_1[7:0] : 8'bz;  // Controlled_Buffer controlled_buffer_1
  Register register_1 (.D(controlled_buffer_1_out), .en(controlled_buffer_21_out), .Q(register_1_q));  // open: clk, clr
  assign out_2[7:0] = n5bitdecoder_1_out_6 ? register_1_q : 8'bz;  // Controlled_Buffer controlled_buffer_2
  assign controlled_buffer_3_out = n5bitdecoder_1_out_11 ? in_1[7:0] : 8'bz;  // Controlled_Buffer controlled_buffer_3
  Register register_2 (.D(controlled_buffer_3_out), .en(controlled_buffer_22_out), .Q(register_2_q));  // open: clk, clr
  assign out_2[7:0] = n5bitdecoder_1_out_11 ? register_2_q : 8'bz;  // Controlled_Buffer controlled_buffer_4
  assign controlled_buffer_5_out = n5bitdecoder_1_out_14 ? in_1[7:0] : 8'bz;  // Controlled_Buffer controlled_buffer_5
  Register register_3 (.D(controlled_buffer_5_out), .en(controlled_buffer_23_out), .Q(register_3_q));  // open: clk, clr
  assign out_2[7:0] = n5bitdecoder_1_out_14 ? register_3_q : 8'bz;  // Controlled_Buffer controlled_buffer_6
  assign controlled_buffer_7_out = n5bitdecoder_1_out_17 ? in_1[7:0] : 8'bz;  // Controlled_Buffer controlled_buffer_7
  Register register_4 (.D(controlled_buffer_7_out), .en(controlled_buffer_24_out), .Q(register_4_q));  // open: clk, clr
  assign out_2[7:0] = n5bitdecoder_1_out_17 ? register_4_q : 8'bz;  // Controlled_Buffer controlled_buffer_8
  assign controlled_buffer_9_out = n5bitdecoder_1_out_20 ? in_1[7:0] : 8'bz;  // Controlled_Buffer controlled_buffer_9
  assign out_2[7:0] = n5bitdecoder_1_out_20 ? register_5_q : 8'bz;  // Controlled_Buffer controlled_buffer_10
  assign controlled_buffer_11_out = n5bitdecoder_1_out_23 ? in_1[7:0] : 8'bz;  // Controlled_Buffer controlled_buffer_11
  assign out_2[7:0] = n5bitdecoder_1_out_23 ? register_6_q : 8'bz;  // Controlled_Buffer controlled_buffer_12
  assign controlled_buffer_13_out = n5bitdecoder_1_out_26 ? in_1[7:0] : 8'bz;  // Controlled_Buffer controlled_buffer_13
  assign out_2[7:0] = n5bitdecoder_1_out_26 ? register_7_q : 8'bz;  // Controlled_Buffer controlled_buffer_14
  assign controlled_buffer_15_out = n5bitdecoder_1_out_29 ? in_1[7:0] : 8'bz;  // Controlled_Buffer controlled_buffer_15
  assign out_2[7:0] = n5bitdecoder_1_out_29 ? register_8_q : 8'bz;  // Controlled_Buffer controlled_buffer_16
  assign controlled_buffer_17_out = n5bitdecoder_1_out_32 ? in_1[7:0] : 8'bz;  // Controlled_Buffer controlled_buffer_17
  assign out_2[7:0] = n5bitdecoder_1_out_32 ? register_9_q : 8'bz;  // Controlled_Buffer controlled_buffer_18
  assign controlled_buffer_19_out = n5bitdecoder_1_out_35 ? in_1[7:0] : 8'bz;  // Controlled_Buffer controlled_buffer_19
  assign out_2[7:0] = n5bitdecoder_1_out_35 ? register_10_q : 8'bz;  // Controlled_Buffer controlled_buffer_20
  assign controlled_buffer_21_out = n5bitdecoder_1_out_6 ? in_1[13] : 1'bz;  // Controlled_Buffer controlled_buffer_21
  assign controlled_buffer_22_out = n5bitdecoder_1_out_11 ? in_1[13] : 1'bz;  // Controlled_Buffer controlled_buffer_22
  assign controlled_buffer_23_out = n5bitdecoder_1_out_14 ? in_1[13] : 1'bz;  // Controlled_Buffer controlled_buffer_23
  assign controlled_buffer_24_out = n5bitdecoder_1_out_17 ? in_1[13] : 1'bz;  // Controlled_Buffer controlled_buffer_24
  assign controlled_buffer_25_out = n5bitdecoder_1_out_20 ? in_1[13] : 1'bz;  // Controlled_Buffer controlled_buffer_25
  Register register_5 (.D(controlled_buffer_9_out), .en(controlled_buffer_25_out), .Q(register_5_q));  // open: clk, clr
  Register register_6 (
    .D(controlled_buffer_11_out), .en(controlled_buffer_26_out), .Q(register_6_q));  // open: clk, clr
  assign controlled_buffer_26_out = n5bitdecoder_1_out_23 ? in_1[13] : 1'bz;  // Controlled_Buffer controlled_buffer_26
  Register register_7 (
    .D(controlled_buffer_13_out), .en(controlled_buffer_27_out), .Q(register_7_q));  // open: clk, clr
  assign controlled_buffer_27_out = n5bitdecoder_1_out_26 ? in_1[13] : 1'bz;  // Controlled_Buffer controlled_buffer_27
  Register register_8 (
    .D(controlled_buffer_15_out), .en(controlled_buffer_28_out), .Q(register_8_q));  // open: clk, clr
  assign controlled_buffer_28_out = n5bitdecoder_1_out_29 ? in_1[13] : 1'bz;  // Controlled_Buffer controlled_buffer_28
  assign controlled_buffer_29_out = n5bitdecoder_1_out_32 ? in_1[13] : 1'bz;  // Controlled_Buffer controlled_buffer_29
  Register register_9 (
    .D(controlled_buffer_17_out), .en(controlled_buffer_29_out), .Q(register_9_q));  // open: clk, clr
  assign controlled_buffer_30_out = n5bitdecoder_1_out_35 ? in_1[13] : 1'bz;  // Controlled_Buffer controlled_buffer_30
  Register register_10 (
    .D(controlled_buffer_19_out), .en(controlled_buffer_30_out), .Q(register_10_q));  // open: clk, clr
  assign controlled_buffer_31_out = n5bitdecoder_1_out_7 ? in_1[7:0] : 8'bz;  // Controlled_Buffer controlled_buffer_31
  Register register_11 (
    .D(controlled_buffer_31_out), .en(controlled_buffer_51_out), .Q(register_11_q));  // open: clk, clr
  assign out_2[7:0] = n5bitdecoder_1_out_7 ? register_11_q : 8'bz;  // Controlled_Buffer controlled_buffer_32
  assign controlled_buffer_33_out = n5bitdecoder_1_out_10 ? in_1[7:0] : 8'bz;  // Controlled_Buffer controlled_buffer_33
  Register register_12 (
    .D(controlled_buffer_33_out), .en(controlled_buffer_52_out), .Q(register_12_q));  // open: clk, clr
  assign out_2[7:0] = n5bitdecoder_1_out_10 ? register_12_q : 8'bz;  // Controlled_Buffer controlled_buffer_34
  assign controlled_buffer_35_out = n5bitdecoder_1_out_36 ? in_1[7:0] : 8'bz;  // Controlled_Buffer controlled_buffer_35
  Register register_13 (
    .D(controlled_buffer_35_out), .en(controlled_buffer_53_out), .Q(register_13_q));  // open: clk, clr
  assign out_2[7:0] = n5bitdecoder_1_out_36 ? register_13_q : 8'bz;  // Controlled_Buffer controlled_buffer_36
  assign controlled_buffer_37_out = n5bitdecoder_1_out_16 ? in_1[7:0] : 8'bz;  // Controlled_Buffer controlled_buffer_37
  Register register_14 (
    .D(controlled_buffer_37_out), .en(controlled_buffer_54_out), .Q(register_14_q));  // open: clk, clr
  assign out_2[7:0] = n5bitdecoder_1_out_16 ? register_14_q : 8'bz;  // Controlled_Buffer controlled_buffer_38
  assign controlled_buffer_39_out = n5bitdecoder_1_out_19 ? in_1[7:0] : 8'bz;  // Controlled_Buffer controlled_buffer_39
  assign out_2[7:0] = n5bitdecoder_1_out_19 ? register_15_q : 8'bz;  // Controlled_Buffer controlled_buffer_40
  assign controlled_buffer_41_out = n5bitdecoder_1_out_22 ? in_1[7:0] : 8'bz;  // Controlled_Buffer controlled_buffer_41
  assign out_2[7:0] = n5bitdecoder_1_out_22 ? register_16_q : 8'bz;  // Controlled_Buffer controlled_buffer_42
  assign controlled_buffer_43_out = n5bitdecoder_1_out_25 ? in_1[7:0] : 8'bz;  // Controlled_Buffer controlled_buffer_43
  assign out_2[7:0] = n5bitdecoder_1_out_25 ? register_17_q : 8'bz;  // Controlled_Buffer controlled_buffer_44
  assign controlled_buffer_45_out = n5bitdecoder_1_out_28 ? in_1[7:0] : 8'bz;  // Controlled_Buffer controlled_buffer_45
  assign out_2[7:0] = n5bitdecoder_1_out_28 ? register_18_q : 8'bz;  // Controlled_Buffer controlled_buffer_46
  assign controlled_buffer_47_out = n5bitdecoder_1_out_31 ? in_1[7:0] : 8'bz;  // Controlled_Buffer controlled_buffer_47
  assign out_2[7:0] = n5bitdecoder_1_out_31 ? register_19_q : 8'bz;  // Controlled_Buffer controlled_buffer_48
  assign controlled_buffer_49_out = n5bitdecoder_1_out_34 ? in_1[7:0] : 8'bz;  // Controlled_Buffer controlled_buffer_49
  assign out_2[7:0] = n5bitdecoder_1_out_34 ? register_20_q : 8'bz;  // Controlled_Buffer controlled_buffer_50
  assign controlled_buffer_51_out = n5bitdecoder_1_out_7 ? in_1[13] : 1'bz;  // Controlled_Buffer controlled_buffer_51
  assign controlled_buffer_52_out = n5bitdecoder_1_out_10 ? in_1[13] : 1'bz;  // Controlled_Buffer controlled_buffer_52
  assign controlled_buffer_53_out = n5bitdecoder_1_out_36 ? in_1[13] : 1'bz;  // Controlled_Buffer controlled_buffer_53
  assign controlled_buffer_54_out = n5bitdecoder_1_out_16 ? in_1[13] : 1'bz;  // Controlled_Buffer controlled_buffer_54
  assign controlled_buffer_55_out = n5bitdecoder_1_out_19 ? in_1[13] : 1'bz;  // Controlled_Buffer controlled_buffer_55
  Register register_15 (
    .D(controlled_buffer_39_out), .en(controlled_buffer_55_out), .Q(register_15_q));  // open: clk, clr
  assign controlled_buffer_56_out = n5bitdecoder_1_out_22 ? in_1[13] : 1'bz;  // Controlled_Buffer controlled_buffer_56
  Register register_16 (
    .D(controlled_buffer_41_out), .en(controlled_buffer_56_out), .Q(register_16_q));  // open: clk, clr
  assign controlled_buffer_57_out = n5bitdecoder_1_out_25 ? in_1[13] : 1'bz;  // Controlled_Buffer controlled_buffer_57
  Register register_17 (
    .D(controlled_buffer_43_out), .en(controlled_buffer_57_out), .Q(register_17_q));  // open: clk, clr
  Register register_18 (
    .D(controlled_buffer_45_out), .en(controlled_buffer_58_out), .Q(register_18_q));  // open: clk, clr
  assign controlled_buffer_58_out = n5bitdecoder_1_out_28 ? in_1[13] : 1'bz;  // Controlled_Buffer controlled_buffer_58
  assign controlled_buffer_59_out = n5bitdecoder_1_out_31 ? in_1[13] : 1'bz;  // Controlled_Buffer controlled_buffer_59
  Register register_19 (
    .D(controlled_buffer_47_out), .en(controlled_buffer_59_out), .Q(register_19_q));  // open: clk, clr
  Register register_20 (
    .D(controlled_buffer_49_out), .en(controlled_buffer_60_out), .Q(register_20_q));  // open: clk, clr
  assign controlled_buffer_60_out = n5bitdecoder_1_out_34 ? in_1[13] : 1'bz;  // Controlled_Buffer controlled_buffer_60
  _5bitdecoder u_5bitdecoder_1 (
    .in_1(in_1[8]), .in_2(in_1[9]), .in_3(in_1[10]), .in_4(in_1[11]), .in_5(in_1[12]),
    .out_6(n5bitdecoder_1_out_6), .out_7(n5bitdecoder_1_out_7), .out_8(n5bitdecoder_1_out_8),
    .out_9(n5bitdecoder_1_out_9), .out_10(n5bitdecoder_1_out_10), .out_11(n5bitdecoder_1_out_11),
    .out_12(n5bitdecoder_1_out_12), .out_13(in_1[13]), .out_14(n5bitdecoder_1_out_14),
    .out_15(n5bitdecoder_1_out_15), .out_16(n5bitdecoder_1_out_16), .out_17(n5bitdecoder_1_out_17),
    .out_18(n5bitdecoder_1_out_18), .out_19(n5bitdecoder_1_out_19), .out_20(n5bitdecoder_1_out_20),
    .out_21(n5bitdecoder_1_out_21), .out_22(n5bitdecoder_1_out_22), .out_23(n5bitdecoder_1_out_23),
    .out_24(n5bitdecoder_1_out_24), .out_25(n5bitdecoder_1_out_25), .out_26(n5bitdecoder_1_out_26),
    .out_27(n5bitdecoder_1_out_27), .out_28(n5bitdecoder_1_out_28), .out_29(n5bitdecoder_1_out_29),
    .out_30(n5bitdecoder_1_out_30), .out_31(n5bitdecoder_1_out_31), .out_32(n5bitdecoder_1_out_32),
    .out_33(n5bitdecoder_1_out_33), .out_34(n5bitdecoder_1_out_34), .out_35(n5bitdecoder_1_out_35),
    .out_36(n5bitdecoder_1_out_36), .out_37(n5bitdecoder_1_out_37));
  assign controlled_buffer_61_out = n5bitdecoder_1_out_8 ? in_1[7:0] : 8'bz;  // Controlled_Buffer controlled_buffer_61
  Register register_21 (
    .D(controlled_buffer_61_out), .en(controlled_buffer_83_out), .Q(register_21_q));  // open: clk, clr
  assign out_2[7:0] = n5bitdecoder_1_out_8 ? register_21_q : 8'bz;  // Controlled_Buffer controlled_buffer_62
  assign controlled_buffer_63_out = n5bitdecoder_1_out_9 ? in_1[7:0] : 8'bz;  // Controlled_Buffer controlled_buffer_63
  Register register_22 (
    .D(controlled_buffer_63_out), .en(controlled_buffer_84_out), .Q(register_22_q));  // open: clk, clr
  assign out_2[7:0] = n5bitdecoder_1_out_9 ? register_22_q : 8'bz;  // Controlled_Buffer controlled_buffer_64
  assign controlled_buffer_65_out = n5bitdecoder_1_out_12 ? in_1[7:0] : 8'bz;  // Controlled_Buffer controlled_buffer_65
  Register register_23 (
    .D(controlled_buffer_65_out), .en(controlled_buffer_85_out), .Q(register_23_q));  // open: clk, clr
  assign out_2[7:0] = n5bitdecoder_1_out_12 ? register_23_q : 8'bz;  // Controlled_Buffer controlled_buffer_66
  assign controlled_buffer_67_out = n5bitdecoder_1_out_15 ? in_1[7:0] : 8'bz;  // Controlled_Buffer controlled_buffer_67
  Register register_24 (
    .D(controlled_buffer_67_out), .en(controlled_buffer_86_out), .Q(register_24_q));  // open: clk, clr
  assign out_2[7:0] = n5bitdecoder_1_out_15 ? register_24_q : 8'bz;  // Controlled_Buffer controlled_buffer_68
  assign controlled_buffer_69_out = n5bitdecoder_1_out_18 ? in_1[7:0] : 8'bz;  // Controlled_Buffer controlled_buffer_69
  assign out_2[7:0] = n5bitdecoder_1_out_18 ? register_25_q : 8'bz;  // Controlled_Buffer controlled_buffer_70
  assign controlled_buffer_71_out = n5bitdecoder_1_out_21 ? in_1[7:0] : 8'bz;  // Controlled_Buffer controlled_buffer_71
  assign out_2[7:0] = n5bitdecoder_1_out_21 ? register_26_q : 8'bz;  // Controlled_Buffer controlled_buffer_72
  assign controlled_buffer_73_out = n5bitdecoder_1_out_24 ? in_1[7:0] : 8'bz;  // Controlled_Buffer controlled_buffer_73
  assign out_2[7:0] = n5bitdecoder_1_out_24 ? register_27_q : 8'bz;  // Controlled_Buffer controlled_buffer_74
  assign controlled_buffer_75_out = n5bitdecoder_1_out_27 ? in_1[7:0] : 8'bz;  // Controlled_Buffer controlled_buffer_75
  assign out_2[7:0] = n5bitdecoder_1_out_27 ? register_28_q : 8'bz;  // Controlled_Buffer controlled_buffer_76
  assign controlled_buffer_77_out = n5bitdecoder_1_out_30 ? in_1[7:0] : 8'bz;  // Controlled_Buffer controlled_buffer_77
  assign out_2[7:0] = n5bitdecoder_1_out_30 ? register_29_q : 8'bz;  // Controlled_Buffer controlled_buffer_78
  assign controlled_buffer_79_out = n5bitdecoder_1_out_33 ? in_1[7:0] : 8'bz;  // Controlled_Buffer controlled_buffer_79
  assign out_2[7:0] = n5bitdecoder_1_out_33 ? register_30_q : 8'bz;  // Controlled_Buffer controlled_buffer_80
  assign controlled_buffer_81_out = n5bitdecoder_1_out_37 ? in_1[7:0] : 8'bz;  // Controlled_Buffer controlled_buffer_81
  assign out_2[7:0] = n5bitdecoder_1_out_37 ? register_31_q : 8'bz;  // Controlled_Buffer controlled_buffer_82
  assign controlled_buffer_83_out = n5bitdecoder_1_out_8 ? in_1[13] : 1'bz;  // Controlled_Buffer controlled_buffer_83
  assign controlled_buffer_84_out = n5bitdecoder_1_out_9 ? in_1[13] : 1'bz;  // Controlled_Buffer controlled_buffer_84
  assign controlled_buffer_85_out = n5bitdecoder_1_out_12 ? in_1[13] : 1'bz;  // Controlled_Buffer controlled_buffer_85
  assign controlled_buffer_86_out = n5bitdecoder_1_out_15 ? in_1[13] : 1'bz;  // Controlled_Buffer controlled_buffer_86
  Register register_25 (
    .D(controlled_buffer_69_out), .en(controlled_buffer_87_out), .Q(register_25_q));  // open: clk, clr
  assign controlled_buffer_87_out = n5bitdecoder_1_out_18 ? in_1[13] : 1'bz;  // Controlled_Buffer controlled_buffer_87
  assign controlled_buffer_88_out = n5bitdecoder_1_out_21 ? in_1[13] : 1'bz;  // Controlled_Buffer controlled_buffer_88
  Register register_26 (
    .D(controlled_buffer_71_out), .en(controlled_buffer_88_out), .Q(register_26_q));  // open: clk, clr
  Register register_27 (
    .D(controlled_buffer_73_out), .en(controlled_buffer_89_out), .Q(register_27_q));  // open: clk, clr
  assign controlled_buffer_89_out = n5bitdecoder_1_out_24 ? in_1[13] : 1'bz;  // Controlled_Buffer controlled_buffer_89
  Register register_28 (
    .D(controlled_buffer_75_out), .en(controlled_buffer_90_out), .Q(register_28_q));  // open: clk, clr
  assign controlled_buffer_90_out = n5bitdecoder_1_out_27 ? in_1[13] : 1'bz;  // Controlled_Buffer controlled_buffer_90
  Register register_29 (
    .D(controlled_buffer_77_out), .en(controlled_buffer_91_out), .Q(register_29_q));  // open: clk, clr
  assign controlled_buffer_91_out = n5bitdecoder_1_out_30 ? in_1[13] : 1'bz;  // Controlled_Buffer controlled_buffer_91
  Register register_30 (
    .D(controlled_buffer_79_out), .en(controlled_buffer_92_out), .Q(register_30_q));  // open: clk, clr
  assign controlled_buffer_92_out = n5bitdecoder_1_out_33 ? in_1[13] : 1'bz;  // Controlled_Buffer controlled_buffer_92
  Register register_31 (
    .D(controlled_buffer_81_out), .en(controlled_buffer_93_out), .Q(register_31_q));  // open: clk, clr
  assign controlled_buffer_93_out = n5bitdecoder_1_out_37 ? in_1[13] : 1'bz;  // Controlled_Buffer controlled_buffer_93

  assign out_2[8] = 1'b1;
endmodule

module _5bitdecoder (
  input  in_1,
  input  in_2,
  input  in_3,
  input  in_4,
  input  in_5,
  output out_6,
  output out_7,
  output out_8,
  output out_9,
  output out_10,
  output out_11,
  output out_12,
  output out_13,
  output out_14,
  output out_15,
  output out_16,
  output out_17,
  output out_18,
  output out_19,
  output out_20,
  output out_21,
  output out_22,
  output out_23,
  output out_24,
  output out_25,
  output out_26,
  output out_27,
  output out_28,
  output out_29,
  output out_30,
  output out_31,
  output out_32,
  output out_33,
  output out_34,
  output out_35,
  output out_36,
  output out_37
);

  wire not_1_out, not_2_out, not_3_out, not_4_out, not_5_out;

  not not_1 (not_1_out, in_5);
  not not_2 (not_2_out, in_4);
  not not_3 (not_3_out, in_3);
  not not_4 (not_4_out, in_2);
  not not_5 (not_5_out, in_1);
  and and_1 (out_6, not_5_out, not_4_out, not_3_out, not_2_out, not_1_out);
  and and_2 (out_7, not_5_out, not_4_out, not_3_out, not_2_out, in_5);
  and and_3 (out_8, not_5_out, not_4_out, not_3_out, in_4, not_1_out);
  and and_4 (out_9, not_5_out, not_4_out, not_3_out, in_4, in_5);
  and and_5 (out_10, not_5_out, not_4_out, in_3, not_2_out, not_1_out);
  and and_6 (out_11, not_5_out, not_4_out, in_3, not_2_out, in_5);
  and and_7 (out_12, not_5_out, not_4_out, in_3, in_4, not_1_out);
  and and_8 (out_13, not_5_out, not_4_out, in_3, in_4, in_5);
  and and_9 (out_14, not_5_out, in_2, not_3_out, not_2_out, not_1_out);
  and and_10 (out_15, not_5_out, in_2, not_3_out, not_2_out, in_5);
  and and_11 (out_16, not_5_out, in_2, not_3_out, in_4, not_1_out);
  and and_12 (out_17, not_5_out, in_2, not_3_out, in_4, in_5);
  and and_13 (out_18, not_5_out, in_2, in_3, not_2_out, not_1_out);
  and and_14 (out_19, not_5_out, in_2, in_3, not_2_out, in_5);
  and and_15 (out_20, not_5_out, in_2, in_3, in_4, not_1_out);
  and and_16 (out_21, not_5_out, in_2, in_3, in_4, in_5);
  and and_17 (out_22, in_1, not_4_out, not_3_out, not_2_out, not_1_out);
  and and_18 (out_23, in_1, not_4_out, not_3_out, not_2_out, in_5);
  and and_19 (out_24, in_1, not_4_out, not_3_out, in_4, not_1_out);
  and and_20 (out_25, in_1, not_4_out, not_3_out, in_4, in_5);
  and and_21 (out_26, in_1, not_4_out, in_3, not_2_out, not_1_out);
  and and_22 (out_27, in_1, not_4_out, in_3, not_2_out, in_5);
  and and_23 (out_28, in_1, not_4_out, in_3, in_4, not_1_out);
  and and_24 (out_29, in_1, not_4_out, in_3, in_4, in_5);
  and and_25 (out_30, in_1, in_2, not_3_out, not_2_out, not_1_out);
  and and_26 (out_31, in_1, in_2, not_3_out, not_2_out, in_5);
  and and_27 (out_32, in_1, in_2, not_3_out, in_4, not_1_out);
  and and_28 (out_33, in_1, in_2, not_3_out, in_4, in_5);
  and and_29 (out_34, in_1, in_2, in_3, not_2_out, not_1_out);
  and and_30 (out_35, in_1, in_2, in_3, not_2_out, in_5);
  and and_31 (out_36, in_1, in_2, in_3, in_4, not_1_out);
  and and_32 (out_37, in_1, in_2, in_3, in_4, in_5);
endmodule

module _3bitdecoder (
  input  in_1,
  input  in_2,
  input  in_3,
  output out_4,
  output out_5,
  output out_6,
  output out_7,
  output out_8,
  output out_9,
  output out_10,
  output out_11
);

  wire not_1_out, not_2_out, not_3_out;

  not not_1 (not_1_out, in_1);
  not not_2 (not_2_out, in_2);
  not not_3 (not_3_out, in_3);
  and and_1 (out_5, in_1, in_2, not_3_out);
  and and_2 (out_4, in_1, in_2, in_3);
  and and_3 (out_7, in_1, not_2_out, not_3_out);
  and and_4 (out_8, not_1_out, in_2, in_3);
  and and_5 (out_6, in_1, not_2_out, in_3);
  and and_6 (out_10, not_1_out, not_2_out, in_3);
  and and_7 (out_11, not_1_out, not_2_out, not_3_out);
  and and_8 (out_9, not_1_out, in_2, not_3_out);
endmodule

module hyper10router (
  input  [7:0] in_1,
  input  X,
  input  [7:0] Mover_2,
  input  [7:0] in_4,
  input  [7:0] in_5,
  input  [7:0] in_6,
  input  [7:0] in_7,
  input  [7:0] in_8,
  input  [7:0] in_9,
  input  [7:0] in_10,
  input  [7:0] in_11,
  input  [7:0] A,
  output [7:0] A_2,
  output out_14,
  output [7:0] out_15,
  output out_16,
  output [7:0] out_17,
  output out_18,
  output [7:0] out_19,
  output out_20,
  output [7:0] out_21,
  output out_22,
  output [7:0] out_23,
  output out_24,
  output [7:0] out_25,
  output out_26,
  output [7:0] out_27,
  output out_28,
  output [7:0] out_29,
  output out_30,
  output [7:0] Mover_2_2,
  output out_32
);

  wire n4bitdecoder_1_o_15, n4bitdecoder_1_out_12, n4bitdecoder_1_out_13, n4bitdecoder_1_out_14,
       n4bitdecoder_1_out_15, n4bitdecoder_1_out_16, n4bitdecoder_2_o_0, n4bitdecoder_2_o_15,
       n4bitdecoder_2_out_3, n4bitdecoder_2_out_4, n4bitdecoder_2_out_5, n4bitdecoder_2_out_6,
       n4bitdecoder_2_out_7, n4bitdecoder_2_out_8, n4bitdecoder_2_out_9, n4bitdecoder_2_out_10,
       n4bitdecoder_2_out_11, n4bitdecoder_2_out_12, n4bitdecoder_2_out_13, n4bitdecoder_2_out_14,
       n4bitdecoder_2_out_15, n4bitdecoder_2_out_16;
  wire [9:0] n4bitdecoder_1_o_0;

  // OR_Gate or_1 has open pins: in0=n4bitdecoder_1_o_15, in1=n4bitdecoder_1_out_16, in2=n4bitdecoder_1_out_15, in3=n4bitdecoder_1_out_14, in4=n4bitdecoder_1_out_13, in5=n4bitdecoder_1_out_12, out=open
  _4bitdecoder u_4bitdecoder_1 (
    .in_1(in_1[7:4]), .O_0(n4bitdecoder_1_o_0[0]), .out_3(n4bitdecoder_1_o_0[1]),
    .out_4(n4bitdecoder_1_o_0[2]), .out_5(n4bitdecoder_1_o_0[3]), .out_6(n4bitdecoder_1_o_0[4]),
    .out_7(n4bitdecoder_1_o_0[5]), .out_8(n4bitdecoder_1_o_0[6]), .out_9(n4bitdecoder_1_o_0[7]),
    .out_10(n4bitdecoder_1_o_0[8]), .out_11(n4bitdecoder_1_o_0[9]), .out_12(n4bitdecoder_1_out_12),
    .out_13(n4bitdecoder_1_out_13), .out_14(n4bitdecoder_1_out_14), .out_15(n4bitdecoder_1_out_15),
    .out_16(n4bitdecoder_1_out_16), .O_15(n4bitdecoder_1_o_15));
  // OR_Gate or_2 has open pins: in0=n4bitdecoder_2_o_15, in1=n4bitdecoder_2_out_16, in2=n4bitdecoder_2_out_15, in3=n4bitdecoder_2_out_14, in4=n4bitdecoder_2_out_13, in5=n4bitdecoder_2_out_12, out=open
  _4bitdecoder u_4bitdecoder_2 (
    .in_1(in_1[3:0]), .O_0(n4bitdecoder_2_o_0), .out_3(n4bitdecoder_2_out_3), .out_4(n4bitdecoder_2_out_4),
    .out_5(n4bitdecoder_2_out_5), .out_6(n4bitdecoder_2_out_6), .out_7(n4bitdecoder_2_out_7),
    .out_8(n4bitdecoder_2_out_8), .out_9(n4bitdecoder_2_out_9), .out_10(n4bitdecoder_2_out_10),
    .out_11(n4bitdecoder_2_out_11), .out_12(n4bitdecoder_2_out_12), .out_13(n4bitdecoder_2_out_13),
    .out_14(n4bitdecoder_2_out_14), .out_15(n4bitdecoder_2_out_15), .out_16(n4bitdecoder_2_out_16),
    .O_15(n4bitdecoder_2_o_15));
  assign A_2 = n4bitdecoder_1_o_0[0] ? A : 8'bz;  // Controlled_Buffer controlled_buffer_1
  assign A_2 = n4bitdecoder_1_o_0[1] ? in_11 : 8'bz;  // Controlled_Buffer controlled_buffer_2
  assign A_2 = n4bitdecoder_1_o_0[2] ? in_10 : 8'bz;  // Controlled_Buffer controlled_buffer_3
  assign A_2 = n4bitdecoder_1_o_0[3] ? in_9 : 8'bz;  // Controlled_Buffer controlled_buffer_4
  assign A_2 = n4bitdecoder_1_o_0[4] ? in_8 : 8'bz;  // Controlled_Buffer controlled_buffer_5
  assign A_2 = n4bitdecoder_1_o_0[5] ? in_7 : 8'bz;  // Controlled_Buffer controlled_buffer_6
  assign A_2 = n4bitdecoder_1_o_0[6] ? in_6 : 8'bz;  // Controlled_Buffer controlled_buffer_7
  assign A_2 = n4bitdecoder_1_o_0[7] ? in_5 : 8'bz;  // Controlled_Buffer controlled_buffer_8
  assign A_2 = n4bitdecoder_1_o_0[8] ? in_4 : 8'bz;  // Controlled_Buffer controlled_buffer_9
  assign A_2 = n4bitdecoder_1_o_0[9] ? Mover_2 : 8'bz;  // Controlled_Buffer controlled_buffer_10
  assign out_15 = n4bitdecoder_1_o_0[0] ? A : 8'bz;  // Controlled_Buffer controlled_buffer_11
  assign out_15 = n4bitdecoder_1_o_0[1] ? in_11 : 8'bz;  // Controlled_Buffer controlled_buffer_12
  assign out_15 = n4bitdecoder_1_o_0[2] ? in_10 : 8'bz;  // Controlled_Buffer controlled_buffer_13
  assign out_15 = n4bitdecoder_1_o_0[3] ? in_9 : 8'bz;  // Controlled_Buffer controlled_buffer_14
  assign out_15 = n4bitdecoder_1_o_0[4] ? in_8 : 8'bz;  // Controlled_Buffer controlled_buffer_15
  assign out_15 = n4bitdecoder_1_o_0[5] ? in_7 : 8'bz;  // Controlled_Buffer controlled_buffer_16
  assign out_15 = n4bitdecoder_1_o_0[6] ? in_6 : 8'bz;  // Controlled_Buffer controlled_buffer_17
  assign out_15 = n4bitdecoder_1_o_0[7] ? in_5 : 8'bz;  // Controlled_Buffer controlled_buffer_18
  assign out_15 = n4bitdecoder_1_o_0[8] ? in_4 : 8'bz;  // Controlled_Buffer controlled_buffer_19
  assign out_15 = n4bitdecoder_1_o_0[9] ? Mover_2 : 8'bz;  // Controlled_Buffer controlled_buffer_20
  assign out_17 = n4bitdecoder_1_o_0[0] ? A : 8'bz;  // Controlled_Buffer controlled_buffer_21
  assign out_17 = n4bitdecoder_1_o_0[1] ? in_11 : 8'bz;  // Controlled_Buffer controlled_buffer_22
  assign out_17 = n4bitdecoder_1_o_0[2] ? in_10 : 8'bz;  // Controlled_Buffer controlled_buffer_23
  assign out_17 = n4bitdecoder_1_o_0[3] ? in_9 : 8'bz;  // Controlled_Buffer controlled_buffer_24
  assign out_17 = n4bitdecoder_1_o_0[4] ? in_8 : 8'bz;  // Controlled_Buffer controlled_buffer_25
  assign out_17 = n4bitdecoder_1_o_0[5] ? in_7 : 8'bz;  // Controlled_Buffer controlled_buffer_26
  assign out_17 = n4bitdecoder_1_o_0[6] ? in_6 : 8'bz;  // Controlled_Buffer controlled_buffer_27
  assign out_17 = n4bitdecoder_1_o_0[7] ? in_5 : 8'bz;  // Controlled_Buffer controlled_buffer_28
  assign out_17 = n4bitdecoder_1_o_0[8] ? in_4 : 8'bz;  // Controlled_Buffer controlled_buffer_29
  assign out_17 = n4bitdecoder_1_o_0[9] ? Mover_2 : 8'bz;  // Controlled_Buffer controlled_buffer_30
  assign out_19 = n4bitdecoder_1_o_0[0] ? A : 8'bz;  // Controlled_Buffer controlled_buffer_31
  assign out_19 = n4bitdecoder_1_o_0[1] ? in_11 : 8'bz;  // Controlled_Buffer controlled_buffer_32
  assign out_19 = n4bitdecoder_1_o_0[2] ? in_10 : 8'bz;  // Controlled_Buffer controlled_buffer_33
  assign out_19 = n4bitdecoder_1_o_0[3] ? in_9 : 8'bz;  // Controlled_Buffer controlled_buffer_34
  assign out_19 = n4bitdecoder_1_o_0[4] ? in_8 : 8'bz;  // Controlled_Buffer controlled_buffer_35
  assign out_19 = n4bitdecoder_1_o_0[5] ? in_7 : 8'bz;  // Controlled_Buffer controlled_buffer_36
  assign out_19 = n4bitdecoder_1_o_0[6] ? in_6 : 8'bz;  // Controlled_Buffer controlled_buffer_37
  assign out_19 = n4bitdecoder_1_o_0[7] ? in_5 : 8'bz;  // Controlled_Buffer controlled_buffer_38
  assign out_19 = n4bitdecoder_1_o_0[8] ? in_4 : 8'bz;  // Controlled_Buffer controlled_buffer_39
  assign out_19 = n4bitdecoder_1_o_0[9] ? Mover_2 : 8'bz;  // Controlled_Buffer controlled_buffer_40
  assign out_21 = n4bitdecoder_1_o_0[0] ? A : 8'bz;  // Controlled_Buffer controlled_buffer_41
  assign out_21 = n4bitdecoder_1_o_0[1] ? in_11 : 8'bz;  // Controlled_Buffer controlled_buffer_42
  assign out_21 = n4bitdecoder_1_o_0[2] ? in_10 : 8'bz;  // Controlled_Buffer controlled_buffer_43
  assign out_21 = n4bitdecoder_1_o_0[3] ? in_9 : 8'bz;  // Controlled_Buffer controlled_buffer_44
  assign out_21 = n4bitdecoder_1_o_0[4] ? in_8 : 8'bz;  // Controlled_Buffer controlled_buffer_45
  assign out_21 = n4bitdecoder_1_o_0[5] ? in_7 : 8'bz;  // Controlled_Buffer controlled_buffer_46
  assign out_21 = n4bitdecoder_1_o_0[6] ? in_6 : 8'bz;  // Controlled_Buffer controlled_buffer_47
  assign out_21 = n4bitdecoder_1_o_0[7] ? in_5 : 8'bz;  // Controlled_Buffer controlled_buffer_48
  assign out_21 = n4bitdecoder_1_o_0[8] ? in_4 : 8'bz;  // Controlled_Buffer controlled_buffer_49
  assign out_21 = n4bitdecoder_1_o_0[9] ? Mover_2 : 8'bz;  // Controlled_Buffer controlled_buffer_50
  assign out_23 = n4bitdecoder_1_o_0[0] ? A : 8'bz;  // Controlled_Buffer controlled_buffer_51
  assign out_23 = n4bitdecoder_1_o_0[1] ? in_11 : 8'bz;  // Controlled_Buffer controlled_buffer_52
  assign out_23 = n4bitdecoder_1_o_0[2] ? in_10 : 8'bz;  // Controlled_Buffer controlled_buffer_53
  assign out_23 = n4bitdecoder_1_o_0[3] ? in_9 : 8'bz;  // Controlled_Buffer controlled_buffer_54
  assign out_23 = n4bitdecoder_1_o_0[4] ? in_8 : 8'bz;  // Controlled_Buffer controlled_buffer_55
  assign out_23 = n4bitdecoder_1_o_0[5] ? in_7 : 8'bz;  // Controlled_Buffer controlled_buffer_56
  assign out_23 = n4bitdecoder_1_o_0[6] ? in_6 : 8'bz;  // Controlled_Buffer controlled_buffer_57
  assign out_23 = n4bitdecoder_1_o_0[7] ? in_5 : 8'bz;  // Controlled_Buffer controlled_buffer_58
  assign out_23 = n4bitdecoder_1_o_0[8] ? in_4 : 8'bz;  // Controlled_Buffer controlled_buffer_59
  assign out_23 = n4bitdecoder_1_o_0[9] ? Mover_2 : 8'bz;  // Controlled_Buffer controlled_buffer_60
  assign out_25 = n4bitdecoder_1_o_0[0] ? A : 8'bz;  // Controlled_Buffer controlled_buffer_61
  assign out_25 = n4bitdecoder_1_o_0[1] ? in_11 : 8'bz;  // Controlled_Buffer controlled_buffer_62
  assign out_25 = n4bitdecoder_1_o_0[2] ? in_10 : 8'bz;  // Controlled_Buffer controlled_buffer_63
  assign out_25 = n4bitdecoder_1_o_0[3] ? in_9 : 8'bz;  // Controlled_Buffer controlled_buffer_64
  assign out_25 = n4bitdecoder_1_o_0[4] ? in_8 : 8'bz;  // Controlled_Buffer controlled_buffer_65
  assign out_25 = n4bitdecoder_1_o_0[5] ? in_7 : 8'bz;  // Controlled_Buffer controlled_buffer_66
  assign out_25 = n4bitdecoder_1_o_0[6] ? in_6 : 8'bz;  // Controlled_Buffer controlled_buffer_67
  assign out_25 = n4bitdecoder_1_o_0[7] ? in_5 : 8'bz;  // Controlled_Buffer controlled_buffer_68
  assign out_25 = n4bitdecoder_1_o_0[8] ? in_4 : 8'bz;  // Controlled_Buffer controlled_buffer_69
  assign out_25 = n4bitdecoder_1_o_0[9] ? Mover_2 : 8'bz;  // Controlled_Buffer controlled_buffer_70
  assign out_27 = n4bitdecoder_1_o_0[0] ? A : 8'bz;  // Controlled_Buffer controlled_buffer_71
  assign out_27 = n4bitdecoder_1_o_0[1] ? in_11 : 8'bz;  // Controlled_Buffer controlled_buffer_72
  assign out_27 = n4bitdecoder_1_o_0[2] ? in_10 : 8'bz;  // Controlled_Buffer controlled_buffer_73
  assign out_27 = n4bitdecoder_1_o_0[3] ? in_9 : 8'bz;  // Controlled_Buffer controlled_buffer_74
  assign out_27 = n4bitdecoder_1_o_0[4] ? in_8 : 8'bz;  // Controlled_Buffer controlled_buffer_75
  assign out_27 = n4bitdecoder_1_o_0[5] ? in_7 : 8'bz;  // Controlled_Buffer controlled_buffer_76
  assign out_27 = n4bitdecoder_1_o_0[6] ? in_6 : 8'bz;  // Controlled_Buffer controlled_buffer_77
  assign out_27 = n4bitdecoder_1_o_0[7] ? in_5 : 8'bz;  // Controlled_Buffer controlled_buffer_78
  assign out_27 = n4bitdecoder_1_o_0[8] ? in_4 : 8'bz;  // Controlled_Buffer controlled_buffer_79
  assign out_27 = n4bitdecoder_1_o_0[9] ? Mover_2 : 8'bz;  // Controlled_Buffer controlled_buffer_80
  assign out_29 = n4bitdecoder_1_o_0[0] ? A : 8'bz;  // Controlled_Buffer controlled_buffer_81
  assign out_29 = n4bitdecoder_1_o_0[1] ? in_11 : 8'bz;  // Controlled_Buffer controlled_buffer_82
  assign out_29 = n4bitdecoder_1_o_0[2] ? in_10 : 8'bz;  // Controlled_Buffer controlled_buffer_83
  assign out_29 = n4bitdecoder_1_o_0[3] ? in_9 : 8'bz;  // Controlled_Buffer controlled_buffer_84
  assign out_29 = n4bitdecoder_1_o_0[4] ? in_8 : 8'bz;  // Controlled_Buffer controlled_buffer_85
  assign out_29 = n4bitdecoder_1_o_0[5] ? in_7 : 8'bz;  // Controlled_Buffer controlled_buffer_86
  assign out_29 = n4bitdecoder_1_o_0[6] ? in_6 : 8'bz;  // Controlled_Buffer controlled_buffer_87
  assign out_29 = n4bitdecoder_1_o_0[7] ? in_5 : 8'bz;  // Controlled_Buffer controlled_buffer_88
  assign out_29 = n4bitdecoder_1_o_0[8] ? in_4 : 8'bz;  // Controlled_Buffer controlled_buffer_89
  assign out_29 = n4bitdecoder_1_o_0[9] ? Mover_2 : 8'bz;  // Controlled_Buffer controlled_buffer_90
  assign Mover_2_2 = n4bitdecoder_1_o_0[0] ? A : 8'bz;  // Controlled_Buffer controlled_buffer_91
  assign Mover_2_2 = n4bitdecoder_1_o_0[1] ? in_11 : 8'bz;  // Controlled_Buffer controlled_buffer_92
  assign Mover_2_2 = n4bitdecoder_1_o_0[2] ? in_10 : 8'bz;  // Controlled_Buffer controlled_buffer_93
  assign Mover_2_2 = n4bitdecoder_1_o_0[3] ? in_9 : 8'bz;  // Controlled_Buffer controlled_buffer_94
  assign Mover_2_2 = n4bitdecoder_1_o_0[4] ? in_8 : 8'bz;  // Controlled_Buffer controlled_buffer_95
  assign Mover_2_2 = n4bitdecoder_1_o_0[5] ? in_7 : 8'bz;  // Controlled_Buffer controlled_buffer_96
  assign Mover_2_2 = n4bitdecoder_1_o_0[6] ? in_6 : 8'bz;  // Controlled_Buffer controlled_buffer_97
  assign Mover_2_2 = n4bitdecoder_1_o_0[7] ? in_5 : 8'bz;  // Controlled_Buffer controlled_buffer_98
  assign Mover_2_2 = n4bitdecoder_1_o_0[8] ? in_4 : 8'bz;  // Controlled_Buffer controlled_buffer_99
  assign Mover_2_2 = n4bitdecoder_1_o_0[9] ? Mover_2 : 8'bz;  // Controlled_Buffer controlled_buffer_100
  assign out_14 = X ? n4bitdecoder_2_o_0 : 1'bz;  // Controlled_Buffer controlled_buffer_101
  assign out_16 = X ? n4bitdecoder_2_out_3 : 1'bz;  // Controlled_Buffer controlled_buffer_102
  assign out_18 = X ? n4bitdecoder_2_out_4 : 1'bz;  // Controlled_Buffer controlled_buffer_103
  assign out_20 = X ? n4bitdecoder_2_out_5 : 1'bz;  // Controlled_Buffer controlled_buffer_104
  assign out_22 = X ? n4bitdecoder_2_out_6 : 1'bz;  // Controlled_Buffer controlled_buffer_105
  assign out_24 = X ? n4bitdecoder_2_out_7 : 1'bz;  // Controlled_Buffer controlled_buffer_106
  assign out_26 = X ? n4bitdecoder_2_out_8 : 1'bz;  // Controlled_Buffer controlled_buffer_107
  assign out_28 = X ? n4bitdecoder_2_out_9 : 1'bz;  // Controlled_Buffer controlled_buffer_108
  assign out_30 = X ? n4bitdecoder_2_out_10 : 1'bz;  // Controlled_Buffer controlled_buffer_109
  assign out_32 = X ? n4bitdecoder_2_out_11 : 1'bz;  // Controlled_Buffer controlled_buffer_110
endmodule

module _4bitdecoder (
  input  [3:0] in_1,
  output O_0,
  output out_3,
  output out_4,
  output out_5,
  output out_6,
  output out_7,
  output out_8,
  output out_9,
  output out_10,
  output out_11,
  output out_12,
  output out_13,
  output out_14,
  output out_15,
  output out_16,
  output O_15
);

  wire not_1_out, not_2_out, not_3_out, not_4_out;

  not not_1 (not_1_out, in_1[2]);
  not not_2 (not_2_out, in_1[1]);
  not not_3 (not_3_out, in_1[3]);
  not not_4 (not_4_out, in_1[0]);
  and and_1 (O_0, not_4_out, not_2_out, not_1_out, not_3_out);
  and and_2 (out_3, not_4_out, not_2_out, not_1_out, in_1[3]);
  and and_3 (out_4, not_4_out, not_2_out, in_1[2], not_3_out);
  and and_4 (out_5, not_4_out, not_2_out, in_1[2], in_1[3]);
  and and_5 (out_6, not_4_out, in_1[1], not_1_out, not_3_out);
  and and_6 (out_7, not_4_out, in_1[1], not_1_out, in_1[3]);
  and and_7 (out_8, not_4_out, in_1[1], in_1[2], not_3_out);
  and and_8 (out_9, not_4_out, in_1[1], in_1[2], in_1[3]);
  and and_9 (out_10, in_1[0], not_2_out, not_1_out, not_3_out);
  and and_10 (out_11, in_1[0], not_2_out, not_1_out, in_1[3]);
  and and_11 (out_12, in_1[0], not_2_out, in_1[2], not_3_out);
  and and_12 (out_13, in_1[0], not_2_out, in_1[2], in_1[3]);
  and and_13 (out_14, in_1[0], in_1[1], not_1_out, not_3_out);
  and and_14 (out_15, in_1[0], in_1[1], not_1_out, in_1[3]);
  and and_15 (out_16, in_1[0], in_1[1], in_1[2], not_3_out);
  and and_16 (O_15, in_1[0], in_1[1], in_1[2], in_1[3]);
endmodule

module _6_64 (
  input  [5:0] in_1,
  input  in_2,
  output out_3,
  output out_4,
  output out_5,
  output out_6,
  output out_7,
  output out_8,
  output out_9,
  output out_10,
  output out_11,
  output out_12,
  output out_13,
  output out_14,
  output out_15,
  output out_16,
  output out_17,
  output out_18,
  output out_19,
  output out_20,
  output out_21,
  output out_22,
  output out_23,
  output out_24,
  output out_25,
  output out_26,
  output out_27,
  output out_28,
  output out_29,
  output out_30,
  output out_31,
  output out_32,
  output out_33,
  output out_34,
  output out_35,
  output out_36,
  output out_37,
  output out_38,
  output out_39,
  output out_40,
  output out_41,
  output out_42,
  output out_43,
  output out_44,
  output out_45,
  output out_46,
  output out_47,
  output out_48,
  output out_49,
  output out_50,
  output out_51,
  output out_52,
  output out_53,
  output out_54,
  output out_55,
  output out_56,
  output out_57,
  output out_58,
  output out_59,
  output out_60,
  output out_61,
  output out_62,
  output out_63,
  output out_64,
  output out_65,
  output out_66
);

  wire not_1_out;
  wire [5:0] controlled_buffer_1_out;

  assign controlled_buffer_1_out = in_2 ? in_1 : 6'bz;  // Controlled_Buffer controlled_buffer_1
  Pull_Resistor pull_resistor_1 (.node(controlled_buffer_1_out[5]));
  not not_1 (not_1_out, controlled_buffer_1_out[5]);
  Decoder #(.select(5), .disabled(0)) decoder_1 (
    .out0(out_3), .out1(out_4), .out2(out_5), .out3(out_6), .out4(out_7), .out5(out_8), .out6(out_9),
    .out7(out_10), .out8(out_11), .out9(out_12), .out10(out_13), .out11(out_14), .out12(out_15),
    .out13(out_16), .out14(out_17), .out15(out_18), .out16(out_19), .out17(out_20), .out18(out_21),
    .out19(out_22), .out20(out_23), .out21(out_24), .out22(out_25), .out23(out_26), .out24(out_27),
    .out25(out_28), .out26(out_29), .out27(out_30), .out28(out_31), .out29(out_32), .out30(out_33),
    .out31(out_34), .sel(controlled_buffer_1_out[4:0]), .en(not_1_out));
  Decoder #(.select(5), .disabled(0)) decoder_2 (
    .out0(out_35), .out1(out_36), .out2(out_37), .out3(out_38), .out4(out_39), .out5(out_40), .out6(out_41),
    .out7(out_42), .out8(out_43), .out9(out_44), .out10(out_45), .out11(out_46), .out12(out_47),
    .out13(out_48), .out14(out_49), .out15(out_50), .out16(out_51), .out17(out_52), .out18(out_53),
    .out19(out_54), .out20(out_55), .out21(out_56), .out22(out_57), .out23(out_58), .out24(out_59),
    .out25(out_60), .out26(out_61), .out27(out_62), .out28(out_63), .out29(out_64), .out30(out_65),
    .out31(out_66), .sel(controlled_buffer_1_out[4:0]), .en(controlled_buffer_1_out[5]));
  Pull_Resistor pull_resistor_2 (.node({out_34, out_33, out_32, out_31, out_30, out_29, out_28, out_27, out_26, out_25, out_24, out_23, out_22, out_21, out_20, out_19, out_18, out_17, out_16, out_15, out_14, out_13, out_12, out_11, out_10, out_9, out_8, out_7, out_6, out_5, out_4, out_3}));
  Pull_Resistor pull_resistor_3 (.node({out_66, out_65, out_64, out_63, out_62, out_61, out_60, out_59, out_58, out_57, out_56, out_55, out_54, out_53, out_52, out_51, out_50, out_49, out_48, out_47, out_46, out_45, out_44, out_43, out_42, out_41, out_40, out_39, out_38, out_37, out_36, out_35}));
endmodule

module _7_128 (
  input  [6:0] in_1,
  input  in_2,
  output out_3,
  output out_4,
  output out_5,
  output out_6,
  output out_7,
  output out_8,
  output out_9,
  output out_10,
  output out_11,
  output out_12,
  output out_13,
  output out_14,
  output out_15,
  output out_16,
  output out_17,
  output out_18,
  output out_19,
  output out_20,
  output out_21,
  output out_22,
  output out_23,
  output out_24,
  output out_25,
  output out_26,
  output out_27,
  output out_28,
  output out_29,
  output out_30,
  output out_31,
  output out_32,
  output out_33,
  output out_34,
  output out_35,
  output out_36,
  output out_37,
  output out_38,
  output out_39,
  output out_40,
  output out_41,
  output out_42,
  output out_43,
  output out_44,
  output out_45,
  output out_46,
  output out_47,
  output out_48,
  output out_49,
  output out_50,
  output out_51,
  output out_52,
  output out_53,
  output out_54,
  output out_55,
  output out_56,
  output out_57,
  output out_58,
  output out_59,
  output out_60,
  output out_61,
  output out_62,
  output out_63,
  output out_64,
  output out_65,
  output out_66,
  output out_67,
  output out_68,
  output out_69,
  output out_70,
  output out_71,
  output out_72,
  output out_73,
  output out_74,
  output out_75,
  output out_76,
  output out_77,
  output out_78,
  output out_79,
  output out_80,
  output out_81,
  output out_82,
  output out_83,
  output out_84,
  output out_85,
  output out_86,
  output out_87,
  output out_88,
  output out_89,
  output out_90,
  output out_91,
  output out_92,
  output out_93,
  output out_94,
  output out_95,
  output out_96,
  output out_97,
  output out_98,
  output out_99,
  output out_100,
  output out_101,
  output out_102,
  output out_103,
  output out_104,
  output out_105,
  output out_106,
  output out_107,
  output out_108,
  output out_109,
  output out_110,
  output out_111,
  output out_112,
  output out_113,
  output out_114,
  output out_115,
  output out_116,
  output out_117,
  output out_118,
  output out_119,
  output out_120,
  output out_121,
  output out_122,
  output out_123,
  output out_124,
  output out_125,
  output out_126,
  output out_127,
  output out_128,
  output out_129,
  output out_130
);

  wire not_1_out;
  wire [6:0] controlled_buffer_1_out;

  assign controlled_buffer_1_out = in_2 ? in_1 : 7'bz;  // Controlled_Buffer controlled_buffer_1
  Pull_Resistor pull_resistor_1 (.node(controlled_buffer_1_out[6]));
  _6_64 u_6_64_1 (
    .in_1(controlled_buffer_1_out[5:0]), .in_2(not_1_out), .out_3(out_3), .out_4(out_4), .out_5(out_5),
    .out_6(out_6), .out_7(out_7), .out_8(out_8), .out_9(out_9), .out_10(out_10), .out_11(out_11),
    .out_12(out_12), .out_13(out_13), .out_14(out_14), .out_15(out_15), .out_16(out_16), .out_17(out_17),
    .out_18(out_18), .out_19(out_19), .out_20(out_20), .out_21(out_21), .out_22(out_22), .out_23(out_23),
    .out_24(out_24), .out_25(out_25), .out_26(out_26), .out_27(out_27), .out_28(out_28), .out_29(out_29),
    .out_30(out_30), .out_31(out_31), .out_32(out_32), .out_33(out_33), .out_34(out_34), .out_35(out_35),
    .out_36(out_36), .out_37(out_37), .out_38(out_38), .out_39(out_39), .out_40(out_40), .out_41(out_41),
    .out_42(out_42), .out_43(out_43), .out_44(out_44), .out_45(out_45), .out_46(out_46), .out_47(out_47),
    .out_48(out_48), .out_49(out_49), .out_50(out_50), .out_51(out_51), .out_52(out_52), .out_53(out_53),
    .out_54(out_54), .out_55(out_55), .out_56(out_56), .out_57(out_57), .out_58(out_58), .out_59(out_59),
    .out_60(out_60), .out_61(out_61), .out_62(out_62), .out_63(out_63), .out_64(out_64), .out_65(out_65),
    .out_66(out_66));
  not not_1 (not_1_out, controlled_buffer_1_out[6]);
  _6_64 u_6_64_2 (
    .in_1(controlled_buffer_1_out[5:0]), .in_2(controlled_buffer_1_out[6]), .out_3(out_67), .out_4(out_68),
    .out_5(out_69), .out_6(out_70), .out_7(out_71), .out_8(out_72), .out_9(out_73), .out_10(out_74),
    .out_11(out_75), .out_12(out_76), .out_13(out_77), .out_14(out_78), .out_15(out_79), .out_16(out_80),
    .out_17(out_81), .out_18(out_82), .out_19(out_83), .out_20(out_84), .out_21(out_85), .out_22(out_86),
    .out_23(out_87), .out_24(out_88), .out_25(out_89), .out_26(out_90), .out_27(out_91), .out_28(out_92),
    .out_29(out_93), .out_30(out_94), .out_31(out_95), .out_32(out_96), .out_33(out_97), .out_34(out_98),
    .out_35(out_99), .out_36(out_100), .out_37(out_101), .out_38(out_102), .out_39(out_103),
    .out_40(out_104), .out_41(out_105), .out_42(out_106), .out_43(out_107), .out_44(out_108),
    .out_45(out_109), .out_46(out_110), .out_47(out_111), .out_48(out_112), .out_49(out_113),
    .out_50(out_114), .out_51(out_115), .out_52(out_116), .out_53(out_117), .out_54(out_118),
    .out_55(out_119), .out_56(out_120), .out_57(out_121), .out_58(out_122), .out_59(out_123),
    .out_60(out_124), .out_61(out_125), .out_62(out_126), .out_63(out_127), .out_64(out_128),
    .out_65(out_129), .out_66(out_130));
endmodule

module _8_256 (
  input  [7:0] in_1,
  input  in_2,
  output out_3,
  output out_4,
  output out_5,
  output out_6,
  output out_7,
  output out_8,
  output out_9,
  output out_10,
  output out_11,
  output out_12,
  output out_13,
  output out_14,
  output out_15,
  output out_16,
  output out_17,
  output out_18,
  output out_19,
  output out_20,
  output out_21,
  output out_22,
  output out_23,
  output out_24,
  output out_25,
  output out_26,
  output out_27,
  output out_28,
  output out_29,
  output out_30,
  output out_31,
  output out_32,
  output out_33,
  output out_34,
  output out_35,
  output out_36,
  output out_37,
  output out_38,
  output out_39,
  output out_40,
  output out_41,
  output out_42,
  output out_43,
  output out_44,
  output out_45,
  output out_46,
  output out_47,
  output out_48,
  output out_49,
  output out_50,
  output out_51,
  output out_52,
  output out_53,
  output out_54,
  output out_55,
  output out_56,
  output out_57,
  output out_58,
  output out_59,
  output out_60,
  output out_61,
  output out_62,
  output out_63,
  output out_64,
  output out_65,
  output out_66,
  output out_67,
  output out_68,
  output out_69,
  output out_70,
  output out_71,
  output out_72,
  output out_73,
  output out_74,
  output out_75,
  output out_76,
  output out_77,
  output out_78,
  output out_79,
  output out_80,
  output out_81,
  output out_82,
  output out_83,
  output out_84,
  output out_85,
  output out_86,
  output out_87,
  output out_88,
  output out_89,
  output out_90,
  output out_91,
  output out_92,
  output out_93,
  output out_94,
  output out_95,
  output out_96,
  output out_97,
  output out_98,
  output out_99,
  output out_100,
  output out_101,
  output out_102,
  output out_103,
  output out_104,
  output out_105,
  output out_106,
  output out_107,
  output out_108,
  output out_109,
  output out_110,
  output out_111,
  output out_112,
  output out_113,
  output out_114,
  output out_115,
  output out_116,
  output out_117,
  output out_118,
  output out_119,
  output out_120,
  output out_121,
  output out_122,
  output out_123,
  output out_124,
  output out_125,
  output out_126,
  output out_127,
  output out_128,
  output out_129,
  output out_130,
  output out_131,
  output out_132,
  output out_133,
  output out_134,
  output out_135,
  output out_136,
  output out_137,
  output out_138,
  output out_139,
  output out_140,
  output out_141,
  output out_142,
  output out_143,
  output out_144,
  output out_145,
  output out_146,
  output out_147,
  output out_148,
  output out_149,
  output out_150,
  output out_151,
  output out_152,
  output out_153,
  output out_154,
  output out_155,
  output out_156,
  output out_157,
  output out_158,
  output out_159,
  output out_160,
  output out_161,
  output out_162,
  output out_163,
  output out_164,
  output out_165,
  output out_166,
  output out_167,
  output out_168,
  output out_169,
  output out_170,
  output out_171,
  output out_172,
  output out_173,
  output out_174,
  output out_175,
  output out_176,
  output out_177,
  output out_178,
  output out_179,
  output out_180,
  output out_181,
  output out_182,
  output out_183,
  output out_184,
  output out_185,
  output out_186,
  output out_187,
  output out_188,
  output out_189,
  output out_190,
  output out_191,
  output out_192,
  output out_193,
  output out_194,
  output out_195,
  output out_196,
  output out_197,
  output out_198,
  output out_199,
  output out_200,
  output out_201,
  output out_202,
  output out_203,
  output out_204,
  output out_205,
  output out_206,
  output out_207,
  output out_208,
  output out_209,
  output out_210,
  output out_211,
  output out_212,
  output out_213,
  output out_214,
  output out_215,
  output out_216,
  output out_217,
  output out_218,
  output out_219,
  output out_220,
  output out_221,
  output out_222,
  output out_223,
  output out_224,
  output out_225,
  output out_226,
  output out_227,
  output out_228,
  output out_229,
  output out_230,
  output out_231,
  output out_232,
  output out_233,
  output out_234,
  output out_235,
  output out_236,
  output out_237,
  output out_238,
  output out_239,
  output out_240,
  output out_241,
  output out_242,
  output out_243,
  output out_244,
  output out_245,
  output out_246,
  output out_247,
  output out_248,
  output out_249,
  output out_250,
  output out_251,
  output out_252,
  output out_253,
  output out_254,
  output out_255,
  output out_256,
  output out_257,
  output out_258
);

  wire not_1_out;
  wire [7:0] controlled_buffer_1_out;

  Pull_Resistor pull_resistor_1 (.node(controlled_buffer_1_out[7]));
  assign controlled_buffer_1_out = in_2 ? in_1 : 8'bz;  // Controlled_Buffer controlled_buffer_1
  _7_128 u_7_128_1 (
    .in_1(controlled_buffer_1_out[6:0]), .in_2(not_1_out), .out_3(out_3), .out_4(out_4), .out_5(out_5),
    .out_6(out_6), .out_7(out_7), .out_8(out_8), .out_9(out_9), .out_10(out_10), .out_11(out_11),
    .out_12(out_12), .out_13(out_13), .out_14(out_14), .out_15(out_15), .out_16(out_16), .out_17(out_17),
    .out_18(out_18), .out_19(out_19), .out_20(out_20), .out_21(out_21), .out_22(out_22), .out_23(out_23),
    .out_24(out_24), .out_25(out_25), .out_26(out_26), .out_27(out_27), .out_28(out_28), .out_29(out_29),
    .out_30(out_30), .out_31(out_31), .out_32(out_32), .out_33(out_33), .out_34(out_34), .out_35(out_35),
    .out_36(out_36), .out_37(out_37), .out_38(out_38), .out_39(out_39), .out_40(out_40), .out_41(out_41),
    .out_42(out_42), .out_43(out_43), .out_44(out_44), .out_45(out_45), .out_46(out_46), .out_47(out_47),
    .out_48(out_48), .out_49(out_49), .out_50(out_50), .out_51(out_51), .out_52(out_52), .out_53(out_53),
    .out_54(out_54), .out_55(out_55), .out_56(out_56), .out_57(out_57), .out_58(out_58), .out_59(out_59),
    .out_60(out_60), .out_61(out_61), .out_62(out_62), .out_63(out_63), .out_64(out_64), .out_65(out_65),
    .out_66(out_66), .out_67(out_67), .out_68(out_68), .out_69(out_69), .out_70(out_70), .out_71(out_71),
    .out_72(out_72), .out_73(out_73), .out_74(out_74), .out_75(out_75), .out_76(out_76), .out_77(out_77),
    .out_78(out_78), .out_79(out_79), .out_80(out_80), .out_81(out_81), .out_82(out_82), .out_83(out_83),
    .out_84(out_84), .out_85(out_85), .out_86(out_86), .out_87(out_87), .out_88(out_88), .out_89(out_89),
    .out_90(out_90), .out_91(out_91), .out_92(out_92), .out_93(out_93), .out_94(out_94), .out_95(out_95),
    .out_96(out_96), .out_97(out_97), .out_98(out_98), .out_99(out_99), .out_100(out_100), .out_101(out_101),
    .out_102(out_102), .out_103(out_103), .out_104(out_104), .out_105(out_105), .out_106(out_106),
    .out_107(out_107), .out_108(out_108), .out_109(out_109), .out_110(out_110), .out_111(out_111),
    .out_112(out_112), .out_113(out_113), .out_114(out_114), .out_115(out_115), .out_116(out_116),
    .out_117(out_117), .out_118(out_118), .out_119(out_119), .out_120(out_120), .out_121(out_121),
    .out_122(out_122), .out_123(out_123), .out_124(out_124), .out_125(out_125), .out_126(out_126),
    .out_127(out_127), .out_128(out_128), .out_129(out_129), .out_130(out_130));
  not not_1 (not_1_out, controlled_buffer_1_out[7]);
  _7_128 u_7_128_2 (
    .in_1(controlled_buffer_1_out[6:0]), .in_2(controlled_buffer_1_out[7]), .out_3(out_131), .out_4(out_132),
    .out_5(out_133), .out_6(out_134), .out_7(out_135), .out_8(out_136), .out_9(out_137), .out_10(out_138),
    .out_11(out_139), .out_12(out_140), .out_13(out_141), .out_14(out_142), .out_15(out_143),
    .out_16(out_144), .out_17(out_145), .out_18(out_146), .out_19(out_147), .out_20(out_148),
    .out_21(out_149), .out_22(out_150), .out_23(out_151), .out_24(out_152), .out_25(out_153),
    .out_26(out_154), .out_27(out_155), .out_28(out_156), .out_29(out_157), .out_30(out_158),
    .out_31(out_159), .out_32(out_160), .out_33(out_161), .out_34(out_162), .out_35(out_163),
    .out_36(out_164), .out_37(out_165), .out_38(out_166), .out_39(out_167), .out_40(out_168),
    .out_41(out_169), .out_42(out_170), .out_43(out_171), .out_44(out_172), .out_45(out_173),
    .out_46(out_174), .out_47(out_175), .out_48(out_176), .out_49(out_177), .out_50(out_178),
    .out_51(out_179), .out_52(out_180), .out_53(out_181), .out_54(out_182), .out_55(out_183),
    .out_56(out_184), .out_57(out_185), .out_58(out_186), .out_59(out_187), .out_60(out_188),
    .out_61(out_189), .out_62(out_190), .out_63(out_191), .out_64(out_192), .out_65(out_193),
    .out_66(out_194), .out_67(out_195), .out_68(out_196), .out_69(out_197), .out_70(out_198),
    .out_71(out_199), .out_72(out_200), .out_73(out_201), .out_74(out_202), .out_75(out_203),
    .out_76(out_204), .out_77(out_205), .out_78(out_206), .out_79(out_207), .out_80(out_208),
    .out_81(out_209), .out_82(out_210), .out_83(out_211), .out_84(out_212), .out_85(out_213),
    .out_86(out_214), .out_87(out_215), .out_88(out_216), .out_89(out_217), .out_90(out_218),
    .out_91(out_219), .out_92(out_220), .out_93(out_221), .out_94(out_222), .out_95(out_223),
    .out_96(out_224), .out_97(out_225), .out_98(out_226), .out_99(out_227), .out_100(out_228),
    .out_101(out_229), .out_102(out_230), .out_103(out_231), .out_104(out_232), .out_105(out_233),
    .out_106(out_234), .out_107(out_235), .out_108(out_236), .out_109(out_237), .out_110(out_238),
    .out_111(out_239), .out_112(out_240), .out_113(out_241), .out_114(out_242), .out_115(out_243),
    .out_116(out_244), .out_117(out_245), .out_118(out_246), .out_119(out_247), .out_120(out_248),
    .out_121(out_249), .out_122(out_250), .out_123(out_251), .out_124(out_252), .out_125(out_253),
    .out_126(out_254), .out_127(out_255), .out_128(out_256), .out_129(out_257), .out_130(out_258));
endmodule
module hyper4router (
  input  [7:0] in_1,
  input  S,
  input  [7:0] R,
  input  [7:0] in_4,
  input  [7:0] in_5,
  input  [7:0] _2,
  output [7:0] R_2,
  output out_8,
  output [7:0] I,
  output out_10,
  output [7:0] _1,
  output out_12,
  output [7:0] _2_2,
  output out_14
);

  wire decoder_1_out0, decoder_1_out1, decoder_1_out2, decoder_1_out3, decoder_2_out0, decoder_2_out1,
       decoder_2_out2, decoder_2_out3;

  Decoder #(.select(2), .enable("false")) decoder_1 (
    .out0(decoder_1_out0), .out1(decoder_1_out1), .out2(decoder_1_out2), .out3(decoder_1_out3),
    .sel(in_1[1:0]));
  Decoder #(.select(2), .enable("false")) decoder_2 (
    .out0(decoder_2_out0), .out1(decoder_2_out1), .out2(decoder_2_out2), .out3(decoder_2_out3),
    .sel(in_1[3:2]));
  assign R_2 = decoder_1_out0 ? _2 : 8'bz;  // Controlled_Buffer controlled_buffer_1
  assign R_2 = decoder_1_out1 ? in_5 : 8'bz;  // Controlled_Buffer controlled_buffer_2
  assign R_2 = decoder_1_out2 ? in_4 : 8'bz;  // Controlled_Buffer controlled_buffer_3
  assign R_2 = decoder_1_out3 ? R : 8'bz;  // Controlled_Buffer controlled_buffer_4
  assign I = decoder_1_out0 ? _2 : 8'bz;  // Controlled_Buffer controlled_buffer_5
  assign I = decoder_1_out1 ? in_5 : 8'bz;  // Controlled_Buffer controlled_buffer_6
  assign I = decoder_1_out2 ? in_4 : 8'bz;  // Controlled_Buffer controlled_buffer_7
  assign I = decoder_1_out3 ? R : 8'bz;  // Controlled_Buffer controlled_buffer_8
  assign _1 = decoder_1_out0 ? _2 : 8'bz;  // Controlled_Buffer controlled_buffer_9
  assign _1 = decoder_1_out1 ? in_5 : 8'bz;  // Controlled_Buffer controlled_buffer_10
  assign _1 = decoder_1_out2 ? in_4 : 8'bz;  // Controlled_Buffer controlled_buffer_11
  assign _1 = decoder_1_out3 ? R : 8'bz;  // Controlled_Buffer controlled_buffer_12
  assign _2_2 = decoder_1_out0 ? _2 : 8'bz;  // Controlled_Buffer controlled_buffer_13
  assign _2_2 = decoder_1_out1 ? in_5 : 8'bz;  // Controlled_Buffer controlled_buffer_14
  assign _2_2 = decoder_1_out2 ? in_4 : 8'bz;  // Controlled_Buffer controlled_buffer_15
  assign _2_2 = decoder_1_out3 ? R : 8'bz;  // Controlled_Buffer controlled_buffer_16
  assign out_8 = S ? decoder_2_out0 : 1'bz;  // Controlled_Buffer controlled_buffer_17
  assign out_10 = S ? decoder_2_out1 : 1'bz;  // Controlled_Buffer controlled_buffer_18
  assign out_12 = S ? decoder_2_out2 : 1'bz;  // Controlled_Buffer controlled_buffer_19
  assign out_14 = S ? decoder_2_out3 : 1'bz;  // Controlled_Buffer controlled_buffer_20
endmodule

module _64constant (
  input  in_1,
  input  in_2,
  input  in_3,
  input  in_4,
  input  in_5,
  input  in_6,
  input  in_7,
  input  in_8,
  input  in_9,
  input  in_10,
  input  in_11,
  input  in_12,
  input  in_13,
  input  in_14,
  input  in_15,
  input  in_16,
  input  in_17,
  input  in_18,
  input  in_19,
  input  in_20,
  input  in_21,
  input  in_22,
  input  in_23,
  input  in_24,
  input  in_25,
  input  in_26,
  input  in_27,
  input  in_28,
  input  in_29,
  input  in_30,
  input  in_31,
  input  in_32,
  input  in_33,
  input  in_34,
  input  in_35,
  input  in_36,
  input  in_37,
  input  in_38,
  input  in_39,
  input  in_40,
  input  in_41,
  input  in_42,
  input  in_43,
  input  in_44,
  input  in_45,
  input  in_46,
  input  in_47,
  input  in_48,
  input  in_49,
  input  in_50,
  input  in_51,
  input  in_52,
  input  in_53,
  input  in_54,
  input  in_55,
  input  in_56,
  input  in_57,
  input  in_58,
  input  in_59,
  input  in_60,
  input  in_61,
  input  in_62,
  input  in_63,
  input  in_64,
  output out_65,
  output [7:0] out_66
);

  wire _64endode01, _64endode11, or_2_out, or_3_out, priority_encoder_1_gs, priority_encoder_2_en_out,
       priority_encoder_2_gs, priority_encoder_3_en_out, priority_encoder_3_gs, priority_encoder_4_en_out,
       priority_encoder_4_gs, priority_encoder_5_en_out, priority_encoder_5_gs, priority_encoder_6_en_out,
       priority_encoder_6_gs, priority_encoder_7_en_out, priority_encoder_7_gs, priority_encoder_8_en_out,
       priority_encoder_8_gs;
  wire [0:0] priority_encoder_1_out, priority_encoder_2_out, priority_encoder_3_out, priority_encoder_4_out,
       priority_encoder_5_out, priority_encoder_6_out, priority_encoder_7_out, priority_encoder_8_out;
  wire [5:0] or_5_out;
  wire [7:0] _64endode0, _64endode1;

  or or_1 (out_65, or_2_out, or_3_out);
  or or_2 (or_2_out, in_1, in_2, in_3, in_4, in_5, in_6, in_7, in_8, in_9, in_10, in_11, in_12, in_13, in_14, in_15, in_16, in_18, in_19, in_20, in_21, in_22, in_23, in_24, in_25, in_26, in_27, in_28, in_29, in_30, in_31, in_32, in_17);
  or or_3 (or_3_out, in_33, in_34, in_35, in_36, in_37, in_38, in_39, in_40, in_41, in_42, in_43, in_44, in_45, in_46, in_47, in_48, in_50, in_51, in_52, in_53, in_54, in_55, in_56, in_57, in_58, in_59, in_60, in_61, in_62, in_63, in_64, in_49);
  ROM #(.addrWidth(6)) rom_1 (
    .addr({or_5_out[5:3], _64endode11, _64endode01, or_5_out[0]}), .data(out_66));  // open: sel
  Priority_Encoder #(.disabled(0)) priority_encoder_1 (
    .in0(in_1), .in1(in_2), .in2(in_3), .in3(in_4), .in4(in_5), .in5(in_6), .in6(in_7), .in7(in_8),
    .out({_64endode1[0], _64endode0[0], priority_encoder_1_out[0]}), .en_in(priority_encoder_2_en_out),
    .gs(priority_encoder_1_gs));  // open: en_out
  Priority_Encoder #(.disabled(0)) priority_encoder_2 (
    .in0(in_9), .in1(in_10), .in2(in_11), .in3(in_12), .in4(in_13), .in5(in_14), .in6(in_15), .in7(in_16),
    .out({_64endode1[1], _64endode0[1], priority_encoder_2_out[0]}), .en_in(priority_encoder_3_en_out),
    .gs(priority_encoder_2_gs), .en_out(priority_encoder_2_en_out));
  Priority_Encoder #(.disabled(0)) priority_encoder_3 (
    .in0(in_17), .in1(in_18), .in2(in_19), .in3(in_20), .in4(in_21), .in5(in_22), .in6(in_23), .in7(in_24),
    .out({_64endode1[2], _64endode0[2], priority_encoder_3_out[0]}), .en_in(priority_encoder_4_en_out),
    .gs(priority_encoder_3_gs), .en_out(priority_encoder_3_en_out));
  Priority_Encoder #(.disabled(0)) priority_encoder_4 (
    .in0(in_25), .in1(in_26), .in2(in_27), .in3(in_28), .in4(in_29), .in5(in_30), .in6(in_31), .in7(in_32),
    .out({_64endode1[3], _64endode0[3], priority_encoder_4_out[0]}), .en_in(priority_encoder_5_en_out),
    .gs(priority_encoder_4_gs), .en_out(priority_encoder_4_en_out));
  Priority_Encoder #(.disabled(0)) priority_encoder_5 (
    .in0(in_33), .in1(in_34), .in2(in_35), .in3(in_36), .in4(in_37), .in5(in_38), .in6(in_39), .in7(in_40),
    .out({_64endode1[4], _64endode0[4], priority_encoder_5_out[0]}), .en_in(priority_encoder_6_en_out),
    .gs(priority_encoder_5_gs), .en_out(priority_encoder_5_en_out));
  Priority_Encoder #(.disabled(0)) priority_encoder_6 (
    .in0(in_41), .in1(in_42), .in2(in_43), .in3(in_44), .in4(in_45), .in5(in_46), .in6(in_47), .in7(in_48),
    .out({_64endode1[5], _64endode0[5], priority_encoder_6_out[0]}), .en_in(priority_encoder_7_en_out),
    .gs(priority_encoder_6_gs), .en_out(priority_encoder_6_en_out));
  Priority_Encoder #(.disabled(0)) priority_encoder_7 (
    .in0(in_49), .in1(in_50), .in2(in_51), .in3(in_52), .in4(in_53), .in5(in_54), .in6(in_55), .in7(in_56),
    .out({_64endode1[6], _64endode0[6], priority_encoder_7_out[0]}), .en_in(priority_encoder_8_en_out),
    .gs(priority_encoder_7_gs), .en_out(priority_encoder_7_en_out));
  Priority_Encoder #(.disabled(0)) priority_encoder_8 (
    .in0(in_57), .in1(in_58), .in2(in_59), .in3(in_60), .in4(in_61), .in5(in_62), .in6(in_63), .in7(in_64),
    .out({_64endode1[7], _64endode0[7], priority_encoder_8_out[0]}), .gs(priority_encoder_8_gs),
    .en_out(priority_encoder_8_en_out));  // open: en_in
  Priority_Encoder #(.disabled(0)) priority_encoder_9 (
    .in0(priority_encoder_1_gs), .in1(priority_encoder_2_gs), .in2(priority_encoder_3_gs),
    .in3(priority_encoder_4_gs), .in4(priority_encoder_5_gs), .in5(priority_encoder_6_gs),
    .in6(priority_encoder_7_gs), .in7(priority_encoder_8_gs), .out(or_5_out[5:3]));  // open: en_in, gs, en_out
  Pull_Resistor pull_resistor_1 (.node({priority_encoder_8_out[0], priority_encoder_7_out[0], priority_encoder_6_out[0], priority_encoder_5_out[0], priority_encoder_4_out[0], priority_encoder_3_out[0], priority_encoder_2_out[0], priority_encoder_1_out[0]}));
  Pull_Resistor pull_resistor_2 (.node(_64endode0));
  or or_4 (_64endode01, _64endode0[0], _64endode0[1], _64endode0[2], _64endode0[3], _64endode0[5], _64endode0[6], _64endode0[7], _64endode0[4]);
  Pull_Resistor pull_resistor_3 (.node(_64endode1));
  or or_5 (or_5_out[0], priority_encoder_1_out[0], priority_encoder_2_out[0], priority_encoder_3_out[0], priority_encoder_4_out[0], priority_encoder_5_out[0], priority_encoder_6_out[0], priority_encoder_7_out[0], priority_encoder_8_out[0]);
  Pull_Resistor pull_resistor_4 (.node(or_5_out[5]));
  Pull_Resistor pull_resistor_5 (.node(or_5_out[3]));
  Pull_Resistor pull_resistor_6 (.node(or_5_out[4]));
  or or_6 (_64endode11, _64endode1[0], _64endode1[1], _64endode1[2], _64endode1[3], _64endode1[5], _64endode1[6], _64endode1[7], _64endode1[4]);

  // Other names for the same wires on the sheet: afsfassaf = _64endode0[2]

  // Notes on the sheet:
  //   contents of rom_1 (hex, n*v repeats v):
  //   0 1 2 3 4 5 6 7 8 9 a b c d e f 10 11 12 13 14 15 16 17 18 19 1a 1b 1c 1d 1e 1f 20 21 22 23 24 25 26
  //   27 28 29 2a 2b 2c 2d 2e 2f 30 31 32 33 34 35 36 37 38 39 3a 3b 3c 3d 3e 3f
endmodule
