// Logisim project ht-pc_complete.circ as structural Verilog
module ht_pc (
);

  wire undriven;
  wire [7:0] commander_1_out_4, ram_1_out_5, rom_1_out_5;

  rom rom_1 (.out_5(rom_1_out_5));  // open: in_1, in_2, in_3, out_4
  commander commander_1 (.in_1(undriven), .out_4(commander_1_out_4), .in_2(rom_1_out_5), .in_3(ram_1_out_5));
  ram ram_1 (.out_5(ram_1_out_5));  // open: out_4, in_1, in_2, in_3
endmodule

module cpu (
  input  [7:0] in_1,
  input  [7:0] in_2,
  input  [7:0] in_3,
  input  [7:0] in_4,
  input  [7:0] in_5,
  output [7:0] out_6,
  output [7:0] out_7,
  output [7:0] out_8,
  output out_9,
  output out_10,
  output out_11,
  output out_12
);

  wire button_1_out, nor_1_out, undriven, undriven_2, undriven_3, undriven_4, undriven_5, undriven_6,
       undriven_7, undriven_8, undriven_9, undriven_10;
  wire [7:0] controlled_buffer_1_out, controlled_buffer_2_out, n8bitreg_2_out_3, n8bitreg_3_out_3,
       n8bitreg_4_out_3, n8bitreg_5_out_3, n8bitreg_6_out_3, n8bitreg_7_out_3, n8bitreg_8_out_3,
       n8bitreg_9_out_3, n8bitreg_10_out_3, n8bitreg_11_out_3;

  _8bitreg u_8bitreg_1 ();  // open: in_1, out_3, in_2
  assign controlled_buffer_1_out = nor_1_out ? in_5 : 8'bz;  // Controlled_Buffer controlled_buffer_1
  assign controlled_buffer_2_out = undriven ? n8bitreg_2_out_3 : 8'bz;  // Controlled_Buffer controlled_buffer_2
  _8bitreg u_8bitreg_2 (.in_1(button_1_out), .out_3(n8bitreg_2_out_3), .in_2(controlled_buffer_1_out));
  Button button_1 (.out(button_1_out));
  Controlled_Buffer #(.width(3)) controlled_buffer_3 (.in(in_4[2:0]), .en(nor_1_out));  // open: out
  nor nor_1 (nor_1_out, in_4[7], in_4[6], in_4[5], in_4[4], in_4[3]);
  assign controlled_buffer_2_out = undriven_2 ? n8bitreg_3_out_3 : 8'bz;  // Controlled_Buffer controlled_buffer_4
  _8bitreg u_8bitreg_3 (.in_1(button_1_out), .out_3(n8bitreg_3_out_3), .in_2(controlled_buffer_1_out));
  assign controlled_buffer_2_out = undriven_3 ? n8bitreg_4_out_3 : 8'bz;  // Controlled_Buffer controlled_buffer_5
  _8bitreg u_8bitreg_4 (.in_1(button_1_out), .out_3(n8bitreg_4_out_3), .in_2(controlled_buffer_1_out));
  assign controlled_buffer_2_out = undriven_4 ? n8bitreg_5_out_3 : 8'bz;  // Controlled_Buffer controlled_buffer_6
  _8bitreg u_8bitreg_5 (.in_1(button_1_out), .out_3(n8bitreg_5_out_3), .in_2(controlled_buffer_1_out));
  assign controlled_buffer_2_out = undriven_5 ? n8bitreg_6_out_3 : 8'bz;  // Controlled_Buffer controlled_buffer_7
  _8bitreg u_8bitreg_6 (.in_1(button_1_out), .out_3(n8bitreg_6_out_3), .in_2(controlled_buffer_1_out));
  assign controlled_buffer_2_out = undriven_6 ? n8bitreg_7_out_3 : 8'bz;  // Controlled_Buffer controlled_buffer_8
  _8bitreg u_8bitreg_7 (.in_1(button_1_out), .out_3(n8bitreg_7_out_3), .in_2(controlled_buffer_1_out));
  assign controlled_buffer_2_out = undriven_7 ? n8bitreg_8_out_3 : 8'bz;  // Controlled_Buffer controlled_buffer_9
  _8bitreg u_8bitreg_8 (.in_1(button_1_out), .out_3(n8bitreg_8_out_3), .in_2(controlled_buffer_1_out));
  assign controlled_buffer_2_out = undriven_8 ? n8bitreg_9_out_3 : 8'bz;  // Controlled_Buffer controlled_buffer_10
  _8bitreg u_8bitreg_9 (.in_1(button_1_out), .out_3(n8bitreg_9_out_3), .in_2(controlled_buffer_1_out));
  assign controlled_buffer_2_out = undriven_9 ? n8bitreg_10_out_3 : 8'bz;  // Controlled_Buffer controlled_buffer_11
  _8bitreg u_8bitreg_10 (.in_1(button_1_out), .out_3(n8bitreg_10_out_3), .in_2(controlled_buffer_1_out));
  assign controlled_buffer_2_out = undriven_10 ? n8bitreg_11_out_3 : 8'bz;  // Controlled_Buffer controlled_buffer_12
  _8bitreg u_8bitreg_11 (.in_1(button_1_out), .out_3(n8bitreg_11_out_3), .in_2(controlled_buffer_1_out));
endmodule

module _8bitreg (
  input  in_1,
  input  [7:0] in_2,
  output [7:0] out_3
);

  wire and_1_out, and_2_out, and_3_out, and_4_out, and_5_out, and_6_out, and_7_out, and_8_out, and_9_out,
       and_10_out, and_11_out, and_12_out, and_13_out, and_14_out, and_15_out, and_16_out, nor_2_out,
       nor_3_out, nor_6_out, nor_8_out, nor_10_out, nor_13_out, nor_14_out, nor_15_out, not_1_out, not_2_out,
       not_3_out, not_4_out, not_5_out, not_6_out, not_7_out, not_8_out;

  nor nor_1 (out_3[7], and_1_out, nor_2_out);
  and and_1 (and_1_out, not_1_out, in_1);
  not not_1 (not_1_out, in_2[7]);
  nor nor_2 (nor_2_out, out_3[7], and_3_out);
  and and_2 (and_2_out, not_2_out, in_1);
  and and_3 (and_3_out, in_1, in_2[7]);
  not not_2 (not_2_out, in_2[6]);
  nor nor_3 (nor_3_out, out_3[6], and_4_out);
  nor nor_4 (out_3[6], and_2_out, nor_3_out);
  and and_4 (and_4_out, in_1, in_2[6]);
  nor nor_5 (out_3[5], and_5_out, nor_6_out);
  and and_5 (and_5_out, not_3_out, in_1);
  not not_3 (not_3_out, in_2[5]);
  nor nor_6 (nor_6_out, out_3[5], and_7_out);
  nor nor_7 (out_3[4], and_6_out, nor_8_out);
  and and_6 (and_6_out, not_4_out, in_1);
  and and_7 (and_7_out, in_1, in_2[5]);
  not not_4 (not_4_out, in_2[4]);
  nor nor_8 (nor_8_out, out_3[4], and_8_out);
  and and_8 (and_8_out, in_1, in_2[4]);
  not not_5 (not_5_out, in_2[3]);
  nor nor_9 (out_3[3], and_10_out, nor_10_out);
  nor nor_10 (nor_10_out, out_3[3], and_9_out);
  and and_9 (and_9_out, in_1, in_2[3]);
  and and_10 (and_10_out, not_5_out, in_1);
  nor nor_11 (out_3[2], and_11_out, nor_13_out);
  and and_11 (and_11_out, not_6_out, in_1);
  not not_6 (not_6_out, in_2[2]);
  nor nor_12 (out_3[1], and_12_out, nor_14_out);
  nor nor_13 (nor_13_out, out_3[2], and_13_out);
  and and_12 (and_12_out, not_7_out, in_1);
  and and_13 (and_13_out, in_1, in_2[2]);
  not not_7 (not_7_out, in_2[1]);
  nor nor_14 (nor_14_out, out_3[1], and_14_out);
  and and_14 (and_14_out, in_1, in_2[1]);
  nor nor_15 (nor_15_out, out_3[0], and_16_out);
  nor nor_16 (out_3[0], and_15_out, nor_15_out);
  and and_15 (and_15_out, not_8_out, in_1);
  not not_8 (not_8_out, in_2[0]);
  and and_16 (and_16_out, in_1, in_2[0]);
endmodule

module command_unit (
  input  [7:0] in_1,
  input  [7:0] in_2,
  input  [7:0] in_3,
  input  [7:0] in_4,
  input  [7:0] in_5,
  input  [7:0] in_6,
  input  [7:0] in_7,
  input  [7:0] in_8,
  input  [7:0] in_9,
  input  [7:0] in_10,
  input  [7:0] in_11,
  input  [7:0] in_12,
  output out_13,
  output out_14,
  output out_15,
  output out_16,
  output out_17,
  output out_18,
  output out_19,
  output out_20,
  output out_21,
  output out_22,
  output [7:0] out_23,
  output [7:0] out_24,
  output [7:0] out_25,
  output [7:0] out_26,
  output [7:0] out_27,
  output [7:0] out_28,
  output [7:0] out_29,
  output [7:0] out_30,
  output [7:0] out_31,
  output [7:0] out_32
);

  wire controlled_buffer_2_out, controlled_buffer_3_out, controlled_buffer_4_out, hyper10router_1_out_14,
       hyper10router_1_out_16, hyper10router_1_out_18, hyper10router_1_out_20, hyper10router_1_out_22,
       hyper10router_1_out_24, hyper10router_1_out_26, hyper10router_1_out_28, n3bitdecoder_1_out_4,
       n3bitdecoder_1_out_5, n3bitdecoder_1_out_6, n3bitdecoder_1_out_7, n3bitdecoder_1_out_8,
       n3bitdecoder_1_out_9, n3bitdecoder_1_out_10, n3bitdecoder_1_out_11, n5bitdecoder_1_out_7, nor_1_out,
       not_1_out;
  wire [7:0] controlled_buffer_5_out, undriven;

  Controlled_Buffer #(.width(8)) controlled_buffer_1 (.in(in_12), .en(nor_1_out));  // open: out
  assign controlled_buffer_2_out = nor_1_out ? in_11[2] : 1'bz;  // Controlled_Buffer controlled_buffer_2
  assign controlled_buffer_3_out = nor_1_out ? in_11[1] : 1'bz;  // Controlled_Buffer controlled_buffer_3
  assign controlled_buffer_4_out = nor_1_out ? in_11[0] : 1'bz;  // Controlled_Buffer controlled_buffer_4
  or or_1 (out_13, n3bitdecoder_1_out_11, hyper10router_1_out_14);
  _3bitdecoder u_3bitdecoder_1 (
    .out_4(n3bitdecoder_1_out_4), .out_5(n3bitdecoder_1_out_5), .out_6(n3bitdecoder_1_out_6),
    .out_7(n3bitdecoder_1_out_7), .out_8(n3bitdecoder_1_out_8), .out_9(n3bitdecoder_1_out_9),
    .out_10(n3bitdecoder_1_out_10), .out_11(n3bitdecoder_1_out_11), .in_1(controlled_buffer_2_out),
    .in_2(controlled_buffer_3_out), .in_3(controlled_buffer_4_out));
  nor nor_1 (nor_1_out, in_11[7], in_11[6], in_11[5], in_11[4], in_11[3]);
  or or_2 (out_15, n3bitdecoder_1_out_9, hyper10router_1_out_18);
  or or_3 (out_14, n3bitdecoder_1_out_10, hyper10router_1_out_16);
  or or_4 (out_17, n3bitdecoder_1_out_7, hyper10router_1_out_22);
  or or_5 (out_16, n3bitdecoder_1_out_8, hyper10router_1_out_20);
  or or_6 (out_18, n3bitdecoder_1_out_6, hyper10router_1_out_24);
  or or_7 (out_19, n3bitdecoder_1_out_5, hyper10router_1_out_26);
  or or_8 (out_20, n3bitdecoder_1_out_4, hyper10router_1_out_28);
  hyper10router hyper10router_1 (
    .A_2(out_32), .out_14(hyper10router_1_out_14), .out_15(out_31), .out_16(hyper10router_1_out_16),
    .out_17(out_30), .out_18(hyper10router_1_out_18), .out_19(out_29), .out_20(hyper10router_1_out_20),
    .out_21(out_28), .out_22(hyper10router_1_out_22), .out_23(out_27), .out_24(hyper10router_1_out_24),
    .out_25(out_26), .out_26(hyper10router_1_out_26), .out_27(out_25), .out_28(hyper10router_1_out_28),
    .out_29(out_24), .out_30(out_21), .Mover_2_2(out_23), .out_32(out_22), .in_1(undriven), .Mover_2(in_10),
    .in_4(in_9), .in_5(in_8), .in_6(in_7), .in_7(in_6), .in_8(in_5), .in_9(in_4), .in_10(in_3), .in_11(in_2),
    .A(in_1), .X(n5bitdecoder_1_out_7));
  assign controlled_buffer_5_out = not_1_out ? in_12 : 8'bz;  // Controlled_Buffer controlled_buffer_5
  not not_1 (not_1_out, nor_1_out);
  _5bitdecoder u_5bitdecoder_1 (
    .in_1(controlled_buffer_5_out[0]), .in_2(controlled_buffer_5_out[1]), .in_3(controlled_buffer_5_out[2]),
    .in_4(controlled_buffer_5_out[3]), .in_5(controlled_buffer_5_out[4]), .out_7(n5bitdecoder_1_out_7));  // open: out_6, out_8, out_9, out_10, out_11, out_12, out_13, out_14, out_15, out_16, out_17, out_18, out_19, out_20, out_21, out_22, out_23, out_24, out_25, out_26, out_27, out_28, out_29, out_30, out_31, out_32, out_33, out_34, out_35, out_36, out_37
endmodule

module commander (
  input  in_1,
  input  [7:0] in_2,
  input  [7:0] in_3,
  output [7:0] out_4
);

  wire not_1_out;
  wire [7:0] controlled_buffer_1_out, controlled_buffer_2_out;

  assign controlled_buffer_1_out = not_1_out ? in_2 : 8'bz;  // Controlled_Buffer controlled_buffer_1
  not not_1 (not_1_out, in_1);
  assign out_4 = controlled_buffer_1_out | controlled_buffer_2_out;  // OR_Gate or_1, 8 bits wide
  assign controlled_buffer_2_out = in_1 ? in_3 : 8'bz;  // Controlled_Buffer controlled_buffer_2
endmodule

module rom (
  input  in_1,
  input  [7:0] in_2,
  input  in_3,
  output [7:0] out_4,
  output [7:0] out_5
);

  wire or_1_out;
  wire [7:0] counter_1_q;

  Counter counter_1 (.load(in_3), .D(in_2), .count(in_1), .Q(counter_1_q), .clk(or_1_out));  // open: carry, clr
  or or_1 (or_1_out, in_3, in_1);
  ROM rom_1 (.addr(counter_1_q), .data(out_5));  // open: sel

  assign out_4 = in_2;
endmodule

module ram (
  input  [7:0] in_1,
  input  [7:0] in_2,
  input  in_3,
  output [7:0] out_4,
  output [7:0] out_5
);

  wire [8:0] ramchip_1_out_2, ramchip_2_out_2, ramchip_3_out_2, ramchip_4_out_2, ramchip_5_out_2,
       ramchip_6_out_2, ramchip_7_out_2, ramchip_8_out_2;
  wire [13:0] ramcontrol_1_out_14, ramcontrol_1_out_15, ramcontrol_1_out_16, ramcontrol_1_out_17,
       ramcontrol_1_out_18, ramcontrol_1_out_19, ramcontrol_1_out_20, ramcontrol_1_out_21;

  ramchip ramchip_1 (.in_1(ramcontrol_1_out_15), .out_2(ramchip_1_out_2));
  ramchip ramchip_2 (.in_1(ramcontrol_1_out_17), .out_2(ramchip_2_out_2));
  ramchip ramchip_3 (.in_1(ramcontrol_1_out_19), .out_2(ramchip_3_out_2));
  ramchip ramchip_4 (.in_1(ramcontrol_1_out_21), .out_2(ramchip_4_out_2));
  ramcontrol ramcontrol_1 (
    .out_15(ramcontrol_1_out_15), .in_5(ramchip_1_out_2), .out_17(ramcontrol_1_out_17),
    .in_7(ramchip_2_out_2), .out_19(ramcontrol_1_out_19), .in_9(ramchip_3_out_2),
    .out_21(ramcontrol_1_out_21), .in_11(ramchip_4_out_2), .out_14(ramcontrol_1_out_14),
    .in_4(ramchip_5_out_2), .out_16(ramcontrol_1_out_16), .in_6(ramchip_6_out_2),
    .out_18(ramcontrol_1_out_18), .in_8(ramchip_7_out_2), .out_20(ramcontrol_1_out_20),
    .in_10(ramchip_8_out_2), .out_12(out_4), .out_13(out_5), .in_1(in_1), .in_2(in_2), .in_3(in_3));
  ramchip ramchip_5 (.in_1(ramcontrol_1_out_14), .out_2(ramchip_5_out_2));
  ramchip ramchip_6 (.in_1(ramcontrol_1_out_16), .out_2(ramchip_6_out_2));
  ramchip ramchip_7 (.in_1(ramcontrol_1_out_18), .out_2(ramchip_7_out_2));
  ramchip ramchip_8 (.in_1(ramcontrol_1_out_20), .out_2(ramchip_8_out_2));
endmodule

module ramcontrol (
  input  [7:0] in_1,
  input  [7:0] in_2,
  input  in_3,
  input  [8:0] in_4,
  input  [8:0] in_5,
  input  [8:0] in_6,
  input  [8:0] in_7,
  input  [8:0] in_8,
  input  [8:0] in_9,
  input  [8:0] in_10,
  input  [8:0] in_11,
  output [7:0] out_12,
  output [7:0] out_13,
  output [13:0] out_14,
  output [13:0] out_15,
  output [13:0] out_16,
  output [13:0] out_17,
  output [13:0] out_18,
  output [13:0] out_19,
  output [13:0] out_20,
  output [13:0] out_21
);

  wire n3bitdecoder_1_out_4, n3bitdecoder_1_out_5, n3bitdecoder_1_out_6, n3bitdecoder_1_out_7,
       n3bitdecoder_1_out_8, n3bitdecoder_1_out_9, n3bitdecoder_1_out_10, n3bitdecoder_1_out_11;

  assign out_15 = n3bitdecoder_1_out_4 ? {in_3, in_1[4:0], in_2} : 14'bz;  // Controlled_Buffer controlled_buffer_1
  assign {out_12[7], out_13} = n3bitdecoder_1_out_4 ? in_5 : 9'bz;  // Controlled_Buffer controlled_buffer_2
  assign out_17 = n3bitdecoder_1_out_5 ? {in_3, in_1[4:0], in_2} : 14'bz;  // Controlled_Buffer controlled_buffer_3
  assign {out_12[6], out_13} = n3bitdecoder_1_out_5 ? in_7 : 9'bz;  // Controlled_Buffer controlled_buffer_4
  assign out_19 = n3bitdecoder_1_out_6 ? {in_3, in_1[4:0], in_2} : 14'bz;  // Controlled_Buffer controlled_buffer_5
  assign {out_12[5], out_13} = n3bitdecoder_1_out_6 ? in_9 : 9'bz;  // Controlled_Buffer controlled_buffer_6
  assign out_21 = n3bitdecoder_1_out_7 ? {in_3, in_1[4:0], in_2} : 14'bz;  // Controlled_Buffer controlled_buffer_7
  assign {out_12[4], out_13} = n3bitdecoder_1_out_7 ? in_11 : 9'bz;  // Controlled_Buffer controlled_buffer_8
  _3bitdecoder u_3bitdecoder_1 (
    .out_4(n3bitdecoder_1_out_4), .out_5(n3bitdecoder_1_out_5), .out_6(n3bitdecoder_1_out_6),
    .out_7(n3bitdecoder_1_out_7), .out_8(n3bitdecoder_1_out_8), .out_9(n3bitdecoder_1_out_9),
    .out_10(n3bitdecoder_1_out_10), .out_11(n3bitdecoder_1_out_11), .in_1(in_1[5]), .in_2(in_1[6]),
    .in_3(in_1[7]));
  assign out_14 = n3bitdecoder_1_out_11 ? {in_3, in_1[4:0], in_2} : 14'bz;  // Controlled_Buffer controlled_buffer_9
  assign {out_12[0], out_13} = n3bitdecoder_1_out_11 ? in_4 : 9'bz;  // Controlled_Buffer controlled_buffer_10
  assign out_16 = n3bitdecoder_1_out_10 ? {in_3, in_1[4:0], in_2} : 14'bz;  // Controlled_Buffer controlled_buffer_11
  assign {out_12[1], out_13} = n3bitdecoder_1_out_10 ? in_6 : 9'bz;  // Controlled_Buffer controlled_buffer_12
  assign out_18 = n3bitdecoder_1_out_9 ? {in_3, in_1[4:0], in_2} : 14'bz;  // Controlled_Buffer controlled_buffer_13
  assign {out_12[2], out_13} = n3bitdecoder_1_out_9 ? in_8 : 9'bz;  // Controlled_Buffer controlled_buffer_14
  assign out_20 = n3bitdecoder_1_out_8 ? {in_3, in_1[4:0], in_2} : 14'bz;  // Controlled_Buffer controlled_buffer_15
  assign {out_12[3], out_13} = n3bitdecoder_1_out_8 ? in_10 : 9'bz;  // Controlled_Buffer controlled_buffer_16
endmodule

module ramchip (
  input  [13:0] in_1,
  output [8:0] out_2
);

  wire controlled_buffer_21_out, controlled_buffer_22_out, controlled_buffer_23_out,
       controlled_buffer_24_out, controlled_buffer_25_out, controlled_buffer_26_out,
       controlled_buffer_27_out, controlled_buffer_28_out, controlled_buffer_29_out,
       controlled_buffer_30_out, controlled_buffer_51_out, controlled_buffer_52_out,
       controlled_buffer_53_out, controlled_buffer_54_out, controlled_buffer_55_out,
       controlled_buffer_56_out, controlled_buffer_57_out, controlled_buffer_58_out,
       controlled_buffer_59_out, controlled_buffer_60_out, controlled_buffer_83_out,
       controlled_buffer_84_out, controlled_buffer_85_out, controlled_buffer_86_out,
       controlled_buffer_87_out, controlled_buffer_88_out, controlled_buffer_89_out,
       controlled_buffer_90_out, controlled_buffer_91_out, controlled_buffer_92_out,
       controlled_buffer_93_out, n5bitdecoder_1_out_6, n5bitdecoder_1_out_7, n5bitdecoder_1_out_8,
       n5bitdecoder_1_out_9, n5bitdecoder_1_out_10, n5bitdecoder_1_out_11, n5bitdecoder_1_out_12,
       n5bitdecoder_1_out_14, n5bitdecoder_1_out_15, n5bitdecoder_1_out_16, n5bitdecoder_1_out_17,
       n5bitdecoder_1_out_18, n5bitdecoder_1_out_19, n5bitdecoder_1_out_20, n5bitdecoder_1_out_21,
       n5bitdecoder_1_out_22, n5bitdecoder_1_out_23, n5bitdecoder_1_out_24, n5bitdecoder_1_out_25,
       n5bitdecoder_1_out_26, n5bitdecoder_1_out_27, n5bitdecoder_1_out_28, n5bitdecoder_1_out_29,
       n5bitdecoder_1_out_30, n5bitdecoder_1_out_31, n5bitdecoder_1_out_32, n5bitdecoder_1_out_33,
       n5bitdecoder_1_out_34, n5bitdecoder_1_out_35, n5bitdecoder_1_out_36, n5bitdecoder_1_out_37;
  wire [7:0] controlled_buffer_1_out, controlled_buffer_3_out, controlled_buffer_5_out,
       controlled_buffer_7_out, controlled_buffer_9_out, controlled_buffer_11_out, controlled_buffer_13_out,
       controlled_buffer_15_out, controlled_buffer_17_out, controlled_buffer_19_out,
       controlled_buffer_31_out, controlled_buffer_33_out, controlled_buffer_35_out,
       controlled_buffer_37_out, controlled_buffer_39_out, controlled_buffer_41_out,
       controlled_buffer_43_out, controlled_buffer_45_out, controlled_buffer_47_out,
       controlled_buffer_49_out, controlled_buffer_61_out, controlled_buffer_63_out,
       controlled_buffer_65_out, controlled_buffer_67_out, controlled_buffer_69_out,
       controlled_buffer_71_out, controlled_buffer_73_out, controlled_buffer_75_out,
       controlled_buffer_77_out, controlled_buffer_79_out, controlled_buffer_81_out, n8bitreg_1_out_3,
       n8bitreg_2_out_3, n8bitreg_3_out_3, n8bitreg_4_out_3, n8bitreg_5_out_3, n8bitreg_6_out_3,
       n8bitreg_7_out_3, n8bitreg_8_out_3, n8bitreg_9_out_3, n8bitreg_10_out_3, n8bitreg_11_out_3,
       n8bitreg_12_out_3, n8bitreg_13_out_3, n8bitreg_14_out_3, n8bitreg_15_out_3, n8bitreg_16_out_3,
       n8bitreg_17_out_3, n8bitreg_18_out_3, n8bitreg_19_out_3, n8bitreg_20_out_3, n8bitreg_21_out_3,
       n8bitreg_22_out_3, n8bitreg_23_out_3, n8bitreg_24_out_3, n8bitreg_25_out_3, n8bitreg_26_out_3,
       n8bitreg_27_out_3, n8bitreg_28_out_3, n8bitreg_29_out_3, n8bitreg_30_out_3, n8bitreg_31_out_3;

  assign controlled_buffer_1_out = n5bitdecoder_1_out_6 ? in_1[7:0] : 8'bz;  // Controlled_Buffer controlled_buffer_1
  _8bitreg u_8bitreg_1 (.in_1(controlled_buffer_21_out), .out_3(n8bitreg_1_out_3), .in_2(controlled_buffer_1_out));
  assign out_2[7:0] = n5bitdecoder_1_out_6 ? n8bitreg_1_out_3 : 8'bz;  // Controlled_Buffer controlled_buffer_2
  assign controlled_buffer_3_out = n5bitdecoder_1_out_11 ? in_1[7:0] : 8'bz;  // Controlled_Buffer controlled_buffer_3
  _8bitreg u_8bitreg_2 (.in_1(controlled_buffer_22_out), .out_3(n8bitreg_2_out_3), .in_2(controlled_buffer_3_out));
  assign out_2[7:0] = n5bitdecoder_1_out_11 ? n8bitreg_2_out_3 : 8'bz;  // Controlled_Buffer controlled_buffer_4
  assign controlled_buffer_5_out = n5bitdecoder_1_out_14 ? in_1[7:0] : 8'bz;  // Controlled_Buffer controlled_buffer_5
  _8bitreg u_8bitreg_3 (.in_1(controlled_buffer_23_out), .out_3(n8bitreg_3_out_3), .in_2(controlled_buffer_5_out));
  assign out_2[7:0] = n5bitdecoder_1_out_14 ? n8bitreg_3_out_3 : 8'bz;  // Controlled_Buffer controlled_buffer_6
  assign controlled_buffer_7_out = n5bitdecoder_1_out_17 ? in_1[7:0] : 8'bz;  // Controlled_Buffer controlled_buffer_7
  _8bitreg u_8bitreg_4 (.in_1(controlled_buffer_24_out), .out_3(n8bitreg_4_out_3), .in_2(controlled_buffer_7_out));
  assign out_2[7:0] = n5bitdecoder_1_out_17 ? n8bitreg_4_out_3 : 8'bz;  // Controlled_Buffer controlled_buffer_8
  assign controlled_buffer_9_out = n5bitdecoder_1_out_20 ? in_1[7:0] : 8'bz;  // Controlled_Buffer controlled_buffer_9
  _8bitreg u_8bitreg_5 (.in_1(controlled_buffer_25_out), .out_3(n8bitreg_5_out_3), .in_2(controlled_buffer_9_out));
  assign out_2[7:0] = n5bitdecoder_1_out_20 ? n8bitreg_5_out_3 : 8'bz;  // Controlled_Buffer controlled_buffer_10
  assign controlled_buffer_11_out = n5bitdecoder_1_out_23 ? in_1[7:0] : 8'bz;  // Controlled_Buffer controlled_buffer_11
  _8bitreg u_8bitreg_6 (.in_1(controlled_buffer_26_out), .out_3(n8bitreg_6_out_3), .in_2(controlled_buffer_11_out));
  assign out_2[7:0] = n5bitdecoder_1_out_23 ? n8bitreg_6_out_3 : 8'bz;  // Controlled_Buffer controlled_buffer_12
  assign controlled_buffer_13_out = n5bitdecoder_1_out_26 ? in_1[7:0] : 8'bz;  // Controlled_Buffer controlled_buffer_13
  _8bitreg u_8bitreg_7 (.in_1(controlled_buffer_27_out), .out_3(n8bitreg_7_out_3), .in_2(controlled_buffer_13_out));
  assign out_2[7:0] = n5bitdecoder_1_out_26 ? n8bitreg_7_out_3 : 8'bz;  // Controlled_Buffer controlled_buffer_14
  assign controlled_buffer_15_out = n5bitdecoder_1_out_29 ? in_1[7:0] : 8'bz;  // Controlled_Buffer controlled_buffer_15
  _8bitreg u_8bitreg_8 (.in_1(controlled_buffer_28_out), .out_3(n8bitreg_8_out_3), .in_2(controlled_buffer_15_out));
  assign out_2[7:0] = n5bitdecoder_1_out_29 ? n8bitreg_8_out_3 : 8'bz;  // Controlled_Buffer controlled_buffer_16
  assign controlled_buffer_17_out = n5bitdecoder_1_out_32 ? in_1[7:0] : 8'bz;  // Controlled_Buffer controlled_buffer_17
  _8bitreg u_8bitreg_9 (.in_1(controlled_buffer_29_out), .out_3(n8bitreg_9_out_3), .in_2(controlled_buffer_17_out));
  assign out_2[7:0] = n5bitdecoder_1_out_32 ? n8bitreg_9_out_3 : 8'bz;  // Controlled_Buffer controlled_buffer_18
  assign controlled_buffer_19_out = n5bitdecoder_1_out_35 ? in_1[7:0] : 8'bz;  // Controlled_Buffer controlled_buffer_19
  _8bitreg u_8bitreg_10 (.in_1(controlled_buffer_30_out), .out_3(n8bitreg_10_out_3), .in_2(controlled_buffer_19_out));
  assign out_2[7:0] = n5bitdecoder_1_out_35 ? n8bitreg_10_out_3 : 8'bz;  // Controlled_Buffer controlled_buffer_20
  assign controlled_buffer_21_out = n5bitdecoder_1_out_6 ? in_1[13] : 1'bz;  // Controlled_Buffer controlled_buffer_21
  assign controlled_buffer_22_out = n5bitdecoder_1_out_11 ? in_1[13] : 1'bz;  // Controlled_Buffer controlled_buffer_22
  assign controlled_buffer_23_out = n5bitdecoder_1_out_14 ? in_1[13] : 1'bz;  // Controlled_Buffer controlled_buffer_23
  assign controlled_buffer_24_out = n5bitdecoder_1_out_17 ? in_1[13] : 1'bz;  // Controlled_Buffer controlled_buffer_24
  assign controlled_buffer_25_out = n5bitdecoder_1_out_20 ? in_1[13] : 1'bz;  // Controlled_Buffer controlled_buffer_25
  assign controlled_buffer_26_out = n5bitdecoder_1_out_23 ? in_1[13] : 1'bz;  // Controlled_Buffer controlled_buffer_26
  assign controlled_buffer_27_out = n5bitdecoder_1_out_26 ? in_1[13] : 1'bz;  // Controlled_Buffer controlled_buffer_27
  assign controlled_buffer_28_out = n5bitdecoder_1_out_29 ? in_1[13] : 1'bz;  // Controlled_Buffer controlled_buffer_28
  assign controlled_buffer_29_out = n5bitdecoder_1_out_32 ? in_1[13] : 1'bz;  // Controlled_Buffer controlled_buffer_29
  assign controlled_buffer_30_out = n5bitdecoder_1_out_35 ? in_1[13] : 1'bz;  // Controlled_Buffer controlled_buffer_30
  assign controlled_buffer_31_out = n5bitdecoder_1_out_7 ? in_1[7:0] : 8'bz;  // Controlled_Buffer controlled_buffer_31
  _8bitreg u_8bitreg_11 (.in_1(controlled_buffer_51_out), .out_3(n8bitreg_11_out_3), .in_2(controlled_buffer_31_out));
  assign out_2[7:0] = n5bitdecoder_1_out_7 ? n8bitreg_11_out_3 : 8'bz;  // Controlled_Buffer controlled_buffer_32
  assign controlled_buffer_33_out = n5bitdecoder_1_out_10 ? in_1[7:0] : 8'bz;  // Controlled_Buffer controlled_buffer_33
  _8bitreg u_8bitreg_12 (.in_1(controlled_buffer_52_out), .out_3(n8bitreg_12_out_3), .in_2(controlled_buffer_33_out));
  assign out_2[7:0] = n5bitdecoder_1_out_10 ? n8bitreg_12_out_3 : 8'bz;  // Controlled_Buffer controlled_buffer_34
  assign controlled_buffer_35_out = n5bitdecoder_1_out_36 ? in_1[7:0] : 8'bz;  // Controlled_Buffer controlled_buffer_35
  _8bitreg u_8bitreg_13 (.in_1(controlled_buffer_53_out), .out_3(n8bitreg_13_out_3), .in_2(controlled_buffer_35_out));
  assign out_2[7:0] = n5bitdecoder_1_out_36 ? n8bitreg_13_out_3 : 8'bz;  // Controlled_Buffer controlled_buffer_36
  assign controlled_buffer_37_out = n5bitdecoder_1_out_16 ? in_1[7:0] : 8'bz;  // Controlled_Buffer controlled_buffer_37
  _8bitreg u_8bitreg_14 (.in_1(controlled_buffer_54_out), .out_3(n8bitreg_14_out_3), .in_2(controlled_buffer_37_out));
  assign out_2[7:0] = n5bitdecoder_1_out_16 ? n8bitreg_14_out_3 : 8'bz;  // Controlled_Buffer controlled_buffer_38
  assign controlled_buffer_39_out = n5bitdecoder_1_out_19 ? in_1[7:0] : 8'bz;  // Controlled_Buffer controlled_buffer_39
  _8bitreg u_8bitreg_15 (.in_1(controlled_buffer_55_out), .out_3(n8bitreg_15_out_3), .in_2(controlled_buffer_39_out));
  assign out_2[7:0] = n5bitdecoder_1_out_19 ? n8bitreg_15_out_3 : 8'bz;  // Controlled_Buffer controlled_buffer_40
  assign controlled_buffer_41_out = n5bitdecoder_1_out_22 ? in_1[7:0] : 8'bz;  // Controlled_Buffer controlled_buffer_41
  _8bitreg u_8bitreg_16 (.in_1(controlled_buffer_56_out), .out_3(n8bitreg_16_out_3), .in_2(controlled_buffer_41_out));
  assign out_2[7:0] = n5bitdecoder_1_out_22 ? n8bitreg_16_out_3 : 8'bz;  // Controlled_Buffer controlled_buffer_42
  assign controlled_buffer_43_out = n5bitdecoder_1_out_25 ? in_1[7:0] : 8'bz;  // Controlled_Buffer controlled_buffer_43
  _8bitreg u_8bitreg_17 (.in_1(controlled_buffer_57_out), .out_3(n8bitreg_17_out_3), .in_2(controlled_buffer_43_out));
  assign out_2[7:0] = n5bitdecoder_1_out_25 ? n8bitreg_17_out_3 : 8'bz;  // Controlled_Buffer controlled_buffer_44
  assign controlled_buffer_45_out = n5bitdecoder_1_out_28 ? in_1[7:0] : 8'bz;  // Controlled_Buffer controlled_buffer_45
  _8bitreg u_8bitreg_18 (.in_1(controlled_buffer_58_out), .out_3(n8bitreg_18_out_3), .in_2(controlled_buffer_45_out));
  assign out_2[7:0] = n5bitdecoder_1_out_28 ? n8bitreg_18_out_3 : 8'bz;  // Controlled_Buffer controlled_buffer_46
  assign controlled_buffer_47_out = n5bitdecoder_1_out_31 ? in_1[7:0] : 8'bz;  // Controlled_Buffer controlled_buffer_47
  _8bitreg u_8bitreg_19 (.in_1(controlled_buffer_59_out), .out_3(n8bitreg_19_out_3), .in_2(controlled_buffer_47_out));
  assign out_2[7:0] = n5bitdecoder_1_out_31 ? n8bitreg_19_out_3 : 8'bz;  // Controlled_Buffer controlled_buffer_48
  assign controlled_buffer_49_out = n5bitdecoder_1_out_34 ? in_1[7:0] : 8'bz;  // Controlled_Buffer controlled_buffer_49
  _8bitreg u_8bitreg_20 (.in_1(controlled_buffer_60_out), .out_3(n8bitreg_20_out_3), .in_2(controlled_buffer_49_out));
  assign out_2[7:0] = n5bitdecoder_1_out_34 ? n8bitreg_20_out_3 : 8'bz;  // Controlled_Buffer controlled_buffer_50
  assign controlled_buffer_51_out = n5bitdecoder_1_out_7 ? in_1[13] : 1'bz;  // Controlled_Buffer controlled_buffer_51
  assign controlled_buffer_52_out = n5bitdecoder_1_out_10 ? in_1[13] : 1'bz;  // Controlled_Buffer controlled_buffer_52
  assign controlled_buffer_53_out = n5bitdecoder_1_out_36 ? in_1[13] : 1'bz;  // Controlled_Buffer controlled_buffer_53
  assign controlled_buffer_54_out = n5bitdecoder_1_out_16 ? in_1[13] : 1'bz;  // Controlled_Buffer controlled_buffer_54
  assign controlled_buffer_55_out = n5bitdecoder_1_out_19 ? in_1[13] : 1'bz;  // Controlled_Buffer controlled_buffer_55
  assign controlled_buffer_56_out = n5bitdecoder_1_out_22 ? in_1[13] : 1'bz;  // Controlled_Buffer controlled_buffer_56
  assign controlled_buffer_57_out = n5bitdecoder_1_out_25 ? in_1[13] : 1'bz;  // Controlled_Buffer controlled_buffer_57
  assign controlled_buffer_58_out = n5bitdecoder_1_out_28 ? in_1[13] : 1'bz;  // Controlled_Buffer controlled_buffer_58
  assign controlled_buffer_59_out = n5bitdecoder_1_out_31 ? in_1[13] : 1'bz;  // Controlled_Buffer controlled_buffer_59
  assign controlled_buffer_60_out = n5bitdecoder_1_out_34 ? in_1[13] : 1'bz;  // Controlled_Buffer controlled_buffer_60
  _5bitdecoder u_5bitdecoder_1 (
    .in_1(in_1[8]), .in_2(in_1[9]), .in_3(in_1[10]), .in_4(in_1[11]), .in_5(in_1[12]),
    .out_6(n5bitdecoder_1_out_6), .out_7(n5bitdecoder_1_out_7), .out_8(n5bitdecoder_1_out_8),
    .out_9(n5bitdecoder_1_out_9), .out_10(n5bitdecoder_1_out_10), .out_11(n5bitdecoder_1_out_11),
    .out_12(n5bitdecoder_1_out_12), .out_13(in_1[13]), .out_14(n5bitdecoder_1_out_14),
    .out_15(n5bitdecoder_1_out_15), .out_16(n5bitdecoder_1_out_16), .out_17(n5bitdecoder_1_out_17),
    .out_18(n5bitdecoder_1_out_18), .out_19(n5bitdecoder_1_out_19), .out_20(n5bitdecoder_1_out_20),
    .out_21(n5bitdecoder_1_out_21), .out_22(n5bitdecoder_1_out_22), .out_23(n5bitdecoder_1_out_23),
    .out_24(n5bitdecoder_1_out_24), .out_25(n5bitdecoder_1_out_25), .out_26(n5bitdecoder_1_out_26),
    .out_27(n5bitdecoder_1_out_27), .out_28(n5bitdecoder_1_out_28), .out_29(n5bitdecoder_1_out_29),
    .out_30(n5bitdecoder_1_out_30), .out_31(n5bitdecoder_1_out_31), .out_32(n5bitdecoder_1_out_32),
    .out_33(n5bitdecoder_1_out_33), .out_34(n5bitdecoder_1_out_34), .out_35(n5bitdecoder_1_out_35),
    .out_36(n5bitdecoder_1_out_36), .out_37(n5bitdecoder_1_out_37));
  assign controlled_buffer_61_out = n5bitdecoder_1_out_8 ? in_1[7:0] : 8'bz;  // Controlled_Buffer controlled_buffer_61
  _8bitreg u_8bitreg_21 (.in_1(controlled_buffer_83_out), .out_3(n8bitreg_21_out_3), .in_2(controlled_buffer_61_out));
  assign out_2[7:0] = n5bitdecoder_1_out_8 ? n8bitreg_21_out_3 : 8'bz;  // Controlled_Buffer controlled_buffer_62
  assign controlled_buffer_63_out = n5bitdecoder_1_out_9 ? in_1[7:0] : 8'bz;  // Controlled_Buffer controlled_buffer_63
  _8bitreg u_8bitreg_22 (.in_1(controlled_buffer_84_out), .out_3(n8bitreg_22_out_3), .in_2(controlled_buffer_63_out));
  assign out_2[7:0] = n5bitdecoder_1_out_9 ? n8bitreg_22_out_3 : 8'bz;  // Controlled_Buffer controlled_buffer_64
  assign controlled_buffer_65_out = n5bitdecoder_1_out_12 ? in_1[7:0] : 8'bz;  // Controlled_Buffer controlled_buffer_65
  _8bitreg u_8bitreg_23 (.in_1(controlled_buffer_85_out), .out_3(n8bitreg_23_out_3), .in_2(controlled_buffer_65_out));
  assign out_2[7:0] = n5bitdecoder_1_out_12 ? n8bitreg_23_out_3 : 8'bz;  // Controlled_Buffer controlled_buffer_66
  assign controlled_buffer_67_out = n5bitdecoder_1_out_15 ? in_1[7:0] : 8'bz;  // Controlled_Buffer controlled_buffer_67
  _8bitreg u_8bitreg_24 (.in_1(controlled_buffer_86_out), .out_3(n8bitreg_24_out_3), .in_2(controlled_buffer_67_out));
  assign out_2[7:0] = n5bitdecoder_1_out_15 ? n8bitreg_24_out_3 : 8'bz;  // Controlled_Buffer controlled_buffer_68
  assign controlled_buffer_69_out = n5bitdecoder_1_out_18 ? in_1[7:0] : 8'bz;  // Controlled_Buffer controlled_buffer_69
  _8bitreg u_8bitreg_25 (.in_1(controlled_buffer_87_out), .out_3(n8bitreg_25_out_3), .in_2(controlled_buffer_69_out));
  assign out_2[7:0] = n5bitdecoder_1_out_18 ? n8bitreg_25_out_3 : 8'bz;  // Controlled_Buffer controlled_buffer_70
  assign controlled_buffer_71_out = n5bitdecoder_1_out_21 ? in_1[7:0] : 8'bz;  // Controlled_Buffer controlled_buffer_71
  _8bitreg u_8bitreg_26 (.in_1(controlled_buffer_88_out), .out_3(n8bitreg_26_out_3), .in_2(controlled_buffer_71_out));
  assign out_2[7:0] = n5bitdecoder_1_out_21 ? n8bitreg_26_out_3 : 8'bz;  // Controlled_Buffer controlled_buffer_72
  assign controlled_buffer_73_out = n5bitdecoder_1_out_24 ? in_1[7:0] : 8'bz;  // Controlled_Buffer controlled_buffer_73
  _8bitreg u_8bitreg_27 (.in_1(controlled_buffer_89_out), .out_3(n8bitreg_27_out_3), .in_2(controlled_buffer_73_out));
  assign out_2[7:0] = n5bitdecoder_1_out_24 ? n8bitreg_27_out_3 : 8'bz;  // Controlled_Buffer controlled_buffer_74
  assign controlled_buffer_75_out = n5bitdecoder_1_out_27 ? in_1[7:0] : 8'bz;  // Controlled_Buffer controlled_buffer_75
  _8bitreg u_8bitreg_28 (.in_1(controlled_buffer_90_out), .out_3(n8bitreg_28_out_3), .in_2(controlled_buffer_75_out));
  assign out_2[7:0] = n5bitdecoder_1_out_27 ? n8bitreg_28_out_3 : 8'bz;  // Controlled_Buffer controlled_buffer_76
  assign controlled_buffer_77_out = n5bitdecoder_1_out_30 ? in_1[7:0] : 8'bz;  // Controlled_Buffer controlled_buffer_77
  _8bitreg u_8bitreg_29 (.in_1(controlled_buffer_91_out), .out_3(n8bitreg_29_out_3), .in_2(controlled_buffer_77_out));
  assign out_2[7:0] = n5bitdecoder_1_out_30 ? n8bitreg_29_out_3 : 8'bz;  // Controlled_Buffer controlled_buffer_78
  assign controlled_buffer_79_out = n5bitdecoder_1_out_33 ? in_1[7:0] : 8'bz;  // Controlled_Buffer controlled_buffer_79
  _8bitreg u_8bitreg_30 (.in_1(controlled_buffer_92_out), .out_3(n8bitreg_30_out_3), .in_2(controlled_buffer_79_out));
  assign out_2[7:0] = n5bitdecoder_1_out_33 ? n8bitreg_30_out_3 : 8'bz;  // Controlled_Buffer controlled_buffer_80
  assign controlled_buffer_81_out = n5bitdecoder_1_out_37 ? in_1[7:0] : 8'bz;  // Controlled_Buffer controlled_buffer_81
  _8bitreg u_8bitreg_31 (.in_1(controlled_buffer_93_out), .out_3(n8bitreg_31_out_3), .in_2(controlled_buffer_81_out));
  assign out_2[7:0] = n5bitdecoder_1_out_37 ? n8bitreg_31_out_3 : 8'bz;  // Controlled_Buffer controlled_buffer_82
  assign controlled_buffer_83_out = n5bitdecoder_1_out_8 ? in_1[13] : 1'bz;  // Controlled_Buffer controlled_buffer_83
  assign controlled_buffer_84_out = n5bitdecoder_1_out_9 ? in_1[13] : 1'bz;  // Controlled_Buffer controlled_buffer_84
  assign controlled_buffer_85_out = n5bitdecoder_1_out_12 ? in_1[13] : 1'bz;  // Controlled_Buffer controlled_buffer_85
  assign controlled_buffer_86_out = n5bitdecoder_1_out_15 ? in_1[13] : 1'bz;  // Controlled_Buffer controlled_buffer_86
  assign controlled_buffer_87_out = n5bitdecoder_1_out_18 ? in_1[13] : 1'bz;  // Controlled_Buffer controlled_buffer_87
  assign controlled_buffer_88_out = n5bitdecoder_1_out_21 ? in_1[13] : 1'bz;  // Controlled_Buffer controlled_buffer_88
  assign controlled_buffer_89_out = n5bitdecoder_1_out_24 ? in_1[13] : 1'bz;  // Controlled_Buffer controlled_buffer_89
  assign controlled_buffer_90_out = n5bitdecoder_1_out_27 ? in_1[13] : 1'bz;  // Controlled_Buffer controlled_buffer_90
  assign controlled_buffer_91_out = n5bitdecoder_1_out_30 ? in_1[13] : 1'bz;  // Controlled_Buffer controlled_buffer_91
  assign controlled_buffer_92_out = n5bitdecoder_1_out_33 ? in_1[13] : 1'bz;  // Controlled_Buffer controlled_buffer_92
  assign controlled_buffer_93_out = n5bitdecoder_1_out_37 ? in_1[13] : 1'bz;  // Controlled_Buffer controlled_buffer_93

  assign out_2[8] = 1'b1;
endmodule

module _5bitdecoder (
  input  in_1,
  input  in_2,
  input  in_3,
  input  in_4,
  input  in_5,
  output out_6,
  output out_7,
  output out_8,
  output out_9,
  output out_10,
  output out_11,
  output out_12,
  output out_13,
  output out_14,
  output out_15,
  output out_16,
  output out_17,
  output out_18,
  output out_19,
  output out_20,
  output out_21,
  output out_22,
  output out_23,
  output out_24,
  output out_25,
  output out_26,
  output out_27,
  output out_28,
  output out_29,
  output out_30,
  output out_31,
  output out_32,
  output out_33,
  output out_34,
  output out_35,
  output out_36,
  output out_37
);

  wire not_1_out, not_2_out, not_3_out, not_4_out, not_5_out;

  not not_1 (not_1_out, in_5);
  not not_2 (not_2_out, in_3);
  not not_3 (not_3_out, in_4);
  not not_4 (not_4_out, in_2);
  not not_5 (not_5_out, in_1);
  and and_1 (out_6, not_5_out, not_4_out, not_2_out, not_3_out, not_1_out);
  and and_2 (out_7, not_5_out, not_4_out, not_2_out, not_3_out, in_5);
  and and_3 (out_8, not_5_out, not_4_out, not_2_out, in_4, not_1_out);
  and and_4 (out_9, not_5_out, not_4_out, not_2_out, in_4, in_5);
  and and_5 (out_10, not_5_out, not_4_out, in_3, not_3_out, not_1_out);
  and and_6 (out_11, not_5_out, not_4_out, in_3, not_3_out, in_5);
  and and_7 (out_12, not_5_out, not_4_out, in_3, in_4, not_1_out);
  and and_8 (out_13, not_5_out, not_4_out, in_3, in_4, in_5);
  and and_9 (out_14, not_5_out, in_2, not_2_out, not_3_out, not_1_out);
  and and_10 (out_15, not_5_out, in_2, not_2_out, not_3_out, in_5);
  and and_11 (out_16, not_5_out, in_2, not_2_out, in_4, not_1_out);
  and and_12 (out_17, not_5_out, in_2, not_2_out, in_4, in_5);
  and and_13 (out_18, not_5_out, in_2, in_3, not_3_out, not_1_out);
  and and_14 (out_19, not_5_out, in_2, in_3, not_3_out, in_5);
  and and_15 (out_20, not_5_out, in_2, in_3, in_4, not_1_out);
  and and_16 (out_21, not_5_out, in_2, in_3, in_4, in_5);
  and and_17 (out_22, in_1, not_4_out, not_2_out, not_3_out, not_1_out);
  and and_18 (out_23, in_1, not_4_out, not_2_out, not_3_out, in_5);
  and and_19 (out_24, in_1, not_4_out, not_2_out, in_4, not_1_out);
  and and_20 (out_25, in_1, not_4_out, not_2_out, in_4, in_5);
  and and_21 (out_26, in_1, not_4_out, in_3, not_3_out, not_1_out);
  and and_22 (out_27, in_1, not_4_out, in_3, not_3_out, in_5);
  and and_23 (out_28, in_1, not_4_out, in_3, in_4, not_1_out);
  and and_24 (out_29, in_1, not_4_out, in_3, in_4, in_5);
  and and_25 (out_30, in_1, in_2, not_2_out, not_3_out, not_1_out);
  and and_26 (out_31, in_1, in_2, not_2_out, not_3_out, in_5);
  and and_27 (out_32, in_1, in_2, not_2_out, in_4, not_1_out);
  and and_28 (out_33, in_1, in_2, not_2_out, in_4, in_5);
  and and_29 (out_34, in_1, in_2, in_3, not_3_out, not_1_out);
  and and_30 (out_35, in_1, in_2, in_3, not_3_out, in_5);
  and and_31 (out_36, in_1, in_2, in_3, in_4, not_1_out);
  and and_32 (out_37, in_1, in_2, in_3, in_4, in_5);
endmodule

module _3bitdecoder (
  input  in_1,
  input  in_2,
  input  in_3,
  output out_4,
  output out_5,
  output out_6,
  output out_7,
  output out_8,
  output out_9,
  output out_10,
  output out_11
);

  wire not_1_out, not_2_out, not_3_out;

  not not_1 (not_1_out, in_1);
  not not_2 (not_2_out, in_2);
  not not_3 (not_3_out, in_3);
  and and_1 (out_5, in_1, in_2, not_3_out);
  and and_2 (out_4, in_1, in_2, in_3);
  and and_3 (out_7, in_1, not_2_out, not_3_out);
  and and_4 (out_6, in_1, not_2_out, in_3);
  and and_5 (out_8, not_1_out, in_2, in_3);
  and and_6 (out_11, not_1_out, not_2_out, not_3_out);
  and and_7 (out_10, not_1_out, not_2_out, in_3);
  and and_8 (out_9, not_1_out, in_2, not_3_out);
endmodule

module hyper10router (
  input  [7:0] in_1,
  input  X,
  input  [7:0] Mover_2,
  input  [7:0] in_4,
  input  [7:0] in_5,
  input  [7:0] in_6,
  input  [7:0] in_7,
  input  [7:0] in_8,
  input  [7:0] in_9,
  input  [7:0] in_10,
  input  [7:0] in_11,
  input  [7:0] A,
  output [7:0] A_2,
  output out_14,
  output [7:0] out_15,
  output out_16,
  output [7:0] out_17,
  output out_18,
  output [7:0] out_19,
  output out_20,
  output [7:0] out_21,
  output out_22,
  output [7:0] out_23,
  output out_24,
  output [7:0] out_25,
  output out_26,
  output [7:0] out_27,
  output out_28,
  output [7:0] out_29,
  output out_30,
  output [7:0] Mover_2_2,
  output out_32
);

  wire n4bitdecoder_1_o_15, n4bitdecoder_1_out_12, n4bitdecoder_1_out_13, n4bitdecoder_1_out_14,
       n4bitdecoder_1_out_15, n4bitdecoder_1_out_16, n4bitdecoder_2_o_0, n4bitdecoder_2_o_15,
       n4bitdecoder_2_out_12, n4bitdecoder_2_out_13, n4bitdecoder_2_out_14, n4bitdecoder_2_out_15,
       n4bitdecoder_2_out_16;
  wire [7:0] controlled_buffer_1_out, controlled_buffer_2_out, controlled_buffer_3_out,
       controlled_buffer_4_out, controlled_buffer_5_out, controlled_buffer_6_out, controlled_buffer_7_out,
       controlled_buffer_8_out, controlled_buffer_9_out, controlled_buffer_10_out, controlled_buffer_11_out,
       controlled_buffer_12_out, controlled_buffer_13_out, controlled_buffer_14_out,
       controlled_buffer_15_out, controlled_buffer_16_out, controlled_buffer_17_out,
       controlled_buffer_18_out, controlled_buffer_19_out, controlled_buffer_20_out,
       controlled_buffer_21_out, controlled_buffer_22_out, controlled_buffer_23_out,
       controlled_buffer_24_out, controlled_buffer_25_out, controlled_buffer_26_out,
       controlled_buffer_27_out, controlled_buffer_28_out, controlled_buffer_29_out,
       controlled_buffer_30_out, controlled_buffer_31_out, controlled_buffer_32_out,
       controlled_buffer_33_out, controlled_buffer_34_out, controlled_buffer_35_out,
       controlled_buffer_36_out, controlled_buffer_37_out, controlled_buffer_38_out,
       controlled_buffer_39_out, controlled_buffer_40_out, controlled_buffer_41_out,
       controlled_buffer_42_out, controlled_buffer_43_out, controlled_buffer_44_out,
       controlled_buffer_45_out, controlled_buffer_46_out, controlled_buffer_47_out,
       controlled_buffer_48_out, controlled_buffer_49_out, controlled_buffer_50_out,
       controlled_buffer_51_out, controlled_buffer_52_out, controlled_buffer_53_out,
       controlled_buffer_54_out, controlled_buffer_55_out, controlled_buffer_56_out,
       controlled_buffer_57_out, controlled_buffer_58_out, controlled_buffer_59_out,
       controlled_buffer_60_out, controlled_buffer_61_out, controlled_buffer_62_out,
       controlled_buffer_63_out, controlled_buffer_64_out, controlled_buffer_65_out,
       controlled_buffer_66_out, controlled_buffer_67_out, controlled_buffer_68_out,
       controlled_buffer_69_out, controlled_buffer_70_out, controlled_buffer_71_out,
       controlled_buffer_72_out, controlled_buffer_73_out, controlled_buffer_74_out,
       controlled_buffer_75_out, controlled_buffer_76_out, controlled_buffer_77_out,
       controlled_buffer_78_out, controlled_buffer_79_out, controlled_buffer_80_out,
       controlled_buffer_81_out, controlled_buffer_82_out, controlled_buffer_83_out,
       controlled_buffer_84_out, controlled_buffer_85_out, controlled_buffer_86_out,
       controlled_buffer_87_out, controlled_buffer_88_out, controlled_buffer_89_out,
       controlled_buffer_90_out, controlled_buffer_91_out, controlled_buffer_92_out,
       controlled_buffer_93_out, controlled_buffer_94_out, controlled_buffer_95_out,
       controlled_buffer_96_out, controlled_buffer_97_out, controlled_buffer_98_out,
       controlled_buffer_99_out, controlled_buffer_100_out;
  wire [9:0] n4bitdecoder_1_o_0;

  // OR_Gate or_1 has open pins: in0=n4bitdecoder_1_o_15, in1=n4bitdecoder_1_out_16, in2=n4bitdecoder_1_out_15, in3=n4bitdecoder_1_out_14, in4=n4bitdecoder_1_out_13, in5=n4bitdecoder_1_out_12, out=open
  _4bitdecoder u_4bitdecoder_1 (
    .in_1(in_1[7:4]), .O_0(n4bitdecoder_1_o_0[0]), .out_3(n4bitdecoder_1_o_0[1]),
    .out_4(n4bitdecoder_1_o_0[2]), .out_5(n4bitdecoder_1_o_0[3]), .out_6(n4bitdecoder_1_o_0[4]),
    .out_7(n4bitdecoder_1_o_0[5]), .out_8(n4bitdecoder_1_o_0[6]), .out_9(n4bitdecoder_1_o_0[7]),
    .out_10(n4bitdecoder_1_o_0[8]), .out_11(n4bitdecoder_1_o_0[9]), .out_12(n4bitdecoder_1_out_12),
    .out_13(n4bitdecoder_1_out_13), .out_14(n4bitdecoder_1_out_14), .out_15(n4bitdecoder_1_out_15),
    .out_16(n4bitdecoder_1_out_16), .O_15(n4bitdecoder_1_o_15));
  // OR_Gate or_2 has open pins: in0=n4bitdecoder_2_o_15, in1=n4bitdecoder_2_out_16, in2=n4bitdecoder_2_out_15, in3=n4bitdecoder_2_out_14, in4=n4bitdecoder_2_out_13, in5=n4bitdecoder_2_out_12, out=open
  _4bitdecoder u_4bitdecoder_2 (
    .in_1(in_1[3:0]), .O_0(n4bitdecoder_2_o_0), .out_3(out_16), .out_4(out_18), .out_5(out_20),
    .out_6(out_22), .out_7(out_24), .out_8(out_26), .out_9(out_28), .out_10(out_30), .out_11(out_32),
    .out_12(n4bitdecoder_2_out_12), .out_13(n4bitdecoder_2_out_13), .out_14(n4bitdecoder_2_out_14),
    .out_15(n4bitdecoder_2_out_15), .out_16(n4bitdecoder_2_out_16), .O_15(n4bitdecoder_2_o_15));
  assign controlled_buffer_1_out = n4bitdecoder_1_o_0[0] ? A : 8'bz;  // Controlled_Buffer controlled_buffer_1
  assign controlled_buffer_2_out = n4bitdecoder_1_o_0[1] ? in_11 : 8'bz;  // Controlled_Buffer controlled_buffer_2
  assign controlled_buffer_3_out = n4bitdecoder_1_o_0[2] ? in_10 : 8'bz;  // Controlled_Buffer controlled_buffer_3
  assign controlled_buffer_4_out = n4bitdecoder_1_o_0[3] ? in_9 : 8'bz;  // Controlled_Buffer controlled_buffer_4
  assign controlled_buffer_5_out = n4bitdecoder_1_o_0[4] ? in_8 : 8'bz;  // Controlled_Buffer controlled_buffer_5
  assign controlled_buffer_6_out = n4bitdecoder_1_o_0[5] ? in_7 : 8'bz;  // Controlled_Buffer controlled_buffer_6
  assign controlled_buffer_7_out = n4bitdecoder_1_o_0[6] ? in_6 : 8'bz;  // Controlled_Buffer controlled_buffer_7
  assign controlled_buffer_8_out = n4bitdecoder_1_o_0[7] ? in_5 : 8'bz;  // Controlled_Buffer controlled_buffer_8
  assign controlled_buffer_9_out = n4bitdecoder_1_o_0[8] ? in_4 : 8'bz;  // Controlled_Buffer controlled_buffer_9
  assign controlled_buffer_10_out = n4bitdecoder_1_o_0[9] ? Mover_2 : 8'bz;  // Controlled_Buffer controlled_buffer_10
  assign controlled_buffer_11_out = n4bitdecoder_1_o_0[0] ? A : 8'bz;  // Controlled_Buffer controlled_buffer_11
  assign controlled_buffer_12_out = n4bitdecoder_1_o_0[1] ? in_11 : 8'bz;  // Controlled_Buffer controlled_buffer_12
  assign controlled_buffer_13_out = n4bitdecoder_1_o_0[2] ? in_10 : 8'bz;  // Controlled_Buffer controlled_buffer_13
  assign controlled_buffer_14_out = n4bitdecoder_1_o_0[3] ? in_9 : 8'bz;  // Controlled_Buffer controlled_buffer_14
  assign controlled_buffer_15_out = n4bitdecoder_1_o_0[4] ? in_8 : 8'bz;  // Controlled_Buffer controlled_buffer_15
  assign controlled_buffer_16_out = n4bitdecoder_1_o_0[5] ? in_7 : 8'bz;  // Controlled_Buffer controlled_buffer_16
  assign controlled_buffer_17_out = n4bitdecoder_1_o_0[6] ? in_6 : 8'bz;  // Controlled_Buffer controlled_buffer_17
  assign controlled_buffer_18_out = n4bitdecoder_1_o_0[7] ? in_5 : 8'bz;  // Controlled_Buffer controlled_buffer_18
  assign controlled_buffer_19_out = n4bitdecoder_1_o_0[8] ? in_4 : 8'bz;  // Controlled_Buffer controlled_buffer_19
  assign controlled_buffer_20_out = n4bitdecoder_1_o_0[9] ? Mover_2 : 8'bz;  // Controlled_Buffer controlled_buffer_20
  assign controlled_buffer_21_out = n4bitdecoder_1_o_0[0] ? A : 8'bz;  // Controlled_Buffer controlled_buffer_21
  assign controlled_buffer_22_out = n4bitdecoder_1_o_0[1] ? in_11 : 8'bz;  // Controlled_Buffer controlled_buffer_22
  assign controlled_buffer_23_out = n4bitdecoder_1_o_0[2] ? in_10 : 8'bz;  // Controlled_Buffer controlled_buffer_23
  assign controlled_buffer_24_out = n4bitdecoder_1_o_0[3] ? in_9 : 8'bz;  // Controlled_Buffer controlled_buffer_24
  assign controlled_buffer_25_out = n4bitdecoder_1_o_0[4] ? in_8 : 8'bz;  // Controlled_Buffer controlled_buffer_25
  assign controlled_buffer_26_out = n4bitdecoder_1_o_0[5] ? in_7 : 8'bz;  // Controlled_Buffer controlled_buffer_26
  assign controlled_buffer_27_out = n4bitdecoder_1_o_0[6] ? in_6 : 8'bz;  // Controlled_Buffer controlled_buffer_27
  assign controlled_buffer_28_out = n4bitdecoder_1_o_0[7] ? in_5 : 8'bz;  // Controlled_Buffer controlled_buffer_28
  assign controlled_buffer_29_out = n4bitdecoder_1_o_0[8] ? in_4 : 8'bz;  // Controlled_Buffer controlled_buffer_29
  assign controlled_buffer_30_out = n4bitdecoder_1_o_0[9] ? Mover_2 : 8'bz;  // Controlled_Buffer controlled_buffer_30
  assign controlled_buffer_31_out = n4bitdecoder_1_o_0[0] ? A : 8'bz;  // Controlled_Buffer controlled_buffer_31
  assign controlled_buffer_32_out = n4bitdecoder_1_o_0[1] ? in_11 : 8'bz;  // Controlled_Buffer controlled_buffer_32
  assign controlled_buffer_33_out = n4bitdecoder_1_o_0[2] ? in_10 : 8'bz;  // Controlled_Buffer controlled_buffer_33
  assign controlled_buffer_34_out = n4bitdecoder_1_o_0[3] ? in_9 : 8'bz;  // Controlled_Buffer controlled_buffer_34
  assign controlled_buffer_35_out = n4bitdecoder_1_o_0[4] ? in_8 : 8'bz;  // Controlled_Buffer controlled_buffer_35
  assign controlled_buffer_36_out = n4bitdecoder_1_o_0[5] ? in_7 : 8'bz;  // Controlled_Buffer controlled_buffer_36
  assign controlled_buffer_37_out = n4bitdecoder_1_o_0[6] ? in_6 : 8'bz;  // Controlled_Buffer controlled_buffer_37
  assign controlled_buffer_38_out = n4bitdecoder_1_o_0[7] ? in_5 : 8'bz;  // Controlled_Buffer controlled_buffer_38
  assign controlled_buffer_39_out = n4bitdecoder_1_o_0[8] ? in_4 : 8'bz;  // Controlled_Buffer controlled_buffer_39
  assign controlled_buffer_40_out = n4bitdecoder_1_o_0[9] ? Mover_2 : 8'bz;  // Controlled_Buffer controlled_buffer_40
  assign controlled_buffer_41_out = n4bitdecoder_1_o_0[0] ? A : 8'bz;  // Controlled_Buffer controlled_buffer_41
  assign controlled_buffer_42_out = n4bitdecoder_1_o_0[1] ? in_11 : 8'bz;  // Controlled_Buffer controlled_buffer_42
  assign controlled_buffer_43_out = n4bitdecoder_1_o_0[2] ? in_10 : 8'bz;  // Controlled_Buffer controlled_buffer_43
  assign controlled_buffer_44_out = n4bitdecoder_1_o_0[3] ? in_9 : 8'bz;  // Controlled_Buffer controlled_buffer_44
  assign controlled_buffer_45_out = n4bitdecoder_1_o_0[4] ? in_8 : 8'bz;  // Controlled_Buffer controlled_buffer_45
  assign controlled_buffer_46_out = n4bitdecoder_1_o_0[5] ? in_7 : 8'bz;  // Controlled_Buffer controlled_buffer_46
  assign controlled_buffer_47_out = n4bitdecoder_1_o_0[6] ? in_6 : 8'bz;  // Controlled_Buffer controlled_buffer_47
  assign controlled_buffer_48_out = n4bitdecoder_1_o_0[7] ? in_5 : 8'bz;  // Controlled_Buffer controlled_buffer_48
  assign controlled_buffer_49_out = n4bitdecoder_1_o_0[8] ? in_4 : 8'bz;  // Controlled_Buffer controlled_buffer_49
  assign controlled_buffer_50_out = n4bitdecoder_1_o_0[9] ? Mover_2 : 8'bz;  // Controlled_Buffer controlled_buffer_50
  assign controlled_buffer_51_out = n4bitdecoder_1_o_0[0] ? A : 8'bz;  // Controlled_Buffer controlled_buffer_51
  assign controlled_buffer_52_out = n4bitdecoder_1_o_0[1] ? in_11 : 8'bz;  // Controlled_Buffer controlled_buffer_52
  assign controlled_buffer_53_out = n4bitdecoder_1_o_0[2] ? in_10 : 8'bz;  // Controlled_Buffer controlled_buffer_53
  assign controlled_buffer_54_out = n4bitdecoder_1_o_0[3] ? in_9 : 8'bz;  // Controlled_Buffer controlled_buffer_54
  assign controlled_buffer_55_out = n4bitdecoder_1_o_0[4] ? in_8 : 8'bz;  // Controlled_Buffer controlled_buffer_55
  assign controlled_buffer_56_out = n4bitdecoder_1_o_0[5] ? in_7 : 8'bz;  // Controlled_Buffer controlled_buffer_56
  assign controlled_buffer_57_out = n4bitdecoder_1_o_0[6] ? in_6 : 8'bz;  // Controlled_Buffer controlled_buffer_57
  assign controlled_buffer_58_out = n4bitdecoder_1_o_0[7] ? in_5 : 8'bz;  // Controlled_Buffer controlled_buffer_58
  assign controlled_buffer_59_out = n4bitdecoder_1_o_0[8] ? in_4 : 8'bz;  // Controlled_Buffer controlled_buffer_59
  assign controlled_buffer_60_out = n4bitdecoder_1_o_0[9] ? Mover_2 : 8'bz;  // Controlled_Buffer controlled_buffer_60
  assign controlled_buffer_61_out = n4bitdecoder_1_o_0[0] ? A : 8'bz;  // Controlled_Buffer controlled_buffer_61
  assign controlled_buffer_62_out = n4bitdecoder_1_o_0[1] ? in_11 : 8'bz;  // Controlled_Buffer controlled_buffer_62
  assign controlled_buffer_63_out = n4bitdecoder_1_o_0[2] ? in_10 : 8'bz;  // Controlled_Buffer controlled_buffer_63
  assign controlled_buffer_64_out = n4bitdecoder_1_o_0[3] ? in_9 : 8'bz;  // Controlled_Buffer controlled_buffer_64
  assign controlled_buffer_65_out = n4bitdecoder_1_o_0[4] ? in_8 : 8'bz;  // Controlled_Buffer controlled_buffer_65
  assign controlled_buffer_66_out = n4bitdecoder_1_o_0[5] ? in_7 : 8'bz;  // Controlled_Buffer controlled_buffer_66
  assign controlled_buffer_67_out = n4bitdecoder_1_o_0[6] ? in_6 : 8'bz;  // Controlled_Buffer controlled_buffer_67
  assign controlled_buffer_68_out = n4bitdecoder_1_o_0[7] ? in_5 : 8'bz;  // Controlled_Buffer controlled_buffer_68
  assign controlled_buffer_69_out = n4bitdecoder_1_o_0[8] ? in_4 : 8'bz;  // Controlled_Buffer controlled_buffer_69
  assign controlled_buffer_70_out = n4bitdecoder_1_o_0[9] ? Mover_2 : 8'bz;  // Controlled_Buffer controlled_buffer_70
  assign controlled_buffer_71_out = n4bitdecoder_1_o_0[0] ? A : 8'bz;  // Controlled_Buffer controlled_buffer_71
  assign controlled_buffer_72_out = n4bitdecoder_1_o_0[1] ? in_11 : 8'bz;  // Controlled_Buffer controlled_buffer_72
  assign controlled_buffer_73_out = n4bitdecoder_1_o_0[2] ? in_10 : 8'bz;  // Controlled_Buffer controlled_buffer_73
  assign controlled_buffer_74_out = n4bitdecoder_1_o_0[3] ? in_9 : 8'bz;  // Controlled_Buffer controlled_buffer_74
  assign controlled_buffer_75_out = n4bitdecoder_1_o_0[4] ? in_8 : 8'bz;  // Controlled_Buffer controlled_buffer_75
  assign controlled_buffer_76_out = n4bitdecoder_1_o_0[5] ? in_7 : 8'bz;  // Controlled_Buffer controlled_buffer_76
  assign controlled_buffer_77_out = n4bitdecoder_1_o_0[6] ? in_6 : 8'bz;  // Controlled_Buffer controlled_buffer_77
  assign controlled_buffer_78_out = n4bitdecoder_1_o_0[7] ? in_5 : 8'bz;  // Controlled_Buffer controlled_buffer_78
  assign controlled_buffer_79_out = n4bitdecoder_1_o_0[8] ? in_4 : 8'bz;  // Controlled_Buffer controlled_buffer_79
  assign controlled_buffer_80_out = n4bitdecoder_1_o_0[9] ? Mover_2 : 8'bz;  // Controlled_Buffer controlled_buffer_80
  assign controlled_buffer_81_out = n4bitdecoder_1_o_0[0] ? A : 8'bz;  // Controlled_Buffer controlled_buffer_81
  assign controlled_buffer_82_out = n4bitdecoder_1_o_0[1] ? in_11 : 8'bz;  // Controlled_Buffer controlled_buffer_82
  assign controlled_buffer_83_out = n4bitdecoder_1_o_0[2] ? in_10 : 8'bz;  // Controlled_Buffer controlled_buffer_83
  assign controlled_buffer_84_out = n4bitdecoder_1_o_0[3] ? in_9 : 8'bz;  // Controlled_Buffer controlled_buffer_84
  assign controlled_buffer_85_out = n4bitdecoder_1_o_0[4] ? in_8 : 8'bz;  // Controlled_Buffer controlled_buffer_85
  assign controlled_buffer_86_out = n4bitdecoder_1_o_0[5] ? in_7 : 8'bz;  // Controlled_Buffer controlled_buffer_86
  assign controlled_buffer_87_out = n4bitdecoder_1_o_0[6] ? in_6 : 8'bz;  // Controlled_Buffer controlled_buffer_87
  assign controlled_buffer_88_out = n4bitdecoder_1_o_0[7] ? in_5 : 8'bz;  // Controlled_Buffer controlled_buffer_88
  assign controlled_buffer_89_out = n4bitdecoder_1_o_0[8] ? in_4 : 8'bz;  // Controlled_Buffer controlled_buffer_89
  assign controlled_buffer_90_out = n4bitdecoder_1_o_0[9] ? Mover_2 : 8'bz;  // Controlled_Buffer controlled_buffer_90
  assign controlled_buffer_91_out = n4bitdecoder_1_o_0[0] ? A : 8'bz;  // Controlled_Buffer controlled_buffer_91
  assign controlled_buffer_92_out = n4bitdecoder_1_o_0[1] ? in_11 : 8'bz;  // Controlled_Buffer controlled_buffer_92
  assign controlled_buffer_93_out = n4bitdecoder_1_o_0[2] ? in_10 : 8'bz;  // Controlled_Buffer controlled_buffer_93
  assign controlled_buffer_94_out = n4bitdecoder_1_o_0[3] ? in_9 : 8'bz;  // Controlled_Buffer controlled_buffer_94
  assign controlled_buffer_95_out = n4bitdecoder_1_o_0[4] ? in_8 : 8'bz;  // Controlled_Buffer controlled_buffer_95
  assign controlled_buffer_96_out = n4bitdecoder_1_o_0[5] ? in_7 : 8'bz;  // Controlled_Buffer controlled_buffer_96
  assign controlled_buffer_97_out = n4bitdecoder_1_o_0[6] ? in_6 : 8'bz;  // Controlled_Buffer controlled_buffer_97
  assign controlled_buffer_98_out = n4bitdecoder_1_o_0[7] ? in_5 : 8'bz;  // Controlled_Buffer controlled_buffer_98
  assign controlled_buffer_99_out = n4bitdecoder_1_o_0[8] ? in_4 : 8'bz;  // Controlled_Buffer controlled_buffer_99
  assign controlled_buffer_100_out = n4bitdecoder_1_o_0[9] ? Mover_2 : 8'bz;  // Controlled_Buffer controlled_buffer_100
  assign A_2 = controlled_buffer_1_out | controlled_buffer_2_out | controlled_buffer_3_out | controlled_buffer_4_out | controlled_buffer_5_out | controlled_buffer_6_out | controlled_buffer_7_out | controlled_buffer_8_out | controlled_buffer_9_out | controlled_buffer_10_out;  // OR_Gate or_3, 8 bits wide
  assign out_14 = X ? n4bitdecoder_2_o_0 : 1'bz;  // Controlled_Buffer controlled_buffer_101
  assign out_15 = controlled_buffer_11_out | controlled_buffer_12_out | controlled_buffer_13_out | controlled_buffer_14_out | controlled_buffer_15_out | controlled_buffer_16_out | controlled_buffer_17_out | controlled_buffer_18_out | controlled_buffer_19_out | controlled_buffer_20_out;  // OR_Gate or_4, 8 bits wide
  assign out_17 = controlled_buffer_21_out | controlled_buffer_22_out | controlled_buffer_23_out | controlled_buffer_24_out | controlled_buffer_25_out | controlled_buffer_26_out | controlled_buffer_27_out | controlled_buffer_28_out | controlled_buffer_29_out | controlled_buffer_30_out;  // OR_Gate or_5, 8 bits wide
  assign out_19 = controlled_buffer_31_out | controlled_buffer_32_out | controlled_buffer_33_out | controlled_buffer_34_out | controlled_buffer_35_out | controlled_buffer_36_out | controlled_buffer_37_out | controlled_buffer_38_out | controlled_buffer_39_out | controlled_buffer_40_out;  // OR_Gate or_6, 8 bits wide
  assign out_21 = controlled_buffer_41_out | controlled_buffer_42_out | controlled_buffer_43_out | controlled_buffer_44_out | controlled_buffer_45_out | controlled_buffer_46_out | controlled_buffer_47_out | controlled_buffer_48_out | controlled_buffer_49_out | controlled_buffer_50_out;  // OR_Gate or_7, 8 bits wide
  assign out_23 = controlled_buffer_51_out | controlled_buffer_52_out | controlled_buffer_53_out | controlled_buffer_54_out | controlled_buffer_55_out | controlled_buffer_56_out | controlled_buffer_57_out | controlled_buffer_58_out | controlled_buffer_59_out | controlled_buffer_60_out;  // OR_Gate or_8, 8 bits wide
  assign out_25 = controlled_buffer_61_out | controlled_buffer_62_out | controlled_buffer_63_out | controlled_buffer_64_out | controlled_buffer_65_out | controlled_buffer_66_out | controlled_buffer_67_out | controlled_buffer_68_out | controlled_buffer_69_out | controlled_buffer_70_out;  // OR_Gate or_9, 8 bits wide
  assign out_27 = controlled_buffer_71_out | controlled_buffer_72_out | controlled_buffer_73_out | controlled_buffer_74_out | controlled_buffer_75_out | controlled_buffer_76_out | controlled_buffer_77_out | controlled_buffer_78_out | controlled_buffer_79_out | controlled_buffer_80_out;  // OR_Gate or_10, 8 bits wide
  assign out_29 = controlled_buffer_81_out | controlled_buffer_82_out | controlled_buffer_83_out | controlled_buffer_84_out | controlled_buffer_85_out | controlled_buffer_86_out | controlled_buffer_87_out | controlled_buffer_88_out | controlled_buffer_89_out | controlled_buffer_90_out;  // OR_Gate or_11, 8 bits wide
  assign Mover_2_2 = controlled_buffer_91_out | controlled_buffer_92_out | controlled_buffer_93_out | controlled_buffer_94_out | controlled_buffer_95_out | controlled_buffer_96_out | controlled_buffer_97_out | controlled_buffer_98_out | controlled_buffer_99_out | controlled_buffer_100_out;  // OR_Gate or_12, 8 bits wide
endmodule

module _4bitdecoder (
  input  [3:0] in_1,
  output O_0,
  output out_3,
  output out_4,
  output out_5,
  output out_6,
  output out_7,
  output out_8,
  output out_9,
  output out_10,
  output out_11,
  output out_12,
  output out_13,
  output out_14,
  output out_15,
  output out_16,
  output O_15
);

  wire not_1_out, not_2_out, not_3_out, not_4_out;

  not not_1 (not_1_out, in_1[1]);
  not not_2 (not_2_out, in_1[2]);
  not not_3 (not_3_out, in_1[3]);
  not not_4 (not_4_out, in_1[0]);
  and and_1 (O_0, not_4_out, not_1_out, not_2_out, not_3_out);
  and and_2 (out_3, not_4_out, not_1_out, not_2_out, in_1[3]);
  and and_3 (out_4, not_4_out, not_1_out, in_1[2], not_3_out);
  and and_4 (out_5, not_4_out, not_1_out, in_1[2], in_1[3]);
  and and_5 (out_6, not_4_out, in_1[1], not_2_out, not_3_out);
  and and_6 (out_7, not_4_out, in_1[1], not_2_out, in_1[3]);
  and and_7 (out_8, not_4_out, in_1[1], in_1[2], not_3_out);
  and and_8 (out_9, not_4_out, in_1[1], in_1[2], in_1[3]);
  and and_9 (out_10, in_1[0], not_1_out, not_2_out, not_3_out);
  and and_10 (out_11, in_1[0], not_1_out, not_2_out, in_1[3]);
  and and_11 (out_12, in_1[0], not_1_out, in_1[2], not_3_out);
  and and_12 (out_13, in_1[0], not_1_out, in_1[2], in_1[3]);
  and and_13 (out_14, in_1[0], in_1[1], not_2_out, not_3_out);
  and and_14 (out_15, in_1[0], in_1[1], not_2_out, in_1[3]);
  and and_15 (out_16, in_1[0], in_1[1], in_1[2], not_3_out);
  and and_16 (O_15, in_1[0], in_1[1], in_1[2], in_1[3]);
endmodule
