// Logisim project ht-pc_mockup.circ as structural Verilog: 11 circuits, main circuit main
module main (
);

  wire clock_1_out_1, cpu_1_out_4, cpu_1_out_6, cpu_1_out_9, cpu_1_out_10;
  wire [7:0] commander_1_out_4, controlled_buffer_1_out, cpu_1_out_5, cpu_1_out_7, cpu_1_out_8, cpu_1_out_11,
       history_1_out_3, input_1_out_1, ram_1_out_4, rom_1_out_4;

  Clock clock_1 (.out_1(clock_1_out_1));
  CPU cpu_1 (
    .in_1(controlled_buffer_1_out), .in_2(ram_1_out_4), .out_5(cpu_1_out_5), .out_7(cpu_1_out_7),
    .out_8(cpu_1_out_8), .out_4(cpu_1_out_4), .in_3(commander_1_out_4), .out_10(cpu_1_out_10),
    .out_11(cpu_1_out_11), .out_6(cpu_1_out_6), .out_9(cpu_1_out_9));
  ROM rom_1 (.out_4(rom_1_out_4), .in_1(clock_1_out_1), .in_2(cpu_1_out_11), .in_3(cpu_1_out_10));
  assign controlled_buffer_1_out = cpu_1_out_4 ? history_1_out_3 : 8'bz;  // Controlled_Buffer controlled_buffer_1
  commander commander_1 (.in_1(cpu_1_out_6), .out_4(commander_1_out_4), .in_2(rom_1_out_4), .in_3(ram_1_out_4));
  RAM ram_1 (.out_4(ram_1_out_4), .in_2(cpu_1_out_8), .in_3(cpu_1_out_7), .in_1(cpu_1_out_9));
  History history_1 (.out_3(history_1_out_3), .in_1(input_1_out_1), .in_2(cpu_1_out_4));
  Input input_1 (.out_1(input_1_out_1));
  Output output_1 (.in_1(cpu_1_out_5));

  // Notes on the sheet:
  //   Next
  //   Command
  //   Next
  //   Use RAM As Command
  //   Jump
  //   Command
  //   Jump Address
  //   Jump Address
  //   Jump
  //   Read
  //   Input
  //   Output
  //   RAM Address
  //   RAM Data
  //   RAM Write
  //   RAM In
  //   Command Out
  //   Use RAM
  //   ROM In
  //   RAM In
  //   Output
  //   Write
  //   Data In
  //   Address
  //   Next
endmodule

module ROM (
  input  in_1,
  input  [7:0] in_2,
  input  in_3,
  output [7:0] out_4
);
endmodule

module CPU (
  input  [7:0] in_1,
  input  [7:0] in_2,
  input  [7:0] in_3,
  output out_4,
  output [7:0] out_5,
  output out_6,
  output [7:0] out_7,
  output [7:0] out_8,
  output out_9,
  output out_10,
  output [7:0] out_11
);
endmodule

module Clock (
  output out_1
);
endmodule

module Input (
  output [7:0] out_1
);
endmodule

module Output (
  input  [7:0] in_1
);
endmodule

module History (
  input  [7:0] in_1,
  input  in_2,
  output [7:0] out_3
);
endmodule

module RAM_chip (
  input  [7:0] in_1,
  input  in_2,
  input  [4:0] in_3,
  output [7:0] out_4
);
endmodule

module RAM (
  input  in_1,
  input  [7:0] in_2,
  input  [7:0] in_3,
  output [7:0] out_4
);

  wire decoder_1_out_2, decoder_1_out_3, decoder_1_out_4, decoder_1_out_5, decoder_1_out_6, decoder_1_out_7,
       decoder_1_out_8, decoder_1_out_9;
  wire [4:0] controlled_buffer_8_out, controlled_buffer_9_out, controlled_buffer_10_out,
       controlled_buffer_11_out, controlled_buffer_14_out, controlled_buffer_16_out,
       controlled_buffer_18_out, controlled_buffer_20_out;
  wire [7:0] controlled_buffer_1_out, controlled_buffer_2_out, controlled_buffer_3_out,
       controlled_buffer_4_out, controlled_buffer_5_out, controlled_buffer_6_out, controlled_buffer_7_out,
       controlled_buffer_12_out, controlled_buffer_13_out, controlled_buffer_15_out,
       controlled_buffer_17_out, controlled_buffer_19_out, controlled_buffer_21_out,
       controlled_buffer_22_out, controlled_buffer_23_out, controlled_buffer_24_out, ram_chip_1_out_4,
       ram_chip_2_out_4, ram_chip_3_out_4, ram_chip_4_out_4, ram_chip_5_out_4, ram_chip_6_out_4,
       ram_chip_7_out_4, ram_chip_8_out_4;

  assign controlled_buffer_1_out = decoder_1_out_7 ? ram_chip_3_out_4 : 8'bz;  // Controlled_Buffer controlled_buffer_1
  assign controlled_buffer_2_out = decoder_1_out_9 ? ram_chip_4_out_4 : 8'bz;  // Controlled_Buffer controlled_buffer_2
  assign out_4 = controlled_buffer_2_out | controlled_buffer_1_out | controlled_buffer_3_out | controlled_buffer_4_out | controlled_buffer_5_out | controlled_buffer_6_out | controlled_buffer_7_out | controlled_buffer_12_out;  // OR_Gate or_1, 8 bits wide
  assign controlled_buffer_3_out = decoder_1_out_5 ? ram_chip_2_out_4 : 8'bz;  // Controlled_Buffer controlled_buffer_3
  assign controlled_buffer_4_out = decoder_1_out_3 ? ram_chip_1_out_4 : 8'bz;  // Controlled_Buffer controlled_buffer_4
  assign controlled_buffer_5_out = decoder_1_out_2 ? ram_chip_5_out_4 : 8'bz;  // Controlled_Buffer controlled_buffer_5
  assign controlled_buffer_6_out = decoder_1_out_4 ? ram_chip_6_out_4 : 8'bz;  // Controlled_Buffer controlled_buffer_6
  assign controlled_buffer_7_out = decoder_1_out_6 ? ram_chip_7_out_4 : 8'bz;  // Controlled_Buffer controlled_buffer_7
  assign controlled_buffer_8_out = decoder_1_out_3 ? in_3[4:0] : 5'bz;  // Controlled_Buffer controlled_buffer_8
  assign controlled_buffer_9_out = decoder_1_out_5 ? in_3[4:0] : 5'bz;  // Controlled_Buffer controlled_buffer_9
  assign controlled_buffer_10_out = decoder_1_out_7 ? in_3[4:0] : 5'bz;  // Controlled_Buffer controlled_buffer_10
  assign controlled_buffer_11_out = decoder_1_out_9 ? in_3[4:0] : 5'bz;  // Controlled_Buffer controlled_buffer_11
  assign controlled_buffer_12_out = decoder_1_out_8 ? ram_chip_8_out_4 : 8'bz;  // Controlled_Buffer controlled_buffer_12
  RAM_chip ram_chip_1 (
    .in_1(controlled_buffer_13_out), .out_4(ram_chip_1_out_4), .in_3(controlled_buffer_8_out));  // open: in_2
  RAM_chip ram_chip_2 (
    .in_1(controlled_buffer_15_out), .out_4(ram_chip_2_out_4), .in_3(controlled_buffer_9_out));  // open: in_2
  RAM_chip ram_chip_3 (
    .in_1(controlled_buffer_17_out), .out_4(ram_chip_3_out_4), .in_3(controlled_buffer_10_out));  // open: in_2
  RAM_chip ram_chip_4 (
    .in_1(controlled_buffer_19_out), .out_4(ram_chip_4_out_4), .in_3(controlled_buffer_11_out));  // open: in_2
  assign controlled_buffer_13_out = decoder_1_out_3 ? in_2 : 8'bz;  // Controlled_Buffer controlled_buffer_13
  assign controlled_buffer_14_out = decoder_1_out_2 ? in_3[4:0] : 5'bz;  // Controlled_Buffer controlled_buffer_14
  assign controlled_buffer_15_out = decoder_1_out_5 ? in_2 : 8'bz;  // Controlled_Buffer controlled_buffer_15
  assign controlled_buffer_16_out = decoder_1_out_4 ? in_3[4:0] : 5'bz;  // Controlled_Buffer controlled_buffer_16
  assign controlled_buffer_17_out = decoder_1_out_7 ? in_2 : 8'bz;  // Controlled_Buffer controlled_buffer_17
  assign controlled_buffer_18_out = decoder_1_out_6 ? in_3[4:0] : 5'bz;  // Controlled_Buffer controlled_buffer_18
  assign controlled_buffer_19_out = decoder_1_out_9 ? in_2 : 8'bz;  // Controlled_Buffer controlled_buffer_19
  assign controlled_buffer_20_out = decoder_1_out_8 ? in_3[4:0] : 5'bz;  // Controlled_Buffer controlled_buffer_20
  RAM_chip ram_chip_5 (
    .in_1(controlled_buffer_21_out), .out_4(ram_chip_5_out_4), .in_3(controlled_buffer_14_out));  // open: in_2
  RAM_chip ram_chip_6 (
    .in_1(controlled_buffer_22_out), .out_4(ram_chip_6_out_4), .in_3(controlled_buffer_16_out));  // open: in_2
  RAM_chip ram_chip_7 (
    .in_1(controlled_buffer_23_out), .out_4(ram_chip_7_out_4), .in_3(controlled_buffer_18_out));  // open: in_2
  RAM_chip ram_chip_8 (
    .in_1(controlled_buffer_24_out), .out_4(ram_chip_8_out_4), .in_3(controlled_buffer_20_out));  // open: in_2
  assign controlled_buffer_21_out = decoder_1_out_2 ? in_2 : 8'bz;  // Controlled_Buffer controlled_buffer_21
  assign controlled_buffer_22_out = decoder_1_out_4 ? in_2 : 8'bz;  // Controlled_Buffer controlled_buffer_22
  assign controlled_buffer_23_out = decoder_1_out_6 ? in_2 : 8'bz;  // Controlled_Buffer controlled_buffer_23
  assign controlled_buffer_24_out = decoder_1_out_8 ? in_2 : 8'bz;  // Controlled_Buffer controlled_buffer_24
  Decoder decoder_1 (
    .in_1(in_3[7:5]), .out_2(decoder_1_out_2), .out_3(decoder_1_out_3), .out_4(decoder_1_out_4),
    .out_5(decoder_1_out_5), .out_6(decoder_1_out_6), .out_7(decoder_1_out_7), .out_8(decoder_1_out_8),
    .out_9(decoder_1_out_9));
endmodule

module Decoder (
  input  [2:0] in_1,
  output out_2,
  output out_3,
  output out_4,
  output out_5,
  output out_6,
  output out_7,
  output out_8,
  output out_9
);
endmodule

module commander (
  input  in_1,
  input  [7:0] in_2,
  input  [7:0] in_3,
  output [7:0] out_4
);
endmodule
